// Digital circuit 128_BIT_RAM.dig as structural Verilog
module _128_BIT_RAM (
  input  D0,
  input  D1,
  input  D2,
  input  D3,
  input  D4,
  input  D5,
  input  D6,
  input  D7,
  input  A3,
  input  A2,
  input  A1,
  input  A0,
  input  EN,
  input  WRT,
  output Q0,
  output Q1,
  output Q2,
  output Q3,
  output Q4,
  output Q5,
  output Q6,
  output Q7
);

  wire RAM0_pin5, RAM0_pin7, RAM0_pin9, RAM0_pin11, RAM1_pin5, RAM1_pin7, RAM1_pin9, RAM1_pin11;

  _7489 RAM0 (
    .pin1(A0), .pin2(1'b0), .pin3(WRT), .pin4(D0), .pin5(RAM0_pin5), .pin6(D1), .pin7(RAM0_pin7),
    .pin8(1'b0), .pin9(RAM0_pin9), .pin10(D2), .pin11(RAM0_pin11), .pin12(D3), .pin13(A3), .pin14(A2),
    .pin15(A1), .pin16(1'b1));
  _7489 RAM1 (
    .pin1(A0), .pin2(1'b0), .pin3(WRT), .pin4(D4), .pin5(RAM1_pin5), .pin6(D5), .pin7(RAM1_pin7),
    .pin8(1'b0), .pin9(RAM1_pin9), .pin10(D6), .pin11(RAM1_pin11), .pin12(D7), .pin13(A3), .pin14(A2),
    .pin15(A1), .pin16(1'b1));
  _74245 _74245_1 (
    .pin1(1'b0), .pin2(Q7), .pin3(Q6), .pin4(Q5), .pin5(Q4), .pin6(Q3), .pin7(Q2), .pin8(Q1), .pin9(Q0),
    .pin10(1'b0), .pin11(RAM0_pin5), .pin12(RAM0_pin7), .pin13(RAM0_pin9), .pin14(RAM0_pin11),
    .pin15(RAM1_pin5), .pin16(RAM1_pin7), .pin17(RAM1_pin9), .pin18(RAM1_pin11), .pin19(EN), .pin20(1'b1));
endmodule
