// Digital circuit 8_BIT_REGISTER.dig as structural Verilog
// An 8-bit buffered register made from 8 D flip-flops
module _8_BIT_REGISTER (
  input  D0,
  input  D1,
  input  D2,
  input  D3,
  input  D4,
  input  D5,
  input  D6,
  input  D7,
  input  EN,
  input  LOAD,
  input  CP,
  input  RESET,
  output Q0,
  output Q1,
  output Q2,
  output Q3,
  output Q4,
  output Q5,
  output Q6,
  output Q7
);

  wire _7404_1_pin10, _7404_1_pin12;

  _7404 _7404_1 (
    .pin1(1'b0), .pin3(1'b0), .pin5(1'b0), .pin7(1'b0), .pin9(1'b0), .pin10(_7404_1_pin10), .pin11(EN),
    .pin12(_7404_1_pin12), .pin13(LOAD), .pin14(1'b1));  // open: pin2, pin4, pin6, pin8
  _74173 _74173_1 (
    .pin1(_7404_1_pin10), .pin2(_7404_1_pin10), .pin3(Q0), .pin4(Q1), .pin5(Q2), .pin6(Q3), .pin7(CP),
    .pin8(1'b0), .pin9(_7404_1_pin12), .pin10(_7404_1_pin12), .pin11(D3), .pin12(D2), .pin13(D1), .pin14(D0),
    .pin15(RESET), .pin16(1'b1));
  _74173 _74173_2 (
    .pin1(_7404_1_pin10), .pin2(_7404_1_pin10), .pin3(Q4), .pin4(Q5), .pin5(Q6), .pin6(Q7), .pin7(CP),
    .pin8(1'b0), .pin9(_7404_1_pin12), .pin10(_7404_1_pin12), .pin11(D7), .pin12(D6), .pin13(D5), .pin14(D4),
    .pin15(RESET), .pin16(1'b1));
endmodule
