// Logisim project 8_bit_micro.circ as structural Verilog: 13 circuits, main circuit main
module main (
);

  wire alu_1_carry, alu_1_eql, alu_1_grtr, alu_1_less, and_1_out, clock_1_clk, clock_1_mode_2, clock_1_power,
       CLOCK_MODE_out, HARD_RESET_out, n8_bit_register_1_q0, n8_bit_register_1_q1, n8_bit_register_1_q2,
       n8_bit_register_1_q3, n8_bit_register_1_q4, n8_bit_register_1_q5, n8_bit_register_1_q6,
       n8_bit_register_1_q7, n8_bit_register_2_q0, n8_bit_register_2_q1, n8_bit_register_2_q2,
       n8_bit_register_2_q3, n8_bit_register_2_q4, n8_bit_register_2_q5, n8_bit_register_2_q6,
       n8_bit_register_2_q7, not_1_out, or_1_out, POWER_2_out, program_decoder_1_alu_en,
       program_decoder_1_alu_lod, program_decoder_1_bp_en, program_decoder_1_bp_lod,
       program_decoder_1_flag_load, program_decoder_1_hlt, program_decoder_1_ir2_lod,
       program_decoder_1_ir3_en, program_decoder_1_ir3_lod, program_decoder_1_ir_lod,
       program_decoder_1_mar_lod, program_decoder_1_mem_en, program_decoder_1_mem_lod,
       program_decoder_1_pc_count, program_decoder_1_pc_en, program_decoder_1_pc_lod,
       program_decoder_1_reg_en, program_decoder_1_reg_lod, program_decoder_1_sp_count,
       program_decoder_1_sp_en, program_decoder_1_sp_lod, register_unit_new_1_alu0, register_unit_new_1_alu1,
       register_unit_new_1_alu2, register_unit_new_1_alu3, register_unit_new_1_alu4,
       register_unit_new_1_alu5, register_unit_new_1_alu6, register_unit_new_1_alu7, RESET_out, STEP_out;
  wire [3:0] program_decoder_1_alu_op, program_decoder_1_out_19;
  wire [7:0] n8_bit_counter_1_counter_hex, n8_bit_register_3_hex_out, ram_chip_1_q0;

  Hex_Digit_Display hex_digit_display_1 (.value(program_decoder_1_out_19));  // open: dp
  not not_1 (not_1_out, program_decoder_1_hlt);
  LED POWER (.in(clock_1_power));
  Button POWER_2 (.out(POWER_2_out));
  Button CLOCK_MODE (.out(CLOCK_MODE_out));
  Button STEP (.out(STEP_out));
  Button RESET (.out(RESET_out));
  Button HARD_RESET (.out(HARD_RESET_out));
  _8_BIT_REGISTER u_8_bit_register_1 (
    .CLK(and_1_out), .LOAD(program_decoder_1_ir_lod), .CLEAR(or_1_out), .D7(ram_chip_1_q0[7]),
    .D6(ram_chip_1_q0[6]), .D5(ram_chip_1_q0[5]), .D4(ram_chip_1_q0[4]), .D3(ram_chip_1_q0[3]),
    .D2(ram_chip_1_q0[2]), .D1(ram_chip_1_q0[1]), .D0(ram_chip_1_q0[0]), .Q7(n8_bit_register_1_q7),
    .Q6(n8_bit_register_1_q6), .Q5(n8_bit_register_1_q5), .Q4(n8_bit_register_1_q4),
    .Q3(n8_bit_register_1_q3), .Q2(n8_bit_register_1_q2), .Q1(n8_bit_register_1_q1), .Q0(n8_bit_register_1_q0));  // open: EN, HEX_OUT
  LED MODE (.in(clock_1_mode_2));
  and and_1 (and_1_out, not_1_out, clock_1_clk);
  CLOCK clock_1 (
    .PWR(POWER_2_out), .MODE(CLOCK_MODE_out), .STEP(STEP_out), .POWER(clock_1_power),
    .MODE_2(clock_1_mode_2), .CLK(clock_1_clk));
  or or_1 (or_1_out, RESET_out, HARD_RESET_out);
  PROGRAM_DECODER program_decoder_1 (
    .CLK(and_1_out), .CLEAR(or_1_out), .out_19(program_decoder_1_out_19), .I7(n8_bit_register_1_q7),
    .I6(n8_bit_register_1_q6), .I5(n8_bit_register_1_q5), .I4(n8_bit_register_1_q4),
    .I3(n8_bit_register_1_q3), .I2(n8_bit_register_1_q2), .I1(n8_bit_register_1_q1),
    .I0(n8_bit_register_1_q0), .BP_EN(program_decoder_1_bp_en), .BP_LOD(program_decoder_1_bp_lod),
    .SP_EN(program_decoder_1_sp_en), .SP_LOD(program_decoder_1_sp_lod), .ALU_OP(program_decoder_1_alu_op),
    .SP_COUNT(program_decoder_1_sp_count), .HLT(program_decoder_1_hlt), .IR3_EN(program_decoder_1_ir3_en),
    .FLAG_LOAD(program_decoder_1_flag_load), .ALU_LOD(program_decoder_1_alu_lod),
    .ALU_EN(program_decoder_1_alu_en), .REG_LOD(program_decoder_1_reg_lod),
    .REG_EN(program_decoder_1_reg_en), .MEM_LOD(program_decoder_1_mem_lod),
    .MEM_EN(program_decoder_1_mem_en), .MAR_LOD(program_decoder_1_mar_lod),
    .IR3_LOD(program_decoder_1_ir3_lod), .IR2_LOD(program_decoder_1_ir2_lod),
    .IR_LOD(program_decoder_1_ir_lod), .PC_LOD(program_decoder_1_pc_lod), .PC_EN(program_decoder_1_pc_en),
    .PC_COUNT(program_decoder_1_pc_count), .R7(n8_bit_register_2_q7), .R6(n8_bit_register_2_q6),
    .R5(n8_bit_register_2_q5), .R4(n8_bit_register_2_q4), .R3(n8_bit_register_2_q3),
    .R2(n8_bit_register_2_q2), .R1(n8_bit_register_2_q1), .R0(n8_bit_register_2_q0));  // open: OUT, IN
  RAM_CHIP ram_chip_1 (
    .MAR_LOAD(program_decoder_1_mar_lod), .CLK(and_1_out), .EN(program_decoder_1_mem_en),
    .LOAD(program_decoder_1_mem_lod), .CLEAR(HARD_RESET_out), .D7(ram_chip_1_q0[7]), .D6(ram_chip_1_q0[6]),
    .D5(ram_chip_1_q0[5]), .D4(ram_chip_1_q0[4]), .D3(ram_chip_1_q0[3]), .D2(ram_chip_1_q0[2]),
    .D1(ram_chip_1_q0[1]), .D0(ram_chip_1_q0[0]), .Q7(ram_chip_1_q0[7]), .Q6(ram_chip_1_q0[6]),
    .Q5(ram_chip_1_q0[5]), .Q4(ram_chip_1_q0[4]), .Q3(ram_chip_1_q0[3]), .Q2(ram_chip_1_q0[2]),
    .Q1(ram_chip_1_q0[1]), .Q0(ram_chip_1_q0[0]), .A7(ram_chip_1_q0[7]), .A6(ram_chip_1_q0[6]),
    .A5(ram_chip_1_q0[5]), .A4(ram_chip_1_q0[4]), .A3(ram_chip_1_q0[3]), .A2(ram_chip_1_q0[2]),
    .A1(ram_chip_1_q0[1]), .A0(ram_chip_1_q0[0]));
  _8_BIT_REGISTER u_8_bit_register_2 (
    .CLK(and_1_out), .LOAD(program_decoder_1_ir2_lod), .CLEAR(or_1_out), .D7(ram_chip_1_q0[7]),
    .D6(ram_chip_1_q0[6]), .D5(ram_chip_1_q0[5]), .D4(ram_chip_1_q0[4]), .D3(ram_chip_1_q0[3]),
    .D2(ram_chip_1_q0[2]), .D1(ram_chip_1_q0[1]), .D0(ram_chip_1_q0[0]), .Q7(n8_bit_register_2_q7),
    .Q6(n8_bit_register_2_q6), .Q5(n8_bit_register_2_q5), .Q4(n8_bit_register_2_q4),
    .Q3(n8_bit_register_2_q3), .Q2(n8_bit_register_2_q2), .Q1(n8_bit_register_2_q1), .Q0(n8_bit_register_2_q0));  // open: EN, HEX_OUT
  _8_BIT_COUNTER u_8_bit_counter_1 (
    .CLK(and_1_out), .EN(program_decoder_1_pc_en), .LOAD(program_decoder_1_pc_lod),
    .COUNT(program_decoder_1_pc_count), .CLEAR(or_1_out), .D7(ram_chip_1_q0[7]), .D6(ram_chip_1_q0[6]),
    .D5(ram_chip_1_q0[5]), .D4(ram_chip_1_q0[4]), .D3(ram_chip_1_q0[3]), .D2(ram_chip_1_q0[2]),
    .D1(ram_chip_1_q0[1]), .D0(ram_chip_1_q0[0]), .Q7(ram_chip_1_q0[7]), .Q6(ram_chip_1_q0[6]),
    .Q5(ram_chip_1_q0[5]), .Q4(ram_chip_1_q0[4]), .Q3(ram_chip_1_q0[3]), .Q2(ram_chip_1_q0[2]),
    .Q1(ram_chip_1_q0[1]), .Q0(ram_chip_1_q0[0]), .COUNTER_HEX(n8_bit_counter_1_counter_hex));
  _8_BIT_REGISTER u_8_bit_register_3 (
    .CLK(and_1_out), .EN(program_decoder_1_ir3_en), .LOAD(program_decoder_1_ir3_lod), .CLEAR(or_1_out),
    .D7(ram_chip_1_q0[7]), .D6(ram_chip_1_q0[6]), .D5(ram_chip_1_q0[5]), .D4(ram_chip_1_q0[4]),
    .D3(ram_chip_1_q0[3]), .D2(ram_chip_1_q0[2]), .D1(ram_chip_1_q0[1]), .D0(ram_chip_1_q0[0]),
    .Q7(ram_chip_1_q0[7]), .Q6(ram_chip_1_q0[6]), .Q5(ram_chip_1_q0[5]), .Q4(ram_chip_1_q0[4]),
    .Q3(ram_chip_1_q0[3]), .Q2(ram_chip_1_q0[2]), .Q1(ram_chip_1_q0[1]), .Q0(ram_chip_1_q0[0]),
    .HEX_OUT(n8_bit_register_3_hex_out));
  _8_BIT_COUNTER u_8_bit_counter_2 (
    .CLK(and_1_out), .EN(program_decoder_1_sp_en), .LOAD(program_decoder_1_sp_lod),
    .COUNT(program_decoder_1_sp_count), .CLEAR(or_1_out), .D7(ram_chip_1_q0[7]), .D6(ram_chip_1_q0[6]),
    .D5(ram_chip_1_q0[5]), .D4(ram_chip_1_q0[4]), .D3(ram_chip_1_q0[3]), .D2(ram_chip_1_q0[2]),
    .D1(ram_chip_1_q0[1]), .D0(ram_chip_1_q0[0]), .Q7(ram_chip_1_q0[7]), .Q6(ram_chip_1_q0[6]),
    .Q5(ram_chip_1_q0[5]), .Q4(ram_chip_1_q0[4]), .Q3(ram_chip_1_q0[3]), .Q2(ram_chip_1_q0[2]),
    .Q1(ram_chip_1_q0[1]), .Q0(ram_chip_1_q0[0]));  // open: COUNTER_HEX
  Hex_Digit_Display hex_digit_display_2 (.value(n8_bit_counter_1_counter_hex[7:4]));  // open: dp
  Hex_Digit_Display hex_digit_display_3 (.value(n8_bit_register_3_hex_out[7:4]));  // open: dp
  Hex_Digit_Display hex_digit_display_4 (.value(n8_bit_counter_1_counter_hex[3:0]));  // open: dp
  Hex_Digit_Display hex_digit_display_5 (.value(n8_bit_register_3_hex_out[3:0]));  // open: dp
  _8_BIT_REGISTER u_8_bit_register_4 (
    .CLK(and_1_out), .EN(program_decoder_1_bp_en), .LOAD(program_decoder_1_bp_lod), .CLEAR(or_1_out),
    .D7(ram_chip_1_q0[7]), .D6(ram_chip_1_q0[6]), .D5(ram_chip_1_q0[5]), .D4(ram_chip_1_q0[4]),
    .D3(ram_chip_1_q0[3]), .D2(ram_chip_1_q0[2]), .D1(ram_chip_1_q0[1]), .D0(ram_chip_1_q0[0]),
    .Q7(ram_chip_1_q0[7]), .Q6(ram_chip_1_q0[6]), .Q5(ram_chip_1_q0[5]), .Q4(ram_chip_1_q0[4]),
    .Q3(ram_chip_1_q0[3]), .Q2(ram_chip_1_q0[2]), .Q1(ram_chip_1_q0[1]), .Q0(ram_chip_1_q0[0]));  // open: HEX_OUT
  Hex_Digit_Display hex_digit_display_6 (.value(ram_chip_1_q0[7:4]));  // open: dp
  Hex_Digit_Display hex_digit_display_7 (.value(ram_chip_1_q0[3:0]));  // open: dp
  REGISTER_UNIT___NEW register_unit_new_1 (
    .CLK(and_1_out), .LOAD(program_decoder_1_reg_lod), .EN(program_decoder_1_reg_en), .CLEAR(or_1_out),
    .R7(n8_bit_register_2_q7), .R6(n8_bit_register_2_q6), .R5(n8_bit_register_2_q5),
    .R4(n8_bit_register_2_q4), .D7(ram_chip_1_q0[7]), .D6(ram_chip_1_q0[6]), .D5(ram_chip_1_q0[5]),
    .D4(ram_chip_1_q0[4]), .D3(ram_chip_1_q0[3]), .D2(ram_chip_1_q0[2]), .D1(ram_chip_1_q0[1]),
    .D0(ram_chip_1_q0[0]), .R3(n8_bit_register_2_q3), .R2(n8_bit_register_2_q2), .R1(n8_bit_register_2_q1),
    .R0(n8_bit_register_2_q0), .Q7(ram_chip_1_q0[7]), .Q6(ram_chip_1_q0[6]), .Q5(ram_chip_1_q0[5]),
    .Q4(ram_chip_1_q0[4]), .Q3(ram_chip_1_q0[3]), .Q2(ram_chip_1_q0[2]), .Q1(ram_chip_1_q0[1]),
    .Q0(ram_chip_1_q0[0]), .ALU7(register_unit_new_1_alu7), .ALU6(register_unit_new_1_alu6),
    .ALU5(register_unit_new_1_alu5), .ALU4(register_unit_new_1_alu4), .ALU3(register_unit_new_1_alu3),
    .ALU2(register_unit_new_1_alu2), .ALU1(register_unit_new_1_alu1), .ALU0(register_unit_new_1_alu0));
  ALU alu_1 (
    .S0(ram_chip_1_q0[0]), .S1(ram_chip_1_q0[1]), .S2(ram_chip_1_q0[2]), .S3(ram_chip_1_q0[3]),
    .S4(ram_chip_1_q0[4]), .S5(ram_chip_1_q0[5]), .S6(ram_chip_1_q0[6]), .S7(ram_chip_1_q0[7]),
    .OP_0(program_decoder_1_alu_op[0]), .OP_1(program_decoder_1_alu_op[1]),
    .OP_2(program_decoder_1_alu_op[2]), .OP_3(program_decoder_1_alu_op[3]), .A7(register_unit_new_1_alu7),
    .A6(register_unit_new_1_alu6), .A5(register_unit_new_1_alu5), .A4(register_unit_new_1_alu4),
    .A3(register_unit_new_1_alu3), .A2(register_unit_new_1_alu2), .A1(register_unit_new_1_alu1),
    .A0(register_unit_new_1_alu0), .D7(ram_chip_1_q0[7]), .D6(ram_chip_1_q0[6]), .D5(ram_chip_1_q0[5]),
    .D4(ram_chip_1_q0[4]), .D3(ram_chip_1_q0[3]), .D2(ram_chip_1_q0[2]), .D1(ram_chip_1_q0[1]),
    .D0(ram_chip_1_q0[0]), .GRTR(alu_1_grtr), .LESS(alu_1_less), .EQL(alu_1_eql), .CARRY(alu_1_carry),
    .LOAD(program_decoder_1_alu_lod), .EN(program_decoder_1_alu_en), .CLEAR(or_1_out), .CLK(and_1_out));
  _8_BIT_REGISTER u_8_bit_register_5 (
    .CLK(and_1_out), .EN(or_1_out), .LOAD(program_decoder_1_flag_load), .CLEAR(or_1_out), .D7(1'b0),
    .D6(1'b0), .D5(1'b0), .D4(1'b0), .D3(alu_1_grtr), .D2(alu_1_less), .D1(alu_1_eql), .D0(alu_1_carry));  // open: Q7, Q6, Q5, Q4, Q3, Q2, Q1, Q0, HEX_OUT
endmodule

module _1_BIT_ADDER (
  input  A,
  input  CIN,
  input  B,
  output S,
  output COUT
);

  wire and_1_out, and_2_out, xor_1_out;

  xor xor_1 (xor_1_out, A, B);
  xor xor_2 (S, xor_1_out, CIN);
  and and_1 (and_1_out, xor_1_out, CIN);
  and and_2 (and_2_out, B, A);
  or or_1 (COUT, and_1_out, and_2_out);
endmodule

module _8_BIT_ADDER (
  input  A7,
  input  A6,
  input  A5,
  input  A4,
  input  A3,
  input  A2,
  input  A1,
  input  A0,
  input  CIN,
  input  B7,
  input  B6,
  input  B5,
  input  B4,
  input  B3,
  input  B2,
  input  B1,
  input  B0,
  output COUT,
  output S0,
  output S1,
  output S2,
  output S3,
  output S4,
  output S5,
  output S6,
  output S7
);

  wire n1_bit_adder_2_cout, n1_bit_adder_3_cout, n1_bit_adder_4_cout, n1_bit_adder_5_cout,
       n1_bit_adder_6_cout, n1_bit_adder_7_cout, n1_bit_adder_8_cout;

  _1_BIT_ADDER u_1_bit_adder_1 (.S(S7), .A(A7), .B(B7), .COUT(COUT), .CIN(n1_bit_adder_2_cout));
  _1_BIT_ADDER u_1_bit_adder_2 (.S(S6), .A(A6), .B(B6), .COUT(n1_bit_adder_2_cout), .CIN(n1_bit_adder_3_cout));
  _1_BIT_ADDER u_1_bit_adder_3 (.S(S5), .A(A5), .B(B5), .COUT(n1_bit_adder_3_cout), .CIN(n1_bit_adder_4_cout));
  _1_BIT_ADDER u_1_bit_adder_4 (.S(S4), .A(A4), .B(B4), .COUT(n1_bit_adder_4_cout), .CIN(n1_bit_adder_5_cout));
  _1_BIT_ADDER u_1_bit_adder_5 (.S(S3), .A(A3), .B(B3), .COUT(n1_bit_adder_5_cout), .CIN(n1_bit_adder_6_cout));
  _1_BIT_ADDER u_1_bit_adder_6 (.S(S2), .A(A2), .B(B2), .COUT(n1_bit_adder_6_cout), .CIN(n1_bit_adder_7_cout));
  _1_BIT_ADDER u_1_bit_adder_7 (.S(S1), .A(A1), .B(B1), .COUT(n1_bit_adder_7_cout), .CIN(n1_bit_adder_8_cout));
  _1_BIT_ADDER u_1_bit_adder_8 (.S(S0), .A(A0), .B(B0), .COUT(n1_bit_adder_8_cout), .CIN(CIN));

  // Notes on the sheet:
  //   B0: pull=up
  //   A0: pull=up
  //   A3: pull=up
  //   A7: pull=up
  //   B5: pull=up
  //   A2: pull=up
  //   A5: pull=up
  //   B6: pull=up
  //   A1: pull=up
  //   A6: pull=up
  //   A4: pull=up
  //   B2: pull=up
  //   B7: pull=up
  //   B3: pull=up
  //   CIN: pull=up
  //   B4: pull=up
  //   B1: pull=up
endmodule

module REGISTER_UNIT (
  input  D7,
  input  D6,
  input  D5,
  input  D4,
  input  D3,
  input  D2,
  input  D1,
  input  D0,
  input  R7,
  input  R6,
  input  R5,
  input  R4,
  input  R3,
  input  R2,
  input  R1,
  input  R0,
  input  CLK,
  input  LOAD,
  input  CLEAR,
  output [7:0] HEX_OUT,
  output Q7,
  output Q6,
  output Q5,
  output Q4,
  output Q3,
  output Q2,
  output Q1,
  output Q0
);

  wire and_1_out, and_2_out, and_3_out, and_4_out, decoder_1_out1, decoder_1_out2, decoder_1_out3,
       decoder_1_out4, decoder_2_out1, decoder_2_out2, decoder_2_out3, decoder_2_out4;
  wire [7:0] A_q, B_q, C_q, D_q;

  Decoder #(.select(4)) decoder_1 (
    .out1(decoder_1_out1), .out2(decoder_1_out2), .out3(decoder_1_out3), .out4(decoder_1_out4),
    .sel({R7, R6, R5, R4}), .en(LOAD));  // open: out0, out5, out6, out7, out8, out9, out10, out11, out12, out13, out14, out15
  Decoder #(.select(4)) decoder_2 (
    .out1(decoder_2_out1), .out2(decoder_2_out2), .out3(decoder_2_out3), .out4(decoder_2_out4),
    .sel({R3, R2, R1, R0}));  // open: out0, out5, out6, out7, out8, out9, out10, out11, out12, out13, out14, out15, en
  and and_1 (and_1_out, decoder_1_out1, LOAD);
  assign HEX_OUT = decoder_2_out1 ? A_q : 8'bz;  // Controlled_Buffer controlled_buffer_1
  Register A (.D({D7, D6, D5, D4, D3, D2, D1, D0}), .en(and_1_out), .Q(A_q), .clk(CLK), .clr(CLEAR));
  Register B (.D({D7, D6, D5, D4, D3, D2, D1, D0}), .en(and_2_out), .Q(B_q), .clk(CLK), .clr(CLEAR));
  assign HEX_OUT = decoder_2_out2 ? B_q : 8'bz;  // Controlled_Buffer controlled_buffer_2
  and and_2 (and_2_out, decoder_1_out2, LOAD);
  Register C (.D({D7, D6, D5, D4, D3, D2, D1, D0}), .en(and_3_out), .Q(C_q), .clk(CLK), .clr(CLEAR));
  and and_3 (and_3_out, decoder_1_out3, LOAD);
  assign HEX_OUT = decoder_2_out3 ? C_q : 8'bz;  // Controlled_Buffer controlled_buffer_3
  Register D (.D({D7, D6, D5, D4, D3, D2, D1, D0}), .en(and_4_out), .Q(D_q), .clk(CLK), .clr(CLEAR));
  and and_4 (and_4_out, decoder_1_out4, LOAD);
  assign HEX_OUT = decoder_2_out4 ? D_q : 8'bz;  // Controlled_Buffer controlled_buffer_4

  assign Q0 = HEX_OUT[0];
  assign Q1 = HEX_OUT[1];
  assign Q2 = HEX_OUT[2];
  assign Q3 = HEX_OUT[3];
  assign Q4 = HEX_OUT[4];
  assign Q5 = HEX_OUT[5];
  assign Q6 = HEX_OUT[6];
  assign Q7 = HEX_OUT[7];

  // Notes on the sheet:
  //   D1: pull=up
  //   D4: pull=up
  //   R1: pull=up
  //   D3: pull=up
  //   R2: pull=up
  //   R0: pull=up
  //   LOAD: pull=up
  //   R4: pull=up
  //   D0: pull=up
  //   R5: pull=up
  //   D5: pull=up
  //   R6: pull=up
  //   D7: pull=up
  //   R7: pull=up
  //   D2: pull=up
  //   D6: pull=up
  //   CLEAR: pull=up
  //   R3: pull=up
endmodule

module ALU (
  input  A7,
  input  A6,
  input  A5,
  input  A4,
  input  A3,
  input  A2,
  input  A1,
  input  A0,
  input  LOAD,
  input  EN,
  input  CLEAR,
  input  CLK,
  input  D7,
  input  D6,
  input  D5,
  input  D4,
  input  D3,
  input  D2,
  input  D1,
  input  D0,
  input  OP_0,
  input  OP_1,
  input  OP_2,
  input  OP_3,
  output GRTR,
  output S0,
  output LESS,
  output S1,
  output EQL,
  output S2,
  output CARRY,
  output S3,
  output S4,
  output S5,
  output S6,
  output S7
);

  wire decoder_1_out1, n8_bit_inverter_1_q0, n8_bit_inverter_1_q1, n8_bit_inverter_1_q2,
       n8_bit_inverter_1_q3, n8_bit_inverter_1_q4, n8_bit_inverter_1_q5, n8_bit_inverter_1_q6,
       n8_bit_inverter_1_q7;
  wire [7:0] ACCUM_q, n8_bit_adder_1_s0;

  Decoder #(.select(4)) decoder_1 (
    .out1(decoder_1_out1), .sel({OP_3, OP_2, OP_1, OP_0}));  // open: out0, out2, out3, out4, out5, out6, out7, out8, out9, out10, out11, out12, out13, out14, out15, en
  Comparator comparator_1 (.a({A7, A6, A5, A4, A3, A2, A1, A0}), .b(ACCUM_q), .gt(GRTR), .eq(EQL), .lt(LESS));
  assign {S7, S6, S5, S4, S3, S2, S1, S0} = EN ? n8_bit_adder_1_s0 : 8'bz;  // Controlled_Buffer controlled_buffer_1
  Register ACCUM (.D({D7, D6, D5, D4, D3, D2, D1, D0}), .en(LOAD), .Q(ACCUM_q), .clk(CLK), .clr(CLEAR));
  _8_BIT_ADDER u_8_bit_adder_1 (
    .S0(n8_bit_adder_1_s0[0]), .S1(n8_bit_adder_1_s0[1]), .S2(n8_bit_adder_1_s0[2]),
    .S3(n8_bit_adder_1_s0[3]), .S4(n8_bit_adder_1_s0[4]), .S5(n8_bit_adder_1_s0[5]),
    .S6(n8_bit_adder_1_s0[6]), .S7(n8_bit_adder_1_s0[7]), .A7(A7), .A6(A6), .A5(A5), .A4(A4), .A3(A3),
    .A2(A2), .A1(A1), .A0(A0), .B7(n8_bit_inverter_1_q7), .B6(n8_bit_inverter_1_q6),
    .B5(n8_bit_inverter_1_q5), .B4(n8_bit_inverter_1_q4), .B3(n8_bit_inverter_1_q3),
    .B2(n8_bit_inverter_1_q2), .B1(n8_bit_inverter_1_q1), .B0(n8_bit_inverter_1_q0), .COUT(CARRY),
    .CIN(decoder_1_out1));
  _8_BIT_INVERTER u_8_bit_inverter_1 (
    .Q7(n8_bit_inverter_1_q7), .Q6(n8_bit_inverter_1_q6), .Q5(n8_bit_inverter_1_q5),
    .Q4(n8_bit_inverter_1_q4), .Q3(n8_bit_inverter_1_q3), .Q2(n8_bit_inverter_1_q2),
    .Q1(n8_bit_inverter_1_q1), .Q0(n8_bit_inverter_1_q0), .D7(ACCUM_q[7]), .D6(ACCUM_q[6]), .D5(ACCUM_q[5]),
    .D4(ACCUM_q[4]), .D3(ACCUM_q[3]), .D2(ACCUM_q[2]), .D1(ACCUM_q[1]), .D0(ACCUM_q[0]),
    .INVERT(decoder_1_out1));

  // Notes on the sheet:
  //   OP_2: pull=up
  //   CLEAR: pull=up
  //   OP_3: pull=up
  //   OP_0: pull=up
  //   EN: pull=up
  //   LOAD: pull=up
  //   CLK: pull=up
  //   OP_1: pull=up
endmodule

module _8_BIT_INVERTER (
  input  INVERT,
  input  D7,
  input  D6,
  input  D5,
  input  D4,
  input  D3,
  input  D2,
  input  D1,
  input  D0,
  output Q7,
  output Q6,
  output Q5,
  output Q4,
  output Q3,
  output Q2,
  output Q1,
  output Q0
);

  xor xor_1 (Q7, INVERT, D7);
  xor xor_2 (Q6, INVERT, D6);
  xor xor_3 (Q3, INVERT, D3);
  xor xor_4 (Q4, INVERT, D4);
  xor xor_5 (Q5, INVERT, D5);
  xor xor_6 (Q1, INVERT, D1);
  xor xor_7 (Q0, INVERT, D0);
  xor xor_8 (Q2, INVERT, D2);

  // Notes on the sheet:
  //   D5: pull=up
  //   D4: pull=up
  //   INVERT: pull=up
  //   D2: pull=up
  //   D3: pull=up
  //   D6: pull=up
  //   D7: pull=up
  //   D0: pull=up
  //   D1: pull=up
endmodule

module _8_BIT_REGISTER (
  input  D7,
  input  D6,
  input  D5,
  input  D4,
  input  D3,
  input  D2,
  input  D1,
  input  D0,
  input  CLK,
  input  EN,
  input  LOAD,
  input  CLEAR,
  output [7:0] HEX_OUT,
  output Q7,
  output Q6,
  output Q5,
  output Q4,
  output Q3,
  output Q2,
  output Q1,
  output Q0
);

  assign {Q7, Q6, Q5, Q4, Q3, Q2, Q1, Q0} = EN ? HEX_OUT : 8'bz;  // Controlled_Buffer controlled_buffer_1
  Register register_1 (.D({D7, D6, D5, D4, D3, D2, D1, D0}), .en(LOAD), .Q(HEX_OUT), .clk(CLK), .clr(CLEAR));

  // Notes on the sheet:
  //   EN: pull=up
  //   CLK: pull=up
endmodule

module CLOCK (
  input  PWR,
  input  MODE,
  input  STEP,
  output POWER,
  output MODE_2,
  output CLK
);

  wire clock_1_out, controlled_buffer_1_out, not_1_out;

  Clock clock_1 (.out(clock_1_out));
  Counter #(.width(1), .max('h1)) counter_1 (.count(PWR), .Q(POWER), .clk(PWR));  // open: load, D, carry, clr
  Counter #(.width(1), .max('h1)) counter_2 (.count(MODE), .Q(MODE_2), .clk(MODE));  // open: load, D, carry, clr
  assign controlled_buffer_1_out = not_1_out ? clock_1_out : 1'bz;  // Controlled_Buffer controlled_buffer_1
  not not_1 (not_1_out, MODE_2);
  assign controlled_buffer_1_out = MODE_2 ? STEP : 1'bz;  // Controlled_Buffer controlled_buffer_2
  and and_1 (CLK, POWER, controlled_buffer_1_out);

  // Notes on the sheet:
  //   STEP: pull=up
  //   PWR: pull=up
  //   MODE: pull=up
endmodule

module _8_BIT_BUFFER (
  input  D7,
  input  D6,
  input  D5,
  input  D4,
  input  D3,
  input  D2,
  input  D1,
  input  D0,
  input  EN,
  output Q7,
  output Q6,
  output Q5,
  output Q4,
  output Q3,
  output Q2,
  output Q1,
  output Q0
);

  assign Q7 = EN ? D7 : 1'bz;  // Controlled_Buffer controlled_buffer_1
  assign Q4 = EN ? D4 : 1'bz;  // Controlled_Buffer controlled_buffer_2
  assign Q6 = EN ? D6 : 1'bz;  // Controlled_Buffer controlled_buffer_3
  assign Q5 = EN ? D5 : 1'bz;  // Controlled_Buffer controlled_buffer_4
  assign Q3 = EN ? D3 : 1'bz;  // Controlled_Buffer controlled_buffer_5
  assign Q2 = EN ? D2 : 1'bz;  // Controlled_Buffer controlled_buffer_6
  assign Q1 = EN ? D1 : 1'bz;  // Controlled_Buffer controlled_buffer_7
  assign Q0 = EN ? D0 : 1'bz;  // Controlled_Buffer controlled_buffer_8
endmodule

module RAM_CHIP (
  input  D7,
  input  D6,
  input  D5,
  input  D4,
  input  D3,
  input  D2,
  input  D1,
  input  D0,
  input  A7,
  input  A6,
  input  A5,
  input  A4,
  input  A3,
  input  A2,
  input  MAR_LOAD,
  input  A1,
  input  A0,
  input  CLK,
  input  EN,
  input  LOAD,
  input  CLEAR,
  output Q7,
  output Q6,
  output Q5,
  output Q4,
  output Q3,
  output Q2,
  output Q1,
  output Q0
);

  wire [7:0] n8_bit_register_1_q0;

  _8_BIT_REGISTER u_8_bit_register_1 (
    .CLK(CLK), .LOAD(MAR_LOAD), .CLEAR(CLEAR), .D7(A7), .D6(A6), .D5(A5), .D4(A4), .D3(A3), .D2(A2), .D1(A1),
    .D0(A0), .Q7(n8_bit_register_1_q0[7]), .Q6(n8_bit_register_1_q0[6]), .Q5(n8_bit_register_1_q0[5]),
    .Q4(n8_bit_register_1_q0[4]), .Q3(n8_bit_register_1_q0[3]), .Q2(n8_bit_register_1_q0[2]),
    .Q1(n8_bit_register_1_q0[1]), .Q0(n8_bit_register_1_q0[0]));  // open: EN, HEX_OUT
  RAM #(.bus("separate")) ram_1 (
    .addr(n8_bit_register_1_q0), .din({D7, D6, D5, D4, D3, D2, D1, D0}),
    .data({Q7, Q6, Q5, Q4, Q3, Q2, Q1, Q0}), .str(LOAD), .clk(CLK), .ld(EN), .clr(CLEAR));  // open: sel

  // Notes on the sheet:
  //   A3: pull=up
  //   D5: pull=up
  //   CLEAR: pull=up
  //   CLK: pull=up
  //   A0: pull=up
  //   A5: pull=up
  //   D3: pull=up
  //   A7: pull=up
  //   MAR_LOAD: pull=up
  //   A2: pull=up
  //   D2: pull=up
  //   EN: pull=up
  //   A1: pull=up
  //   D0: pull=up
  //   D4: pull=up
  //   D7: pull=up
  //   LOAD: pull=up
  //   D1: pull=up
  //   D6: pull=up
  //   A4: pull=up
  //   A6: pull=up
endmodule

module _8_BIT_COUNTER (
  input  D7,
  input  D6,
  input  D5,
  input  D4,
  input  D3,
  input  D2,
  input  D1,
  input  D0,
  input  CLK,
  input  EN,
  input  LOAD,
  input  COUNT,
  input  CLEAR,
  output [7:0] COUNTER_HEX,
  output Q7,
  output Q6,
  output Q5,
  output Q4,
  output Q3,
  output Q2,
  output Q1,
  output Q0
);

  Counter counter_1 (
    .load(LOAD), .D({D7, D6, D5, D4, D3, D2, D1, D0}), .count(COUNT), .Q(COUNTER_HEX), .clk(CLK), .clr(CLEAR));  // open: carry
  assign {Q7, Q6, Q5, Q4, Q3, Q2, Q1, Q0} = EN ? COUNTER_HEX : 8'bz;  // Controlled_Buffer controlled_buffer_1

  // Notes on the sheet:
  //   CLEAR: pull=up
  //   D5: pull=up
  //   D0: pull=up
  //   D6: pull=up
  //   D7: pull=up
  //   D1: pull=up
  //   D2: pull=up
  //   D3: pull=up
  //   D4: pull=up
endmodule

module PROGRAM_DECODER (
  input  I7,
  input  I6,
  input  I5,
  input  I4,
  input  I3,
  input  I2,
  input  I1,
  input  I0,
  input  R7,
  input  R6,
  input  R5,
  input  R4,
  input  R3,
  input  R2,
  input  R1,
  input  R0,
  input  CLK,
  input  CLEAR,
  output [3:0] out_19,
  output PC_COUNT,
  output PC_EN,
  output PC_LOD,
  output IR_LOD,
  output IR2_LOD,
  output IR3_LOD,
  output MAR_LOD,
  output MEM_EN,
  output MEM_LOD,
  output REG_EN,
  output REG_LOD,
  output ALU_EN,
  output ALU_LOD,
  output FLAG_LOAD,
  output IR3_EN,
  output HLT,
  output SP_COUNT,
  output IN,
  output OUT,
  output [3:0] ALU_OP,
  output SP_LOD,
  output SP_EN,
  output BP_LOD,
  output BP_EN
);

  wire not_1_out, or_1_out;
  wire [31:17] rom_1_data;

  Counter #(.width(4), .max('h8)) counter_1 (
    .Q(out_19), .clk(not_1_out), .clr(or_1_out));  // open: load, D, count, carry
  not not_1 (not_1_out, CLK);
  or or_1 (or_1_out, CLEAR, rom_1_data[17]);
  ROM #(.addrWidth(20), .dataWidth(32)) rom_1 (
    .addr({I7, I6, I5, I4, I3, I2, I1, I0, R7, R6, R5, R4, R3, R2, R1, R0, out_19}),
    .data({rom_1_data[31:28], BP_EN, BP_LOD, SP_EN, SP_LOD, ALU_OP, OUT, IN, rom_1_data[17], SP_COUNT, HLT, IR3_EN, FLAG_LOAD, ALU_LOD, ALU_EN, REG_LOD, REG_EN, MEM_LOD, MEM_EN, MAR_LOD, IR3_LOD, IR2_LOD, IR_LOD, PC_LOD, PC_EN, PC_COUNT}));  // open: sel

  // Notes on the sheet:
  //   contents of rom_1 (hex, n*v repeats v):
  //   42 89 14*0 42 89 14*0 42 89 14*0 42 89 14*0 42 89 14*0 42 89 14*0 42 89 14*0 42 89 14*0 42 89 14*0
  //   42 89 14*0 42 89 14*0 42 89 14*0 42 89 14*0 42 89 14*0 42 89 14*0 42 89 14*0 42 89 14*0 42 89 14*0
  //   42 89 14*0 42 89 14*0 42 89 14*0 42 89 14*0 42 89 14*0 42 89 14*0 42 89 14*0 42 89 14*0 42 89 14*0
  //   42 89 14*0 42 89 14*0 42 89 14*0 42 89 14*0 42 89 14*0 42 89 14*0 42 89 14*0 42 89 14*0 42 89 14*0
  //   42 89 14*0 42 89 14*0 42 89 14*0 42 89 14*0 42 89 14*0 42 89 14*0 42 89 14*0 42 89 14*0 42 89 14*0
  //   42 89 14*0 42 89 14*0 42 89 14*0 42 89 14*0 42 89 14*0 42 89 14*0 42 89 14*0 42 89 14*0 42 89 14*0
  //   42 89 14*0 42 89 14*0 42 89 14*0 42 89 14*0 42 89 14*0 42 89 14*0 42 89 14*0 42 89 14*0 42 89 14*0
  //   42 89 14*0 42 89 14*0 42 89 14*0 42 89 14*0 42 89 14*0 42 89 14*0 42 89 14*0 42 89 14*0 42 89 14*0
  //   42 89 14*0 42 89 14*0 42 89 14*0 42 89 14*0 42 89 14*0 42 89 14*0 42 89 14*0 42 89 14*0 42 89 14*0
  //   42 89 14*0 42 89 14*0 42 89 14*0 42 89 14*0 42 89 14*0 42 89 14*0 42 89 14*0 42 89 14*0 42 89 14*0
  //   42 89 14*0 42 89 14*0 42 89 14*0 42 89 14*0 42 89 14*0 42 89 14*0 42 89 14*0 42 89 14*0 42 89 14*0
  //   42 89 14*0 42 89 14*0 42 89 14*0 42 89 14*0 42 89 14*0 42 89 14*0 42 89 14*0 42 89 14*0 42 89 14*0
  //   42 89 14*0 42 89 14*0 42 89 14*0 42 89 14*0 42 89 14*0 42 89 14*0 42 89 14*0 42 89 14*0 42 89 14*0
  //   42 89 14*0 42 89 14*0 42 89 14*0 42 89 14*0 42 89 14*0 42 89 14*0 42 89 14*0 42 89 14*0 42 89 14*0
  //   42 89 14*0 42 89 14*0 42 89 14*0 42 89 14*0 42 89 14*0 42 89 14*0 42 89 14*0 42 89 14*0 42 89 14*0
  //   42 89 14*0 42 89 14*0 42 89 14*0 42 89 14*0 42 89 14*0 42 89 14*0 42 89 14*0 42 89 14*0 42 89 14*0
  //   42 89 14*0 42 89 14*0 42 89 14*0 42 89 14*0 42 89 14*0 42 89 14*0 42 89 14*0 42 89 14*0 42 89 14*0
  //   42 89 14*0 42 89 14*0 42 89 14*0 42 89 14*0 42 89 14*0 42 89 14*0 42 89 14*0 42 89 14*0 42 89 14*0
  //   42 89 14*0 42 89 14*0 42 89 14*0 42 89 14*0 42 89 14*0 42 89 14*0 42 89 14*0 42 89 14*0 42 89 14*0
  //   42 89 14*0 42 89 14*0 42 89 14*0 42 89 14*0 42 89 14*0 42 89 14*0 42 89 14*0 42 89 14*0 42 89 14*0
  //   42 89 14*0 42 89 14*0 42 89 14*0 42 89 14*0 42 89 14*0 42 89 14*0 42 89 14*0 42 89 14*0 42 89 14*0
  //   42 89 14*0 42 89 14*0 42 89 14*0 42 89 14*0 42 89 14*0 42 89 14*0 42 89 14*0 42 89 14*0 42 89 14*0
  //   42 89 14*0 42 89 14*0 42 89 14*0 42 89 14*0 42 89 14*0 42 89 14*0 42 89 14*0 42 89 14*0 42 89 14*0
  //   42 89 14*0 42 89 14*0 42 89 14*0 42 89 14*0 42 89 14*0 42 89 14*0 42 89 14*0 42 89 14*0 42 89 14*0
  //   42 89 14*0 42 89 14*0 42 89 14*0 42 89 14*0 42 89 14*0 42 89 14*0 42 89 14*0 42 89 14*0 42 89 14*0
  //   42 89 14*0 42 89 14*0 42 89 14*0 42 89 14*0 42 89 14*0 42 89 14*0 42 89 14*0 42 89 14*0 42 89 14*0
  //   42 89 14*0 42 89 14*0 42 89 14*0 42 89 14*0 42 89 14*0 42 89 14*0 42 89 14*0 42 89 14*0 42 89 14*0
  //   42 89 14*0 42 89 14*0 42 89 14*0 42 89 14*0 42 89 14*0 42 89 14*0 42 89 14*0 42 89 14*0 42 89 14*0
  //   42 89 14*0 42 89 14*0 42 89 14*0 42 89 14*0 42 89 42 91 600 20000 10*0 42 89 42 91 600 20000 10*0 42
  //   89 42 91 600 20000 10*0 42 89 42 91 600 20000 10*0 42 89 42 91 600 20000 10*0 42 89 42 91 600 20000
  //   10*0 42 89 42 91 600 20000 10*0 42 89 42 91 600 20000 10*0 42 89 42 91 42 480 20000 9*0 42 89 42 91
  //   42 c1 480 20000 8*0 42 89 42 91 600 20000 10*0 42 89 42 91 600 20000 10*0 42 89 42 91 600 20000 10*0
  //   42 89 42 91 600 20000 10*0 42 89 42 91 600 20000 10*0 42 89 42 91 600 20000 10*0 42 89 42 91 600
  //   20000 10*0 42 89 42 91 600 20000 10*0 42 89 42 91 600 20000 10*0 42 89 42 91 600 20000 10*0 42 89 42
  //   91 600 20000 10*0 42 89 42 91 600 20000 10*0 42 89 42 91 600 20000 10*0 42 89 42 91 600 20000 10*0
  //   42 89 42 91 42 480 20000 9*0 42 89 42 91 42 c1 480 20000 8*0 42 89 42 91 600 20000 10*0 42 89 42 91
  //   600 20000 10*0 42 89 42 91 600 20000 10*0 42 89 42 91 600 20000 10*0 42 89 42 91 600 20000 10*0 42
  //   89 42 91 600 20000 10*0 42 89 42 91 600 20000 10*0 42 89 42 91 600 20000 10*0 42 89 42 91 600 20000
  //   10*0 42 89 42 91 600 20000 10*0 42 89 42 91 600 20000 10*0 42 89 42 91 600 20000 10*0 42 89 42 91
  //   600 20000 10*0 42 89 42 91 600 20000 10*0 42 89 42 91 42 480 20000 9*0 42 89 42 91 42 c1 480 20000
  //   8*0 42 89 42 91 600 20000 10*0 42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
endmodule

module REGISTER_UNIT___NEW (
  input  D7,
  input  D6,
  input  D5,
  input  D4,
  input  D3,
  input  D2,
  input  D1,
  input  D0,
  input  R7,
  input  R6,
  input  R5,
  input  R4,
  input  CLK,
  input  LOAD,
  input  EN,
  input  CLEAR,
  input  R3,
  input  R2,
  input  R1,
  input  R0,
  output ALU7,
  output ALU6,
  output ALU5,
  output ALU4,
  output ALU3,
  output ALU2,
  output ALU1,
  output ALU0,
  output Q7,
  output Q6,
  output Q5,
  output Q4,
  output Q3,
  output Q2,
  output Q1,
  output Q0
);

  wire and_1_out, and_2_out, and_3_out, and_4_out, and_5_out, and_6_out, and_7_out, and_8_out, and_9_out,
       and_10_out, and_11_out, and_12_out, and_13_out, and_14_out, and_15_out, and_16_out, and_17_out,
       and_18_out, and_19_out, and_20_out, and_21_out, and_22_out, and_23_out, and_24_out, and_25_out,
       and_26_out, and_27_out, and_28_out, and_29_out, and_30_out, and_31_out, and_32_out, decoder_1_out0,
       decoder_1_out1, decoder_1_out2, decoder_1_out3, decoder_1_out4, decoder_1_out5, decoder_1_out6,
       decoder_1_out7, decoder_1_out8, decoder_1_out9, decoder_1_out10, decoder_1_out11, decoder_1_out12,
       decoder_1_out13, decoder_1_out14, decoder_1_out15, decoder_2_out0, decoder_2_out1, decoder_2_out2,
       decoder_2_out3, decoder_2_out4, decoder_2_out5, decoder_2_out6, decoder_2_out7, decoder_2_out8,
       decoder_2_out9, decoder_2_out10, decoder_2_out11, decoder_2_out12, decoder_2_out13, decoder_2_out14,
       decoder_2_out15;
  wire [7:0] R0_q, R1_q, R2_q, R3_q, R4_q, R5_q, R6_q, R7_q, R8_q, R9_q, R10_q, R11_q, R12_q, R13_q, R14_q,
       R15_q, undriven;

  Decoder #(.select(4)) decoder_1 (
    .out0(decoder_1_out0), .out1(decoder_1_out1), .out2(decoder_1_out2), .out3(decoder_1_out3),
    .out4(decoder_1_out4), .out5(decoder_1_out5), .out6(decoder_1_out6), .out7(decoder_1_out7),
    .out8(decoder_1_out8), .out9(decoder_1_out9), .out10(decoder_1_out10), .out11(decoder_1_out11),
    .out12(decoder_1_out12), .out13(decoder_1_out13), .out14(decoder_1_out14), .out15(decoder_1_out15),
    .sel({R7, R6, R5, R4}));  // open: en
  Decoder #(.select(4)) decoder_2 (
    .out0(decoder_2_out0), .out1(decoder_2_out1), .out2(decoder_2_out2), .out3(decoder_2_out3),
    .out4(decoder_2_out4), .out5(decoder_2_out5), .out6(decoder_2_out6), .out7(decoder_2_out7),
    .out8(decoder_2_out8), .out9(decoder_2_out9), .out10(decoder_2_out10), .out11(decoder_2_out11),
    .out12(decoder_2_out12), .out13(decoder_2_out13), .out14(decoder_2_out14), .out15(decoder_2_out15),
    .sel({R3, R2, R1, R0}));  // open: en
  and and_1 (and_1_out, LOAD, decoder_1_out8);
  Register R8 (.D(undriven), .en(and_1_out), .Q(R8_q), .clk(CLK), .clr(CLEAR));
  and and_2 (and_2_out, LOAD, decoder_1_out0);
  Register u_R0 (.D({D7, D6, D5, D4, D3, D2, D1, D0}), .en(and_2_out), .Q(R0_q), .clk(CLK), .clr(CLEAR));
  and and_3 (and_3_out, LOAD, decoder_1_out9);
  Register R9 (.D(undriven), .en(and_3_out), .Q(R9_q), .clk(CLK), .clr(CLEAR));
  assign {ALU7, ALU6, ALU5, ALU4, ALU3, ALU2, ALU1, ALU0} = decoder_1_out8 ? R8_q : 8'bz;  // Controlled_Buffer controlled_buffer_1
  assign {Q7, Q6, Q5, Q4, Q3, Q2, Q1, Q0} = and_4_out ? R8_q : 8'bz;  // Controlled_Buffer controlled_buffer_2
  and and_4 (and_4_out, decoder_2_out8, EN);
  and and_5 (and_5_out, LOAD, decoder_1_out1);
  Register u_R1 (.D({D7, D6, D5, D4, D3, D2, D1, D0}), .en(and_5_out), .Q(R1_q), .clk(CLK), .clr(CLEAR));
  assign {ALU7, ALU6, ALU5, ALU4, ALU3, ALU2, ALU1, ALU0} = decoder_1_out0 ? R0_q : 8'bz;  // Controlled_Buffer controlled_buffer_3
  assign {Q7, Q6, Q5, Q4, Q3, Q2, Q1, Q0} = and_6_out ? R0_q : 8'bz;  // Controlled_Buffer controlled_buffer_4
  and and_6 (and_6_out, decoder_2_out0, EN);
  and and_7 (and_7_out, LOAD, decoder_1_out10);
  Register R10 (.D(undriven), .en(and_7_out), .Q(R10_q), .clk(CLK), .clr(CLEAR));
  assign {ALU7, ALU6, ALU5, ALU4, ALU3, ALU2, ALU1, ALU0} = decoder_1_out9 ? R9_q : 8'bz;  // Controlled_Buffer controlled_buffer_5
  assign {Q7, Q6, Q5, Q4, Q3, Q2, Q1, Q0} = and_8_out ? R9_q : 8'bz;  // Controlled_Buffer controlled_buffer_6
  and and_8 (and_8_out, decoder_2_out9, EN);
  and and_9 (and_9_out, LOAD, decoder_1_out2);
  Register u_R2 (.D({D7, D6, D5, D4, D3, D2, D1, D0}), .en(and_9_out), .Q(R2_q), .clk(CLK), .clr(CLEAR));
  assign {ALU7, ALU6, ALU5, ALU4, ALU3, ALU2, ALU1, ALU0} = decoder_1_out1 ? R1_q : 8'bz;  // Controlled_Buffer controlled_buffer_7
  assign {Q7, Q6, Q5, Q4, Q3, Q2, Q1, Q0} = and_10_out ? R1_q : 8'bz;  // Controlled_Buffer controlled_buffer_8
  and and_10 (and_10_out, decoder_2_out1, EN);
  and and_11 (and_11_out, LOAD, decoder_1_out11);
  Register R11 (.D(undriven), .en(and_11_out), .Q(R11_q), .clk(CLK), .clr(CLEAR));
  assign {ALU7, ALU6, ALU5, ALU4, ALU3, ALU2, ALU1, ALU0} = decoder_1_out10 ? R10_q : 8'bz;  // Controlled_Buffer controlled_buffer_9
  assign {Q7, Q6, Q5, Q4, Q3, Q2, Q1, Q0} = and_12_out ? R10_q : 8'bz;  // Controlled_Buffer controlled_buffer_10
  and and_12 (and_12_out, decoder_2_out10, EN);
  and and_13 (and_13_out, LOAD, decoder_1_out3);
  Register u_R3 (.D({D7, D6, D5, D4, D3, D2, D1, D0}), .en(and_13_out), .Q(R3_q), .clk(CLK), .clr(CLEAR));
  assign {ALU7, ALU6, ALU5, ALU4, ALU3, ALU2, ALU1, ALU0} = decoder_1_out2 ? R2_q : 8'bz;  // Controlled_Buffer controlled_buffer_11
  assign {Q7, Q6, Q5, Q4, Q3, Q2, Q1, Q0} = and_14_out ? R2_q : 8'bz;  // Controlled_Buffer controlled_buffer_12
  and and_14 (and_14_out, decoder_2_out2, EN);
  and and_15 (and_15_out, LOAD, decoder_1_out12);
  Register R12 (.D(undriven), .en(and_15_out), .Q(R12_q), .clk(CLK), .clr(CLEAR));
  assign {ALU7, ALU6, ALU5, ALU4, ALU3, ALU2, ALU1, ALU0} = decoder_1_out11 ? R11_q : 8'bz;  // Controlled_Buffer controlled_buffer_13
  assign {Q7, Q6, Q5, Q4, Q3, Q2, Q1, Q0} = and_16_out ? R11_q : 8'bz;  // Controlled_Buffer controlled_buffer_14
  and and_16 (and_16_out, decoder_2_out11, EN);
  and and_17 (and_17_out, LOAD, decoder_1_out4);
  Register u_R4 (.D({D7, D6, D5, D4, D3, D2, D1, D0}), .en(and_17_out), .Q(R4_q), .clk(CLK), .clr(CLEAR));
  assign {ALU7, ALU6, ALU5, ALU4, ALU3, ALU2, ALU1, ALU0} = decoder_1_out3 ? R3_q : 8'bz;  // Controlled_Buffer controlled_buffer_15
  assign {Q7, Q6, Q5, Q4, Q3, Q2, Q1, Q0} = and_18_out ? R3_q : 8'bz;  // Controlled_Buffer controlled_buffer_16
  and and_18 (and_18_out, decoder_2_out3, EN);
  and and_19 (and_19_out, LOAD, decoder_1_out13);
  Register R13 (.D(undriven), .en(and_19_out), .Q(R13_q), .clk(CLK), .clr(CLEAR));
  assign {ALU7, ALU6, ALU5, ALU4, ALU3, ALU2, ALU1, ALU0} = decoder_1_out12 ? R12_q : 8'bz;  // Controlled_Buffer controlled_buffer_17
  assign {Q7, Q6, Q5, Q4, Q3, Q2, Q1, Q0} = and_20_out ? R12_q : 8'bz;  // Controlled_Buffer controlled_buffer_18
  and and_20 (and_20_out, decoder_2_out12, EN);
  and and_21 (and_21_out, LOAD, decoder_1_out5);
  Register u_R5 (.D({D7, D6, D5, D4, D3, D2, D1, D0}), .en(and_21_out), .Q(R5_q), .clk(CLK), .clr(CLEAR));
  assign {ALU7, ALU6, ALU5, ALU4, ALU3, ALU2, ALU1, ALU0} = decoder_1_out4 ? R4_q : 8'bz;  // Controlled_Buffer controlled_buffer_19
  assign {Q7, Q6, Q5, Q4, Q3, Q2, Q1, Q0} = and_22_out ? R4_q : 8'bz;  // Controlled_Buffer controlled_buffer_20
  and and_22 (and_22_out, decoder_2_out4, EN);
  and and_23 (and_23_out, LOAD, decoder_1_out14);
  Register R14 (.D(undriven), .en(and_23_out), .Q(R14_q), .clk(CLK), .clr(CLEAR));
  assign {ALU7, ALU6, ALU5, ALU4, ALU3, ALU2, ALU1, ALU0} = decoder_1_out13 ? R13_q : 8'bz;  // Controlled_Buffer controlled_buffer_21
  assign {Q7, Q6, Q5, Q4, Q3, Q2, Q1, Q0} = and_24_out ? R13_q : 8'bz;  // Controlled_Buffer controlled_buffer_22
  and and_24 (and_24_out, decoder_2_out13, EN);
  and and_25 (and_25_out, LOAD, decoder_1_out6);
  Register u_R6 (.D({D7, D6, D5, D4, D3, D2, D1, D0}), .en(and_25_out), .Q(R6_q), .clk(CLK), .clr(CLEAR));
  assign {ALU7, ALU6, ALU5, ALU4, ALU3, ALU2, ALU1, ALU0} = decoder_1_out5 ? R5_q : 8'bz;  // Controlled_Buffer controlled_buffer_23
  assign {Q7, Q6, Q5, Q4, Q3, Q2, Q1, Q0} = and_26_out ? R5_q : 8'bz;  // Controlled_Buffer controlled_buffer_24
  and and_26 (and_26_out, decoder_2_out5, EN);
  and and_27 (and_27_out, LOAD, decoder_1_out15);
  Register R15 (.D(undriven), .en(and_27_out), .Q(R15_q), .clk(CLK), .clr(CLEAR));
  assign {ALU7, ALU6, ALU5, ALU4, ALU3, ALU2, ALU1, ALU0} = decoder_1_out14 ? R14_q : 8'bz;  // Controlled_Buffer controlled_buffer_25
  assign {Q7, Q6, Q5, Q4, Q3, Q2, Q1, Q0} = and_28_out ? R14_q : 8'bz;  // Controlled_Buffer controlled_buffer_26
  and and_28 (and_28_out, decoder_2_out14, EN);
  and and_29 (and_29_out, LOAD, decoder_1_out7);
  Register u_R7 (.D({D7, D6, D5, D4, D3, D2, D1, D0}), .en(and_29_out), .Q(R7_q), .clk(CLK), .clr(CLEAR));
  assign {ALU7, ALU6, ALU5, ALU4, ALU3, ALU2, ALU1, ALU0} = decoder_1_out6 ? R6_q : 8'bz;  // Controlled_Buffer controlled_buffer_27
  assign {Q7, Q6, Q5, Q4, Q3, Q2, Q1, Q0} = and_30_out ? R6_q : 8'bz;  // Controlled_Buffer controlled_buffer_28
  and and_30 (and_30_out, decoder_2_out6, EN);
  assign {ALU7, ALU6, ALU5, ALU4, ALU3, ALU2, ALU1, ALU0} = decoder_1_out15 ? R15_q : 8'bz;  // Controlled_Buffer controlled_buffer_29
  assign {Q7, Q6, Q5, Q4, Q3, Q2, Q1, Q0} = and_31_out ? R15_q : 8'bz;  // Controlled_Buffer controlled_buffer_30
  and and_31 (and_31_out, decoder_2_out15, EN);
  assign {ALU7, ALU6, ALU5, ALU4, ALU3, ALU2, ALU1, ALU0} = decoder_1_out7 ? R7_q : 8'bz;  // Controlled_Buffer controlled_buffer_31
  assign {Q7, Q6, Q5, Q4, Q3, Q2, Q1, Q0} = and_32_out ? R7_q : 8'bz;  // Controlled_Buffer controlled_buffer_32
  and and_32 (and_32_out, decoder_2_out7, EN);

  // Notes on the sheet:
  //   R1: pull=up
  //   CLEAR: pull=up
  //   LOAD: pull=up
  //   R6: pull=up
  //   R3: pull=up
  //   D6: pull=up
  //   D0: pull=up
  //   CLK: pull=up
  //   R0: pull=up
  //   EN: pull=up
  //   D2: pull=up
  //   D1: pull=up
  //   R2: pull=up
  //   R5: pull=up
  //   R4: pull=up
  //   D7: pull=up
  //   R7: pull=up
  //   D3: pull=up
  //   D4: pull=up
  //   D5: pull=up
endmodule
