// Digital circuit ALU_UNIT.dig as structural Verilog
module ALU_UNIT (
  input  D0,
  input  D1,
  input  D2,
  input  D3,
  input  D4,
  input  D5,
  input  D6,
  input  D7,
  input  LOAD_AC,
  input  CP,
  input  S0,
  input  S1,
  input  S2,
  input  S3,
  input  LOGIC,
  input  RESET,
  input  ALU_EN,
  input  RESULT_LOAD,
  input  CIN,
  output Q0,
  output Q1,
  output Q2,
  output Q3,
  output Q4,
  output Q5,
  output Q6,
  output Q7,
  output CF,
  output ZF
);

  wire _7402_1_pin1, _7402_1_pin3, _7402_1_pin4, _7402_1_pin9, _7402_1_pin10, _7402_1_pin13, _7404_1_pin1,
       _7404_1_pin4, _7404_1_pin8, _7408_1_pin3, _7408_1_pin6, _74173_1_pin4, _74173_1_pin5, _74173_1_pin6,
       _74173_1_pin9, _74173_2_pin4, _74173_2_pin5, _74173_2_pin6, _74181_1_pin1, _74181_1_pin7,
       _74181_1_pin9, _74181_1_pin10, _74181_1_pin11, _74181_2_pin1, _74181_2_pin7, _74181_2_pin9,
       _74181_2_pin10, _74181_2_pin11;

  _74181 _74181_1 (
    .pin1(_74181_1_pin1), .pin2(D0), .pin3(S3), .pin4(S2), .pin5(S1), .pin6(S0), .pin7(_74181_1_pin7),
    .pin8(LOGIC), .pin9(_74181_1_pin9), .pin10(_74181_1_pin10), .pin11(_74181_1_pin11), .pin12(1'b0));  // open: pin13, pin14, pin15, pin16, pin17, pin18, pin19, pin20, pin21, pin22, pin23, pin24
  _74173 _74173_1 (
    .pin1(1'b0), .pin2(1'b0), .pin3(_74181_1_pin1), .pin4(_74173_1_pin4), .pin5(_74173_1_pin5),
    .pin6(_74173_1_pin6), .pin7(CP), .pin8(1'b0), .pin9(_74173_1_pin9), .pin10(_74173_1_pin9), .pin11(D3),
    .pin12(D2), .pin13(D1), .pin14(D0), .pin15(RESET), .pin16(1'b1));
  _74181 _74181_2 (
    .pin1(_74181_2_pin1), .pin2(D4), .pin3(S3), .pin4(S2), .pin5(S1), .pin6(S0), .pin7(_74181_2_pin7),
    .pin8(LOGIC), .pin9(_74181_2_pin9), .pin10(_74181_2_pin10), .pin11(_74181_2_pin11), .pin12(1'b0));  // open: pin13, pin14, pin15, pin16, pin17, pin18, pin19, pin20, pin21, pin22, pin23, pin24
  _74173 _74173_2 (
    .pin1(1'b0), .pin2(1'b0), .pin3(_74181_2_pin1), .pin4(_74173_2_pin4), .pin5(_74173_2_pin5),
    .pin6(_74173_2_pin6), .pin7(CP), .pin8(1'b0), .pin9(_74173_1_pin9), .pin10(_74173_1_pin9), .pin11(D7),
    .pin12(D6), .pin13(D5), .pin14(D4), .pin15(RESET), .pin16(1'b1));
  _7402 _7402_1 (
    .pin1(_7402_1_pin1), .pin2(_74181_2_pin11), .pin3(_7402_1_pin3), .pin4(_7402_1_pin4),
    .pin5(_74181_2_pin9), .pin6(_74181_2_pin10), .pin7(1'b0), .pin8(_74181_1_pin11), .pin9(_7402_1_pin9),
    .pin10(_7402_1_pin10), .pin11(_74181_1_pin9), .pin12(_74181_1_pin10), .pin13(_7402_1_pin13), .pin14(1'b1));
  _7404 _7404_1 (
    .pin1(_7404_1_pin1), .pin2(CF), .pin3(ALU_EN), .pin4(_7404_1_pin4), .pin5(LOAD_AC), .pin6(_74173_1_pin9),
    .pin7(1'b0), .pin8(_7404_1_pin8), .pin9(RESULT_LOAD), .pin10(_74181_1_pin7), .pin11(CIN), .pin13(1'b0),
    .pin14(1'b1));  // open: pin12
  _7408 _7408_1 (
    .pin1(_7402_1_pin1), .pin2(_7402_1_pin4), .pin3(_7408_1_pin3), .pin4(_7402_1_pin13),
    .pin5(_7402_1_pin10), .pin6(_7408_1_pin6), .pin7(1'b0), .pin8(ZF), .pin9(_7408_1_pin3),
    .pin10(_7408_1_pin6), .pin12(1'b0), .pin13(1'b0), .pin14(1'b1));  // open: pin11
  _74173 _74173_3 (
    .pin1(_7404_1_pin4), .pin2(_7404_1_pin4), .pin3(Q0), .pin4(Q1), .pin5(Q2), .pin6(Q3), .pin7(CP),
    .pin8(1'b0), .pin9(_7404_1_pin8), .pin10(_7404_1_pin8), .pin11(_7402_1_pin9), .pin12(_74181_1_pin11),
    .pin13(_74181_1_pin10), .pin14(_74181_1_pin9), .pin15(RESET), .pin16(1'b1));
  _74173 _74173_4 (
    .pin1(_7404_1_pin4), .pin2(_7404_1_pin4), .pin3(Q4), .pin4(Q5), .pin5(Q6), .pin6(Q7), .pin7(CP),
    .pin8(1'b0), .pin9(_7404_1_pin8), .pin10(_7404_1_pin8), .pin11(_7402_1_pin3), .pin12(_74181_2_pin11),
    .pin13(_74181_2_pin10), .pin14(_74181_2_pin9), .pin15(RESET), .pin16(1'b1));

  // Notes on the sheet:
  //   LOAD_AC: Loads a value from the data bus into the accumulator
  //   CP: Clock pulse: value in accumulator updates on transition from low to high
endmodule
