// Digital circuit ALU_UNIT_2.dig as structural Verilog
module ALU_UNIT_2 (
  input  D0,
  input  D1,
  input  D2,
  input  D3,
  input  D4,
  input  D5,
  input  D6,
  input  D7,
  input  S0,
  input  S1,
  input  S2,
  input  ARG1_LOAD,
  input  ARG2_LOAD,
  input  CP,
  input  RESET,
  input  ALU_EN,
  output Q0,
  output Q1,
  output Q2,
  output Q3,
  output Q4,
  output Q5,
  output Q6,
  output Q7,
  output ZF,
  output CF,
  output GF,
  output LF
);

  wire _7404_1_pin2, _7404_2_pin13, _74245_1_pin5, _74245_1_pin9, ALU_CHIP_2_pin7, ALU_CHIP_2_pin9,
       ALU_CHIP_2_pin10, ALU_CHIP_2_pin11, ALU_CHIP_pin1, ALU_CHIP_pin3, ALU_CHIP_pin8, ALU_CHIP_pin9,
       ALU_CHIP_pin10, ALU_CHIP_pin11, ALU_ROM0_p9, ALU_ROM0_p10, ALU_ROM0_p11, ALU_ROM0_p20, ARG1_q0,
       ARG1_q1, ARG1_q2, ARG1_q3, ARG1_q4, ARG1_q5, ARG1_q6, ARG1_q7, ARG2_q1, ARG2_q2, ARG2_q3, ARG2_q4,
       ARG2_q5, ARG2_q6, ARG2_q7;

  _7404 _7404_1 (
    .pin1(ALU_EN), .pin2(_7404_1_pin2), .pin3(1'b0), .pin5(1'b0), .pin7(1'b0), .pin9(1'b0), .pin11(1'b0),
    .pin13(1'b0), .pin14(1'b1));  // open: pin4, pin6, pin8, pin10, pin12
  // _28c16 ALU_ROM0: pin names not known; wires that end beside it: 1'b0, 1'b0, 1'b0, 1'b0, 1'b0, S2, S1, S0, ALU_ROM0_p9, ALU_ROM0_p10, ALU_ROM0_p11, 1'b0, 1'b1, 1'b0, 1'b0, 1'b1, 1'b0, 1'b0, 1'b0, ALU_ROM0_p20, 1'b1
  _8_BIT_REGISTER ARG1 (
    .D0(D0), .D1(D1), .D2(D2), .D3(D3), .D4(D4), .D5(D5), .D6(D6), .D7(D7), .EN(1'b1), .LOAD(ARG1_LOAD),
    .CP(CP), .RESET(RESET), .Q0(ARG1_q0), .Q1(ARG1_q1), .Q2(ARG1_q2), .Q3(ARG1_q3), .Q4(ARG1_q4),
    .Q5(ARG1_q5), .Q6(ARG1_q6), .Q7(ARG1_q7));
  _74181 ALU_CHIP (
    .pin1(ALU_CHIP_pin1), .pin2(ARG1_q0), .pin3(ALU_CHIP_pin3), .pin4(ALU_ROM0_p11), .pin5(ALU_ROM0_p10),
    .pin6(ALU_ROM0_p9), .pin7(ALU_ROM0_p20), .pin8(ALU_CHIP_pin8), .pin9(ALU_CHIP_pin9),
    .pin10(ALU_CHIP_pin10), .pin11(ALU_CHIP_pin11), .pin12(1'b0));  // open: pin13, pin14, pin15, pin16, pin17, pin18, pin19, pin20, pin21, pin22, pin23, pin24
  _8_BIT_REGISTER ARG2 (
    .D0(D0), .D1(D1), .D2(D2), .D3(D3), .D4(D4), .D5(D5), .D6(D6), .D7(D7), .EN(1'b1), .LOAD(ARG2_LOAD),
    .CP(CP), .RESET(RESET), .Q0(ALU_CHIP_pin1), .Q1(ARG2_q1), .Q2(ARG2_q2), .Q3(ARG2_q3), .Q4(ARG2_q4),
    .Q5(ARG2_q5), .Q6(ARG2_q6), .Q7(ARG2_q7));
  _74181 ALU_CHIP_2 (
    .pin1(ARG2_q4), .pin2(ARG1_q4), .pin3(ALU_CHIP_pin3), .pin4(ALU_ROM0_p11), .pin5(ALU_ROM0_p10),
    .pin6(ALU_ROM0_p9), .pin7(ALU_CHIP_2_pin7), .pin8(ALU_CHIP_pin8), .pin9(ALU_CHIP_2_pin9),
    .pin10(ALU_CHIP_2_pin10), .pin11(ALU_CHIP_2_pin11), .pin12(1'b0));  // open: pin13, pin14, pin15, pin16, pin17, pin18, pin19, pin20, pin21, pin22, pin23, pin24
  CMP_LOGIC cmp_logic_1 (
    .D0_1(ARG1_q0), .D0_2(ARG1_q1), .D0_3(ARG1_q2), .D0_4(ARG1_q3), .D0_5(ARG1_q4), .D0_6(ARG1_q5),
    .D0_7(ARG1_q6), .D0_8(ARG1_q7), .D1_1(ALU_CHIP_pin1), .D1_2(ARG2_q1), .D1_3(ARG2_q2), .D1_4(ARG2_q3),
    .D1_5(ARG2_q4), .D1_6(ARG2_q5), .D1_7(ARG2_q6), .D1_8(ARG2_q7), .GT(GF), .LT(LF));
  ZF_LOGIC zf_logic_1 (
    .D0(ALU_CHIP_pin9), .D1(ALU_CHIP_pin10), .D2(ALU_CHIP_pin11), .D3(_74245_1_pin5), .D4(ALU_CHIP_2_pin9),
    .D5(ALU_CHIP_2_pin10), .D6(ALU_CHIP_2_pin11), .D7(_74245_1_pin9), .ZF(ZF));
  _74245 _74245_1 (
    .pin1(1'b1), .pin2(ALU_CHIP_pin9), .pin3(ALU_CHIP_pin10), .pin4(ALU_CHIP_pin11), .pin5(_74245_1_pin5),
    .pin6(ALU_CHIP_2_pin9), .pin7(ALU_CHIP_2_pin10), .pin8(ALU_CHIP_2_pin11), .pin9(_74245_1_pin9),
    .pin10(1'b0), .pin11(Q7), .pin12(Q6), .pin13(Q5), .pin14(Q4), .pin15(Q3), .pin16(Q2), .pin17(Q1),
    .pin18(Q0), .pin19(_7404_1_pin2), .pin20(1'b1));
  _7404 _7404_2 (
    .pin1(1'b0), .pin3(1'b0), .pin5(1'b0), .pin7(1'b0), .pin9(1'b0), .pin11(1'b0), .pin12(CF),
    .pin13(_7404_2_pin13), .pin14(1'b1));  // open: pin2, pin4, pin6, pin8, pin10

  // Notes on the sheet:
  //   contents of ALU ROM0 (hex, n*v repeats v):
  //   29,6,1b,21,16,0,2f
endmodule
