// Digital circuit CLOCK_UNIT.dig as structural Verilog
module CLOCK_UNIT (
  input  MODE,
  input  MAIN_CLK,
  input  PULSE,
  input  HALT,
  input  RESET,
  output CLK_OUT
);

  wire _7404_1_pin6, _7404_1_pin8, _7408_1_pin12, _7432_1_pin4, _7432_1_pin5, _7432_1_pin6;

  _7404 _7404_1 (
    .pin1(1'b0), .pin3(1'b0), .pin5(MODE), .pin6(_7404_1_pin6), .pin7(1'b0), .pin8(_7404_1_pin8),
    .pin9(RESET), .pin11(1'b0), .pin13(1'b0), .pin14(1'b1));  // open: pin2, pin4, pin10, pin12
  _7432 _7432_1 (
    .pin1(1'b0), .pin2(1'b0), .pin4(_7432_1_pin4), .pin5(_7432_1_pin5), .pin6(_7432_1_pin6), .pin7(1'b0),
    .pin9(1'b0), .pin10(1'b0), .pin12(1'b0), .pin13(1'b0), .pin14(1'b1));  // open: pin3, pin8, pin11
  _7408 _7408_1 (
    .pin1(MODE), .pin2(PULSE), .pin3(_7432_1_pin4), .pin4(MAIN_CLK), .pin5(_7404_1_pin6),
    .pin6(_7432_1_pin5), .pin7(1'b0), .pin9(1'b0), .pin10(1'b0), .pin11(CLK_OUT), .pin12(_7408_1_pin12),
    .pin13(_7432_1_pin6), .pin14(1'b1));  // open: pin8
  _74173 _74173_1 (
    .pin1(1'b0), .pin2(1'b0), .pin3(_7408_1_pin12), .pin7(MAIN_CLK), .pin8(1'b0), .pin9(_7404_1_pin8),
    .pin10(_7404_1_pin8), .pin11(1'b0), .pin12(1'b0), .pin13(1'b0), .pin14(RESET), .pin15(HALT), .pin16(1'b1));  // open: pin4, pin5, pin6

  // Notes on the sheet:
  //   HALT: Halt the machine
endmodule
