// Digital circuit CMP_LOGIC.dig as structural Verilog
module CMP_LOGIC (
  input  D0_1,
  input  D0_2,
  input  D0_3,
  input  D0_4,
  input  D0_5,
  input  D0_6,
  input  D0_7,
  input  D0_8,
  input  D1_1,
  input  D1_2,
  input  D1_3,
  input  D1_4,
  input  D1_5,
  input  D1_6,
  input  D1_7,
  input  D1_8,
  output GT,
  output LT
);

  wire _74682_1_pin1, _74682_1_pin19;

  _74682 _74682_1 (
    .pin1(_74682_1_pin1), .pin2(D0_1), .pin3(D1_1), .pin4(D0_2), .pin5(D1_2), .pin6(D0_3), .pin7(D1_3),
    .pin8(D0_4), .pin9(D1_4), .pin10(1'b0), .pin11(D0_5), .pin12(D1_5), .pin13(D0_6), .pin14(D1_6),
    .pin15(D0_7), .pin16(D1_7), .pin17(D0_8), .pin18(D1_8), .pin19(_74682_1_pin19), .pin20(1'b1));
  _7404 _7404_1 (
    .pin1(_74682_1_pin1), .pin2(GT), .pin3(1'b0), .pin5(1'b0), .pin7(1'b0), .pin8(1'b0), .pin9(1'b0),
    .pin11(1'b0), .pin13(1'b0), .pin14(1'b1));  // open: pin4, pin6, pin10, pin12
  _7408 _7408_1 (
    .pin1(_74682_1_pin1), .pin2(_74682_1_pin19), .pin3(LT), .pin4(1'b0), .pin5(1'b0), .pin7(1'b0),
    .pin9(1'b0), .pin10(1'b0), .pin12(1'b0), .pin13(1'b0), .pin14(1'b1));  // open: pin6, pin8, pin11
endmodule
