// Digital circuit CPU.dig as structural Verilog
module CPU (
  input  MAIN_CLK,
  input  PROGRAM_CLOCK
);

  wire alu_unit_2_1_cf, alu_unit_2_1_gf, alu_unit_2_1_lf, alu_unit_2_1_zf, and_1_out, CLK_MODE_out,
       clock_unit_1_clk_out, control_unit_1_alu_en, control_unit_1_arg1_load, control_unit_1_arg2_load,
       control_unit_1_arg_en, control_unit_1_arg_load, control_unit_1_flags_load, control_unit_1_flags_set,
       control_unit_1_halt, control_unit_1_instr_load, control_unit_1_mar_load, control_unit_1_mem_en,
       control_unit_1_mem_load, control_unit_1_out_load, control_unit_1_pc_count, control_unit_1_pc_en,
       control_unit_1_pc_load, control_unit_1_reg_en, control_unit_1_reg_load, control_unit_1_s0,
       control_unit_1_s1, control_unit_1_s2, control_unit_1_sel2_load, fetch_unit_1_ir0, fetch_unit_1_ir1,
       fetch_unit_1_ir2, fetch_unit_1_ir3, fetch_unit_1_ir4, fetch_unit_1_ir5, fetch_unit_1_ir6,
       fetch_unit_1_ir7, fetch_unit_1_s1d0, fetch_unit_1_s1d1, fetch_unit_1_s1d2, fetch_unit_1_s2d0,
       fetch_unit_1_s2d1, fetch_unit_1_s2d2, flag_unit_1_fq0, flag_unit_1_fq1, flag_unit_1_fq2,
       flag_unit_1_fq3, GOTO_PROGRAM_out, or_1_out, or_2_out, or_3_out, or_4_out, PROGRAM_out,
       program_unit_1_busy, program_unit_1_en_mem, program_unit_1_load_mar, program_unit_1_load_mem,
       program_unit_1_writing, READ_out, RESET_out, SINGLE_STEP_out, WRITE_out;
  wire [3:0] control_unit_1_step_counter, dipswitch_1_out, dipswitch_5_out, fetch_unit_1_instr_out,
       fetch_unit_1_instr_out_2, memory_unit_2_1_mar_out, memory_unit_2_1_mar_out_2, output_register_1_outp0,
       output_register_1_outp1, program_counter_1_pc_out;
  wire [7:0] program_unit_1_data_out;
  wire [7:4] program_counter_1_pc_out_2;

  DipSwitch dipswitch_1 (.out(dipswitch_1_out[0]));
  DipSwitch dipswitch_2 (.out(dipswitch_1_out[1]));
  DipSwitch dipswitch_3 (.out(dipswitch_1_out[2]));
  DipSwitch dipswitch_4 (.out(dipswitch_1_out[3]));
  DipSwitch dipswitch_5 (.out(dipswitch_5_out[0]));
  DipSwitch dipswitch_6 (.out(dipswitch_5_out[1]));
  DipSwitch dipswitch_7 (.out(dipswitch_5_out[2]));
  DipSwitch dipswitch_8 (.out(dipswitch_5_out[3]));
  Button GOTO_PROGRAM (.out(GOTO_PROGRAM_out));
  DipSwitch PROGRAM (.out(PROGRAM_out));
  Button READ (.out(READ_out));
  Button WRITE (.out(WRITE_out));
  PROGRAM_UNIT program_unit_1 (
    .PROGRAM(PROGRAM_out), .READ_PIN(READ_out), .CLOCK_IN(PROGRAM_CLOCK), .WRITE_PIN(WRITE_out),
    .RESET(RESET_out), .INSTR({dipswitch_5_out, dipswitch_1_out}), .BUSY(program_unit_1_busy),
    .WRITING(program_unit_1_writing), .EN_MEM(program_unit_1_en_mem), .LOAD_MEM(program_unit_1_load_mem),
    .LOAD_MAR(program_unit_1_load_mar), .DATA_OUT(program_unit_1_data_out));
  Seven_Seg_Hex seven_seg_hex_1 (.d(dipswitch_5_out), .dp(1'b0));
  Seven_Seg_Hex seven_seg_hex_2 (.d(dipswitch_1_out), .dp(1'b0));
  LED led_1 (.in(program_unit_1_busy));
  LED led_2 (.in(program_unit_1_writing));
  DipSwitch #(.dipDefault("true")) CLK_MODE (.out(CLK_MODE_out));
  Button SINGLE_STEP (.out(SINGLE_STEP_out));
  Button RESET (.out(RESET_out));
  Button button_1 ();  // open: out
  and and_1 (and_1_out, PROGRAM_CLOCK, PROGRAM_out);
  Seven_Seg_Hex seven_seg_hex_3 (.d(program_counter_1_pc_out_2), .dp(1'b0));
  CLOCK_UNIT clock_unit_1 (
    .MODE(CLK_MODE_out), .MAIN_CLK(MAIN_CLK), .PULSE(SINGLE_STEP_out), .HALT(control_unit_1_halt),
    .RESET(RESET_out), .CLK_OUT(clock_unit_1_clk_out));
  or or_1 (or_1_out, clock_unit_1_clk_out, and_1_out);
  or or_2 (or_2_out, control_unit_1_mem_en, program_unit_1_en_mem);
  or or_3 (or_3_out, control_unit_1_mem_load, program_unit_1_load_mem);
  or or_4 (or_4_out, program_unit_1_load_mar, control_unit_1_mar_load);
  Seven_Seg_Hex seven_seg_hex_4 (.d(program_counter_1_pc_out), .dp(1'b0));
  PROGRAM_COUNTER program_counter_1 (
    .D0(program_unit_1_data_out[0]), .D1(program_unit_1_data_out[1]), .D2(program_unit_1_data_out[2]),
    .D3(program_unit_1_data_out[3]), .D4(program_unit_1_data_out[4]), .D5(program_unit_1_data_out[5]),
    .D6(program_unit_1_data_out[6]), .D7(program_unit_1_data_out[7]), .LOAD(control_unit_1_pc_load),
    .COUNT(control_unit_1_pc_count), .EN(control_unit_1_pc_en), .CLEAR(RESET_out), .CP(or_1_out),
    .Q0(program_unit_1_data_out[0]), .Q1(program_unit_1_data_out[1]), .Q2(program_unit_1_data_out[2]),
    .Q3(program_unit_1_data_out[3]), .Q4(program_unit_1_data_out[4]), .Q5(program_unit_1_data_out[5]),
    .Q6(program_unit_1_data_out[6]), .Q7(program_unit_1_data_out[7]),
    .PC_OUT({program_counter_1_pc_out_2, program_counter_1_pc_out}));
  MEMORY_UNIT_2 memory_unit_2_1 (
    .D0(program_unit_1_data_out[0]), .D1(program_unit_1_data_out[1]), .D2(program_unit_1_data_out[2]),
    .D3(program_unit_1_data_out[3]), .D4(program_unit_1_data_out[4]), .D5(program_unit_1_data_out[5]),
    .D6(program_unit_1_data_out[6]), .D7(program_unit_1_data_out[7]), .EN_MEM(or_2_out), .LOAD_MEM(or_3_out),
    .LOAD_MAR(or_4_out), .CP(or_1_out), .RESET(RESET_out), .RESET_MAR(GOTO_PROGRAM_out),
    .Q0(program_unit_1_data_out[0]), .Q1(program_unit_1_data_out[1]), .Q2(program_unit_1_data_out[2]),
    .Q3(program_unit_1_data_out[3]), .Q4(program_unit_1_data_out[4]), .Q5(program_unit_1_data_out[5]),
    .Q6(program_unit_1_data_out[6]), .Q7(program_unit_1_data_out[7]),
    .MAR_OUT({memory_unit_2_1_mar_out_2, memory_unit_2_1_mar_out}));
  FETCH_UNIT fetch_unit_1 (
    .D0(program_unit_1_data_out[0]), .D1(program_unit_1_data_out[1]), .D2(program_unit_1_data_out[2]),
    .D3(program_unit_1_data_out[3]), .D4(program_unit_1_data_out[4]), .D5(program_unit_1_data_out[5]),
    .D6(program_unit_1_data_out[6]), .D7(program_unit_1_data_out[7]), .CP(or_1_out), .RESET(RESET_out),
    .ARG_EN(control_unit_1_arg_en), .ARG_LOAD(control_unit_1_arg_load),
    .INSTR_LOAD(control_unit_1_instr_load), .SEL2_LOAD(control_unit_1_sel2_load),
    .A0(program_unit_1_data_out[0]), .A1(program_unit_1_data_out[1]), .A2(program_unit_1_data_out[2]),
    .A3(program_unit_1_data_out[3]), .A4(program_unit_1_data_out[4]), .A5(program_unit_1_data_out[5]),
    .A6(program_unit_1_data_out[6]), .A7(program_unit_1_data_out[7]), .IR7(fetch_unit_1_ir7),
    .IR6(fetch_unit_1_ir6), .IR5(fetch_unit_1_ir5), .IR4(fetch_unit_1_ir4), .IR3(fetch_unit_1_ir3),
    .IR2(fetch_unit_1_ir2), .IR1(fetch_unit_1_ir1), .IR0(fetch_unit_1_ir0), .S1D0(fetch_unit_1_s1d0),
    .S1D1(fetch_unit_1_s1d1), .S1D2(fetch_unit_1_s1d2), .S2D0(fetch_unit_1_s2d0), .S2D1(fetch_unit_1_s2d1),
    .S2D2(fetch_unit_1_s2d2), .INSTR_OUT({fetch_unit_1_instr_out_2, fetch_unit_1_instr_out}));
  Seven_Seg_Hex seven_seg_hex_5 (.d(fetch_unit_1_instr_out_2), .dp(1'b0));
  Seven_Seg_Hex seven_seg_hex_6 (.d(memory_unit_2_1_mar_out_2), .dp(1'b0));
  Seven_Seg_Hex seven_seg_hex_7 (.d(fetch_unit_1_instr_out), .dp(1'b0));
  Seven_Seg_Hex seven_seg_hex_8 (.d(memory_unit_2_1_mar_out), .dp(1'b0));
  Seven_Seg_Hex seven_seg_hex_9 (.d(control_unit_1_step_counter), .dp(1'b0));
  CONTROL_UNIT control_unit_1 (
    .IR7(fetch_unit_1_ir7), .IR6(fetch_unit_1_ir6), .IR5(fetch_unit_1_ir5), .IR4(fetch_unit_1_ir4),
    .IR3(fetch_unit_1_ir3), .IR2(fetch_unit_1_ir2), .IR1(fetch_unit_1_ir1), .IR0(fetch_unit_1_ir0),
    .CP(or_1_out), .F0(flag_unit_1_fq0), .F1(flag_unit_1_fq1), .F2(flag_unit_1_fq2), .F3(flag_unit_1_fq3),
    .RESET(RESET_out), .DISABLE(PROGRAM_out), .PC_COUNT(control_unit_1_pc_count),
    .PC_LOAD(control_unit_1_pc_load), .PC_EN(control_unit_1_pc_en), .MAR_LOAD(control_unit_1_mar_load),
    .MEM_LOAD(control_unit_1_mem_load), .MEM_EN(control_unit_1_mem_en), .REG_LOAD(control_unit_1_reg_load),
    .REG_EN(control_unit_1_reg_en), .INSTR_LOAD(control_unit_1_instr_load),
    .ARG_LOAD(control_unit_1_arg_load), .ARG_EN(control_unit_1_arg_en), .S0(control_unit_1_s0),
    .S1(control_unit_1_s1), .S2(control_unit_1_s2), .ARG1_LOAD(control_unit_1_arg1_load),
    .ARG2_LOAD(control_unit_1_arg2_load), .ALU_EN(control_unit_1_alu_en), .HALT(control_unit_1_halt),
    .OUT_LOAD(control_unit_1_out_load), .FLAGS_LOAD(control_unit_1_flags_load),
    .FLAGS_SET(control_unit_1_flags_set), .SEL2_LOAD(control_unit_1_sel2_load),
    .STEP_COUNTER(control_unit_1_step_counter));  // open: NOOUT, NONE2
  REGISTER_UNIT register_unit_1 (
    .D0(program_unit_1_data_out[0]), .D1(program_unit_1_data_out[1]), .D2(program_unit_1_data_out[2]),
    .D3(program_unit_1_data_out[3]), .D4(program_unit_1_data_out[4]), .D5(program_unit_1_data_out[5]),
    .D6(program_unit_1_data_out[6]), .D7(program_unit_1_data_out[7]), .LOAD(control_unit_1_reg_load),
    .EN(control_unit_1_reg_en), .CP(or_1_out), .RESET(RESET_out), .S1D0(fetch_unit_1_s1d0),
    .S1D1(fetch_unit_1_s1d1), .S1D2(fetch_unit_1_s1d2), .S2D0(fetch_unit_1_s2d0), .S2D1(fetch_unit_1_s2d1),
    .S2D2(fetch_unit_1_s2d2), .Q0(program_unit_1_data_out[0]), .Q1(program_unit_1_data_out[1]),
    .Q2(program_unit_1_data_out[2]), .Q3(program_unit_1_data_out[3]), .Q4(program_unit_1_data_out[4]),
    .Q5(program_unit_1_data_out[5]), .Q6(program_unit_1_data_out[6]), .Q7(program_unit_1_data_out[7]));
  ALU_UNIT_2 alu_unit_2_1 (
    .D0(program_unit_1_data_out[0]), .D1(program_unit_1_data_out[1]), .D2(program_unit_1_data_out[2]),
    .D3(program_unit_1_data_out[3]), .D4(program_unit_1_data_out[4]), .D5(program_unit_1_data_out[5]),
    .D6(program_unit_1_data_out[6]), .D7(program_unit_1_data_out[7]), .S0(control_unit_1_s0),
    .S1(control_unit_1_s1), .S2(control_unit_1_s2), .ARG1_LOAD(control_unit_1_arg1_load),
    .ARG2_LOAD(control_unit_1_arg2_load), .CP(or_1_out), .RESET(RESET_out), .ALU_EN(control_unit_1_alu_en),
    .Q0(program_unit_1_data_out[0]), .Q1(program_unit_1_data_out[1]), .Q2(program_unit_1_data_out[2]),
    .Q3(program_unit_1_data_out[3]), .Q4(program_unit_1_data_out[4]), .Q5(program_unit_1_data_out[5]),
    .Q6(program_unit_1_data_out[6]), .Q7(program_unit_1_data_out[7]), .ZF(alu_unit_2_1_zf),
    .CF(alu_unit_2_1_cf), .GF(alu_unit_2_1_gf), .LF(alu_unit_2_1_lf));
  FLAG_UNIT flag_unit_1 (
    .F0(alu_unit_2_1_zf), .F1(alu_unit_2_1_cf), .F2(alu_unit_2_1_gf), .F3(alu_unit_2_1_lf),
    .IR5(fetch_unit_1_ir5), .IR6(fetch_unit_1_ir6), .IR7(fetch_unit_1_ir7),
    .FLAGS_LOAD(control_unit_1_flags_load), .FLAGS_SET(control_unit_1_flags_set), .CP(or_1_out),
    .RESET(RESET_out), .FQ0(flag_unit_1_fq0), .FQ1(flag_unit_1_fq1), .FQ2(flag_unit_1_fq2),
    .FQ3(flag_unit_1_fq3));
  OUTPUT_REGISTER output_register_1 (
    .D0(program_unit_1_data_out[0]), .D1(program_unit_1_data_out[1]), .D2(program_unit_1_data_out[2]),
    .D3(program_unit_1_data_out[3]), .D4(program_unit_1_data_out[4]), .D5(program_unit_1_data_out[5]),
    .D6(program_unit_1_data_out[6]), .D7(program_unit_1_data_out[7]), .LOAD_OUT(control_unit_1_out_load),
    .RESET(RESET_out), .CP(or_1_out), .OUTP0(output_register_1_outp0), .OUTP1(output_register_1_outp1));
  Seven_Seg_Hex seven_seg_hex_10 (.d(output_register_1_outp1), .dp(1'b0));
  Seven_Seg_Hex seven_seg_hex_11 (.d(output_register_1_outp0), .dp(1'b0));

  // Notes on the sheet:
  //   MAIN_CLK: Hz: 500
  //   PROGRAM_CLOCK: Hz: 20
  //   contents of R2 (hex, n*v repeats v):
  //   0,40,0,0,0,40,0,0,0,40,0,0,0,0,0,0,0,40,0,0,0,0,0,0,0,40,0,0,0,0,0,0,0,40,0,0,0,0, 0,0,0,40,
  //   8,0,0,0,0,0,0,40,0,0,0,11,0,0,0,40,0,0,40,0,11,0,0,40,0,0,0,11,0,0,0,40, 0,0,0,0,0,0,0,40,0,
  //   0,0,40,0,0,0,40,0,0,0,0,0,0,0,40,0,0,0,40,0,0,0,40,0,0,0,0,0,0, 0,40,0,0,0,40,0,0,0,40,0,0,
  //   0,0,0,0,0,40,20,0,0,40,0,0,0,40,0,0,0,0,0,0,0,40,0,0,0, 40,0,0,0,40,0,0,0,0,0,0,0,40,0,0,0,
  //   40,0,0,0,40,0,0,0,0,0,0,0,40,0,0,0,40,0,0,0,40, 0,0,0,0,0,0,0,40,0,0,0,40,0,0,0,40,0,0,0,0,
  //   0,0,0,40,0,0,0,40,0,0,0,40,0,0,0,0,0,0, 0,40,0,0,0,40,0,0,0,40,0,0,0,0,0,0,0,40,0,0,0,40,0,
  //   0,0,40,0,0,0,0,0,0,0,40,0,0,0, 40,0,0,0,40,40,0,0,0,0,0,0,40,0,0,0,0,0,0,0,40,0,0,0,0,0,0,0,
  //   40,0,0,0,0,0,0,0,40, 8,0,0,0,0,0,0,40,0,0,0,11,0,0,0,40,0,0,40,0,11,0,0,40,0,0,0,11,0,0,0,40,
  //   0,0,0,0,0, 0,0,40,0,0,0,40,0,0,0,40,0,0,0,0,0,0,0,40,0,0,0,40,0,0,0,40,0,0,0,0,0,0,0,40,0,0,
  //    0,40,0,0,0,40,0,0,0,0,0,0,0,40,20,0,0,40,0,0,0,40,0,0,0,0,0,0,0,40,0,0,0,40,0,0,0, 40,0,0,
  //   0,0,0,0,0,40,0,0,0,40,0,0,0,40,0,0,0,0,0,0,0,40,0,0,0,40,0,0,0,40,0,0,0,0, 0,0,0,40,0,0,0,40,
  //   0,0,0,40,0,0,0,0,0,0,0,40,0,0,0,40,0,0,0,40,0,0,0,0,0,0,0,40,0, 0,0,40,0,0,0,40,0,0,0,0,0,0,
  //   0,40,0,0,0,40,0,0,0,40,0,0,0,0,0,0,0,40,0,0,0,40,0,0, 0,40,40,0,0,0,0,0,0,40,0,0,0,0,0,0,0,
  //   40,0,0,0,0,0,0,0,40,0,0,0,0,0,0,0,40,8,0,0,0, 0,0,0,40,0,0,0,11,0,0,0,40,0,0,40,0,11,0,0,40,
  //   0,0,0,11,0,0,0,40,0,90,1,0,0,0,0,40, 0,0,0,40,0,0,0,40,0,0,0,0,0,0,0,40,0,0,0,40,0,0,0,40,0,
  //   0,0,0,0,0,0,40,0,0,0,40,0, 0,0,40,0,0,0,0,0,0,0,40,20,0,0,40,0,0,0,40,0,0,0,0,0,0,0,40,0,0,
  //   0,40,0,0,0,40,0,0, 0,0,0,0,0,40,0,0,0,40,0,0,0,40,0,0,0,0,0,0,0,40,0,0,0,40,0,0,0,40,0,0,0,
  //   0,0,0,0,40, 0,0,0,40,0,0,0,40,0,0,0,0,0,0,0,40,0,0,0,40,0,0,0,40,0,0,0,0,0,0,0,40,0,0,0,40,
  //   0, 0,0,40,0,0,0,0,0,0,0,40,0,0,0,40,0,0,0,40,0,0,0,0,0,0,0,40,0,0,0,40,0,0,0,40,40,0, 0,0,0,
  //   0,0,40,0,0,0,0,0,0,0,40,0,0,0,0,0,0,0,40,0,0,0,0,0,0,0,40,8,0,0,0,0,0,0,40, 0,0,0,11,0,0,0,
  //   40,0,0,40,0,11,0,0,40,0,0,0,11,0,0,0,40,0,0,0,0,0,0,0,40,0,0,0,40, 0,0,0,40,0,0,0,0,0,0,0,40,
  //   0,0,0,40,0,0,0,40,0,0,0,0,0,0,0,40,0,0,0,40,0,0,0,40,0, 0,0,0,0,0,0,40,20,0,0,40,0,0,0,40,0,
  //   0,0,0,0,0,0,40,0,0,0,40,0,0,0,40,0,0,0,0,0,0, 0,40,0,0,0,40,0,0,0,40,0,0,0,0,0,0,0,40,0,0,0,
  //   40,0,0,0,40,0,0,0,0,0,0,0,40,0,0,0, 40,0,0,0,40,0,0,0,0,0,0,0,40,0,0,0,40,0,0,0,40,0,0,0,0,
  //   0,0,0,40,0,0,0,40,0,0,0,40, 0,0,0,0,0,0,0,40,0,0,0,40,0,0,0,40,0,0,0,0,0,0,0,40,0,0,0,40,0,
  //   0,0,40,40,0,0,0,0, 0,0,40,0,0,0,0,0,0,0,40,0,0,0,0,0,0,0,40,0,0,0,0,0,0,0,40,8,0,0,0,0,0,0,
  //   40,0,0,0, 11,0,0,0,40,0,0,40,0,11,0,0,40,0,0,0,40,0,0,0,40,0,0,0,0,0,0,0,40,0,0,0,40,0,0,0,
  //    40,0,0,0,0,0,0,0,40,0,4,0,0,0,0,0,40,0,0,0,0,0,0,0,40,0,0,0,40,0,0,0,40,0,0,0,0,0, 0,0,40,
  //   20,0,0,0,0,0,0,40,0,0,0,0,0,0,0,40,0,0,0,40,0,0,0,40,0,0,0,0,0,0,0,40,0,0, 0,40,0,0,0,40,0,
  //   0,0,0,0,0,0,40,0,0,0,40,0,0,0,40,0,0,0,0,0,0,0,40,0,0,0,40,0,0,0, 40,0,0,0,0,0,0,0,40,0,0,0,
  //   40,0,0,0,40,0,0,0,0,0,0,0,40,0,0,0,40,0,0,0,40,0,0,0,0, 0,0,0,40,0,0,0,40,0,0,0,40,0,0,0,0,
  //   0,0,0,40,0,0,0,40,0,0,0,40,40,0,0,0,0,0,0,40,0, 0,0,0,0,0,0,40,0,0,0,0,0,0,0,40,0,0,0,0,0,0,
  //   0,40,8,0,0,0,0,0,0,40,0,0,0,11,0,0,0, 40,0,0,40,0,11,0,0,40,0,0,0,40,0,0,0,40,0,0,0,0,0,0,0,
  //   40,0,0,0,40,0,0,0,40,0,0,0, 0,0,0,0,40,0,4,0,0,0,0,0,40,0,0,0,0,0,0,0,40,0,0,0,40,0,0,0,40,
  //   0,0,0,0,0,0,0,40,20, 0,0,0,0,0,0,40,0,0,0,0,0,0,0,40,0,0,0,40,0,0,0,40,0,0,0,0,0,0,0,40,0,0,
  //   0,40,0,0,0, 40,0,0,0,0,0,0,0,40,0,0,0,40,0,0,0,40,0,0,0,0,0,0,0,40,0,0,0,40,0,0,0,40,0,0,0,
  //   0, 0,0,0,40,0,0,0,40,0,0,0,40,0,0,0,0,0,0,0,40,0,0,0,40,0,0,0,40,0,0,0,0,0,0,0,40,0, 0,0,40,
  //   0,0,0,40,0,0,0,0,0,0,0,40,0,0,0,40,0,0,0,40,40,0,0,0,0,0,0,40,0,0,0,0,0,0, 0,40,0,0,0,0,0,0,
  //   0,40,0,0,0,0,0,0,0,40,8,0,0,0,0,0,0,40,0,0,0,11,0,0,0,40,0,0,40, 0,11,0,0,40,0,0,0,40,0,0,0,
  //   40,0,0,0,0,0,0,0,40,0,0,0,40,0,0,0,40,0,0,0,0,0,0,0,40, 0,4,0,0,0,0,0,40,0,0,0,0,0,0,0,40,0,
  //   0,0,40,0,0,0,40,0,0,0,0,0,0,0,40,20,0,0,0,0,0, 0,40,0,0,0,0,0,0,0,40,0,0,0,40,0,0,0,40,0,0,
  //   0,0,0,0,0,40,0,0,0,40,0,0,0,40,0,0,0, 0,0,0,0,40,0,0,0,40,0,0,0,40,0,0,0,0,0,0,0,40,0,0,0,40,
  //   0,0,0,40,0,0,0,0,0,0,0,40, 0,0,0,40,0,0,0,40,0,0,0,0,0,0,0,40,0,0,0,40,0,0,0,40,0,0,0,0,0,0,
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  //   contents of PROGRAM ROM (hex, n*v repeats v):
  //   10,4,2,20,0,0,0,8,0,0,0,0,0,0,0,0,0,0,0,0,0,0,0,0,0,0,0,0,0,0,0,8
  //   contents of ALU ROM0 (hex, n*v repeats v):
  //   29,6
  //   contents of R0 (hex, n*v repeats v):
  //   c,21,0,0,c,21,0,0,c,21,61,0,0,0,0,0,c,21,c,61,0,0,0,0,c,21,c,61,0,0,0,0,c,21,c,28, 0,0,0,0,
  //   c,21,80,0,0,0,0,0,c,21,c,21,80,40,0,0,c,21,c,80,21,80,40,0,c,21,c,21,80,40, 0,0,c,21,0,0,0,
  //   0,0,0,c,21,0,0,c,21,0,0,c,21,0,0,0,0,0,0,c,21,c,22,0,0,0,0,c,21,0, 0,0,0,0,0,c,21,0,0,c,21,
  //   0,0,c,21,0,0,0,0,0,0,c,21,0,0,c,21,0,0,c,21,0,0,0,0,0,0,c, 21,0,0,c,21,0,0,c,21,0,0,0,0,0,0,
  //   c,21,0,0,c,21,0,0,c,21,0,0,0,0,0,0,c,21,0,0,c,21, 0,0,c,21,0,0,0,0,0,0,c,21,0,0,cc,21,0,0,c,
  //   21,0,0,0,0,0,0,c,21,0,0,c,21,0,0,c,21,0, 0,0,0,0,0,c,21,0,0,c,21,0,0,c,21,0,0,0,0,0,0,c,21,
  //   0,0,c,21,0,0,c,21,0,0,0,0,0,0,c, 21,0,0,c,21,0,0,c,21,20,c1,0,0,0,0,c,21,c,28,61,0,0,0,c,21,
  //   c,61,0,0,0,0,c,21,c,28, 91,0,0,0,c,21,80,0,0,0,0,0,c,21,c,21,80,40,0,0,c,21,c,80,21,80,40,0,
  //   c,21,c,21,80, 40,0,0,c,21,0,0,0,0,0,0,c,21,0,0,c,21,0,0,c,21,0,0,0,0,0,0,c,21,0,0,0,0,0,0,c,
  //   21, 0,0,0,0,0,0,c,21,0,0,c,21,0,0,c,21,0,0,0,0,0,0,c,21,0,0,c,21,0,0,c,21,0,0,0,0,0,0, c,21,
  //   0,0,c,21,0,0,c,21,0,0,0,0,0,0,c,21,0,0,c,21,0,0,c,21,0,0,0,0,0,0,c,21,0,0,c, 21,0,0,c,21,0,
  //   0,0,0,0,0,c,21,0,0,c,21,0,0,c,21,0,0,0,0,0,0,c,21,0,0,c,21,0,0,c,21, 0,0,0,0,0,0,c,21,0,0,c,
  //   21,0,0,c,21,0,0,0,0,0,0,c,21,0,0,c,21,0,0,c,21,0,0,0,0,0,0, c,21,0,0,c,21,0,0,c,21,20,c1,0,
  //   0,0,0,c,21,c,28,61,0,0,0,c,21,c,61,0,0,0,0,c,21,c, 28,91,0,0,0,c,21,80,0,0,0,0,0,c,21,c,21,
  //   80,40,0,0,c,21,c,80,21,80,40,0,c,21,c,21, 80,40,0,0,c,21,0,0,0,0,0,0,c,21,0,0,c,21,0,0,c,21,
  //   0,0,0,0,0,0,c,21,0,0,0,0,0,0,c, 21,0,0,0,0,0,0,c,21,0,0,c,21,0,0,c,21,0,0,0,0,0,0,c,21,0,0,
  //   c,21,0,0,c,21,0,0,0,0, 0,0,c,21,0,0,c,21,0,0,c,21,0,0,0,0,0,0,c,21,0,0,c,21,0,0,c,21,0,0,0,
  //   0,0,0,c,21,0, 0,c,21,0,0,c,21,0,0,0,0,0,0,c,21,0,0,c,21,0,0,c,21,0,0,0,0,0,0,c,21,0,0,c,21,
  //   0,0, c,21,0,0,0,0,0,0,c,21,0,0,c,21,0,0,c,21,0,0,0,0,0,0,c,21,0,0,c,21,0,0,c,21,0,0,0, 0,0,
  //   0,c,21,0,0,c,21,0,0,c,21,20,c1,0,0,0,0,c,21,c,28,61,0,0,0,c,21,c,61,0,0,0,0,c, 21,c,28,91,0,
  //   0,0,c,21,80,0,0,0,0,0,c,21,c,21,80,40,0,0,c,21,c,80,21,80,40,0,c,21, c,21,80,40,0,0,c,21,0,
  //   0,0,0,0,0,c,21,0,0,c,21,0,0,c,21,0,0,0,0,0,0,c,21,0,0,0,0,0, 0,c,21,0,0,0,0,0,0,c,21,0,0,c,
  //   21,0,0,c,21,0,0,0,0,0,0,c,21,0,0,c,21,0,0,c,21,0,0, 0,0,0,0,c,21,0,0,c,21,0,0,c,21,0,0,0,0,
  //   0,0,c,21,0,0,c,21,0,0,c,21,0,0,0,0,0,0,c,21, 0,0,c,21,0,0,c,21,0,0,0,0,0,0,c,21,0,0,c,21,0,
  //   0,c,21,0,0,0,0,0,0,c,21,0,0,c,21,0, 0,c,21,0,0,0,0,0,0,c,21,0,0,c,21,0,0,c,21,0,0,0,0,0,0,c,
  //   21,0,0,c,21,0,0,c,21,0,0, 0,0,0,0,c,21,0,0,c,21,0,0,c,21,20,c1,0,0,0,0,c,21,c,28,61,0,0,0,c,
  //   21,c,61,0,0,0,0, c,21,c,28,91,0,0,0,c,21,80,0,0,0,0,0,c,21,c,21,80,40,0,0,c,21,c,80,21,80,40,
  //   0,c,21, 0,0,c,21,0,0,c,21,0,0,0,0,0,0,c,21,0,0,c,21,0,0,c,21,0,0,0,0,0,0,c,21,c,20,0,0,0, 0,
  //   c,21,0,0,0,0,0,0,c,21,0,0,c,21,0,0,c,21,0,0,0,0,0,0,c,21,0,0,0,0,0,0,c,21,0,0,0, 0,0,0,c,21,
  //   0,0,c,21,0,0,c,21,0,0,0,0,0,0,c,21,0,0,c,21,0,0,c,21,0,0,0,0,0,0,c,21, 0,0,c,21,0,0,c,21,0,
  //   0,0,0,0,0,c,21,0,0,c,21,0,0,c,21,0,0,0,0,0,0,c,21,0,0,c,21,0, 0,c,21,0,0,0,0,0,0,c,21,0,0,c,
  //   21,0,0,c,21,0,0,0,0,0,0,c,21,0,0,c,21,0,0,c,21,0,0, 0,0,0,0,c,21,0,0,c,21,0,0,c,21,20,c1,0,
  //   0,0,0,c,21,c,28,61,0,0,0,c,21,c,61,0,0,0,0, c,21,c,28,91,0,0,0,c,21,80,0,0,0,0,0,c,21,c,21,
  //   80,40,0,0,c,21,c,80,21,80,40,0,c,21, 0,0,c,21,0,0,c,21,0,0,0,0,0,0,c,21,0,0,c,21,0,0,c,21,0,
  //   0,0,0,0,0,c,21,c,20,0,0,0, 0,c,21,0,0,0,0,0,0,c,21,0,0,c,21,0,0,c,21,0,0,0,0,0,0,c,21,0,0,0,
  //   0,0,0,c,21,0,0,0, 0,0,0,c,21,0,0,c,21,0,0,c,21,0,0,0,0,0,0,c,21,0,0,c,21,0,0,c,21,0,0,0,0,0,
  //   0,c,21, 0,0,c,21,0,0,c,21,0,0,0,0,0,0,c,21,0,0,c,21,0,0,c,21,0,0,0,0,0,0,c,21,0,0,c,21,0, 0,
  //   c,21,0,0,0,0,0,0,c,21,0,0,c,21,0,0,c,21,0,0,0,0,0,0,c,21,0,0,c,21,0,0,c,21,0,0, 0,0,0,0,c,21,
  //   0,0,c,21,0,0,c,21,20,c1,0,0,0,0,c,21,c,28,61,0,0,0,c,21,c,61,0,0,0,0, c,21,c,28,91,0,0,0,c,
  //   21,80,0,0,0,0,0,c,21,c,21,80,40,0,0,c,21,c,80,21,80,40,0,c,21, 0,0,c,21,0,0,c,21,0,0,0,0,0,
  //   0,c,21,0,0,c,21,0,0,c,21,0,0,0,0,0,0,c,21,c,20,0,0,0, 0,c,21,0,0,0,0,0,0,c,21,0,0,c,21,0,0,
  //   c,21,0,0,0,0,0,0,c,21,0,0,0,0,0,0,c,21,0,0,0, 0,0,0,c,21,0,0,c,21,0,0,c,21,0,0,0,0,0,0,c,21,
  //   0,0,c,21,0,0,c,21,0,0,0,0,0,0,c,21, 0,0,c,21,0,0,c,21,0,0,0,0,0,0,c,21,0,0,c,21,0,0,c,21,0,
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  //   contents of R1 (hex, n*v repeats v):
  //   0,1,0,0,0,1,0,0,0,1,0,0,0,0,0,0,0,1,0,0,0,0,0,0,0,1,0,0,0,48,0,0,0,1,0,0,0,0,0,0, 0,1,0,0,0,
  //   0,0,0,0,1,0,80,40,0,0,0,0,1,0,40,0,80,0,0,0,1,0,80,40,8,0,0,0,1,0,0,0,0, 0,0,0,1,0,0,0,1,0,
  //   0,0,1,0,0,0,0,0,0,0,1,0,0,0,1,0,0,0,1,0,0,0,0,0,0,0,1,0,0,0,1,0, 0,0,1,0,0,0,0,0,0,0,1,0,0,
  //   0,1,0,0,0,1,0,0,0,0,0,0,0,1,0,0,0,1,0,0,0,1,0,0,0,0,0,0, 0,1,0,0,0,1,0,0,0,1,0,0,0,0,0,0,0,
  //   1,0,0,0,1,0,0,0,1,0,0,0,0,0,0,0,1,0,0,0,1,0,0,0, 1,0,0,0,0,0,0,0,1,0,0,0,1,0,0,0,1,0,0,0,0,
  //   0,0,0,1,0,0,0,1,0,0,0,1,0,0,0,0,0,0,0,1, 0,0,0,1,0,0,0,1,0,0,0,0,0,0,0,1,0,0,0,1,0,0,0,1,0,
  //   0,0,0,0,0,0,1,0,0,0,0,0,0,0,1,0, 0,0,48,0,0,0,1,0,0,0,0,0,0,0,1,0,0,0,0,0,0,0,1,0,80,40,0,0,
  //   0,0,1,0,40,0,80,0,0,0, 1,0,80,40,8,0,0,0,1,0,0,0,0,0,0,0,1,0,0,0,1,0,0,0,1,0,0,0,0,0,0,0,1,
  //   0,0,0,1,0,0,0, 1,0,0,0,0,0,0,0,1,0,0,0,1,0,0,0,1,0,0,0,0,0,0,0,1,0,0,0,1,0,0,0,1,0,0,0,0,0,
  //   0,0,1, 0,0,0,1,0,0,0,1,0,0,0,0,0,0,0,1,0,0,0,1,0,0,0,1,0,0,0,0,0,0,0,1,0,0,0,1,0,0,0,1,0, 0,
  //   0,0,0,0,0,1,0,0,0,1,0,0,0,1,0,0,0,0,0,0,0,1,0,0,0,1,0,0,0,1,0,0,0,0,0,0,0,1,0,0, 0,1,0,0,0,
  //   1,0,0,0,0,0,0,0,1,0,0,0,1,0,0,0,1,0,0,0,0,0,0,0,1,0,0,0,1,0,0,0,1,0,0,0, 0,0,0,0,1,0,0,0,0,
  //   0,0,0,1,0,0,0,48,0,0,0,1,0,0,0,0,0,0,0,1,0,0,0,0,0,0,0,1,0,80,40, 0,0,0,0,1,0,40,0,80,0,0,0,
  //   1,0,80,40,8,0,0,0,1,0,0,0,0,0,0,0,1,0,0,0,1,0,0,0,1,0,0, 0,0,0,0,0,1,0,0,0,1,0,0,0,1,0,0,0,
  //   0,0,0,0,1,0,0,0,1,0,0,0,1,0,0,0,0,0,0,0,1,0,0,0, 1,0,0,0,1,0,0,0,0,0,0,0,1,0,0,0,1,0,0,0,1,
  //   0,0,0,0,0,0,0,1,0,0,0,1,0,0,0,1,0,0,0,0, 0,0,0,1,0,0,0,1,0,0,0,1,0,0,0,0,0,0,0,1,0,0,0,1,0,
  //   0,0,1,0,0,0,0,0,0,0,1,0,0,0,1,0, 0,0,1,0,0,0,0,0,0,0,1,0,0,0,1,0,0,0,1,0,0,0,0,0,0,0,1,0,0,
  //   0,1,0,0,0,1,0,0,0,0,0,0, 0,1,0,0,0,1,0,0,0,1,0,0,0,0,0,0,0,1,0,0,0,0,0,0,0,1,0,0,0,48,0,0,0,
  //   1,0,0,0,0,0,0, 0,1,0,0,0,0,0,0,0,1,0,80,40,0,0,0,0,1,0,40,0,80,0,0,0,1,0,80,40,8,0,0,0,1,0,
  //   0,0,0, 0,0,0,1,0,0,0,1,0,0,0,1,0,0,0,0,0,0,0,1,0,0,0,1,0,0,0,1,0,0,0,0,0,0,0,1,0,0,0,1,0, 0,
  //   0,1,0,0,0,0,0,0,0,1,0,0,0,1,0,0,0,1,0,0,0,0,0,0,0,1,0,0,0,1,0,0,0,1,0,0,0,0,0,0, 0,1,0,0,0,
  //   1,0,0,0,1,0,0,0,0,0,0,0,1,0,0,0,1,0,0,0,1,0,0,0,0,0,0,0,1,0,0,0,1,0,0,0, 1,0,0,0,0,0,0,0,1,
  //   0,0,0,1,0,0,0,1,0,0,0,0,0,0,0,1,0,0,0,1,0,0,0,1,0,0,0,0,0,0,0,1, 0,0,0,1,0,0,0,1,0,0,0,0,0,
  //   0,0,1,0,0,0,1,0,0,0,1,0,0,0,0,0,0,0,1,0,0,0,0,0,0,0,1,0, 0,0,48,0,0,0,1,0,0,0,0,0,0,0,1,0,0,
  //   0,0,0,0,0,1,0,80,40,0,0,0,0,1,0,40,0,80,0,0,0, 1,0,0,0,1,0,0,0,1,0,0,0,0,0,0,0,1,0,0,0,1,0,
  //   0,0,1,0,0,0,0,0,0,0,1,0,0,0,1,0,0,0,1, 0,0,0,0,0,0,0,1,0,0,0,1,0,0,0,1,0,0,0,0,0,0,0,1,0,0,
  //   0,1,0,0,0,1,0,0,0,0,0,0,0,1,0, 0,0,1,0,0,0,1,0,0,0,0,0,0,0,1,0,0,0,1,0,0,0,1,0,0,0,0,0,0,0,
  //   1,0,0,0,1,0,0,0,1,0,0, 0,0,0,0,0,1,0,0,0,1,0,0,0,1,0,0,0,0,0,0,0,1,0,0,0,1,0,0,0,1,0,0,0,0,
  //   0,0,0,1,0,0,0, 1,0,0,0,1,0,0,0,0,0,0,0,1,0,0,0,1,0,0,0,1,0,0,0,0,0,0,0,1,0,0,0,1,0,0,0,1,0,
  //   0,0,0, 0,0,0,1,0,0,0,0,0,0,0,1,0,0,0,48,0,0,0,1,0,0,0,0,0,0,0,1,0,0,0,0,0,0,0,1,0,80,40, 0,
  //   0,0,0,1,0,40,0,80,0,0,0,1,0,0,0,1,0,0,0,1,0,0,0,0,0,0,0,1,0,0,0,1,0,0,0,1,0,0,0, 0,0,0,0,1,
  //   0,0,0,1,0,0,0,1,0,0,0,0,0,0,0,1,0,0,0,1,0,0,0,1,0,0,0,0,0,0,0,1,0,0,0,1, 0,0,0,1,0,0,0,0,0,
  //   0,0,1,0,0,0,1,0,0,0,1,0,0,0,0,0,0,0,1,0,0,0,1,0,0,0,1,0,0,0,0,0, 0,0,1,0,0,0,1,0,0,0,1,0,0,
  //   0,0,0,0,0,1,0,0,0,1,0,0,0,1,0,0,0,0,0,0,0,1,0,0,0,1,0,0, 0,1,0,0,0,0,0,0,0,1,0,0,0,1,0,0,0,
  //   1,0,0,0,0,0,0,0,1,0,0,0,1,0,0,0,1,0,0,0,0,0,0,0, 1,0,0,0,1,0,0,0,1,0,0,0,0,0,0,0,1,0,0,0,0,
  //   0,0,0,1,0,0,0,48,0,0,0,1,0,0,0,0,0,0,0, 1,0,0,0,0,0,0,0,1,0,80,40,0,0,0,0,1,0,40,0,80,0,0,0,
  //   1,0,0,0,1,0,0,0,1,0,0,0,0,0,0, 0,1,0,0,0,1,0,0,0,1,0,0,0,0,0,0,0,1,0,0,0,1,0,0,0,1,0,0,0,0,
  //   0,0,0,1,0,0,0,1,0,0,0, 1,0,0,0,0,0,0,0,1,0,0,0,1,0,0,0,1,0,0,0,0,0,0,0,1,0,0,0,1,0,0,0,1,0,
  //   0,0,0,0,0,0,1, 0,0,0,1,0,0,0,1,0,0,0,0,0,0,0,1,0,0,0,1,0,0,0,1,0,0,0,0,0,0,0,1,0,0,0,1,0,0,
  //   0,1,0, 0,0,0,0,0,0,1,0,0,0,1,0,0,0,1,0,0,0,0,0,0,0,1,0,0,0,1,0,0,0,1,0,0,0,0,0,0,0,1,0,0, 0,
  //   1,0,0,0,1,0,0,0,0,0,0,0,1,0,0,0,1,0,0,0,1,0,0,0,0,0,0,0,1,0,0,0,0,0,0,0,1,0,0,0, 48,0,0,0,1,
  //   0,0,0,0,0,0,0,1,0,0,0,0,0,0,0,1,0,80,40,0,0,0,0,1,0,40,0,80,0,0,0,1,0, 0,0,1,0,0,0,1,0,0,0,
  //   0,0,0,0,1,0,0,0,1,0,0,0,1,0,0,0,0,0,0,0,1,0,0,0,1,0,0,0,1,0,0, 0,0,0,0,0,1,0,0,0,1,0,0,0,1,
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endmodule
