// Digital circuit FETCH_UNIT.dig as structural Verilog
module FETCH_UNIT (
  input  D0,
  input  D1,
  input  D2,
  input  D3,
  input  D4,
  input  D5,
  input  D6,
  input  D7,
  input  CP,
  input  RESET,
  input  ARG_EN,
  input  ARG_LOAD,
  input  INSTR_LOAD,
  input  SEL2_LOAD,
  output A0,
  output A1,
  output A2,
  output A3,
  output A4,
  output A5,
  output A6,
  output A7,
  output IR7,
  output IR6,
  output IR5,
  output IR4,
  output IR3,
  output IR2,
  output IR1,
  output IR0,
  output S1D0,
  output S1D1,
  output S1D2,
  output S2D0,
  output S2D1,
  output S2D2,
  output [7:0] INSTR_OUT
);

  wire _7404_1_pin4, _7404_1_pin10, _7404_1_pin12, _74173_1_pin9;

  _74173 _74173_1 (
    .pin1(1'b0), .pin2(1'b0), .pin3(INSTR_OUT[0]), .pin4(INSTR_OUT[1]), .pin5(INSTR_OUT[2]),
    .pin6(INSTR_OUT[3]), .pin7(CP), .pin8(1'b0), .pin9(_74173_1_pin9), .pin10(_74173_1_pin9), .pin11(D3),
    .pin12(D2), .pin13(D1), .pin14(D0), .pin15(RESET), .pin16(1'b1));
  _74173 _74173_2 (
    .pin1(1'b0), .pin2(1'b0), .pin3(INSTR_OUT[4]), .pin4(INSTR_OUT[5]), .pin5(INSTR_OUT[6]),
    .pin6(INSTR_OUT[7]), .pin7(CP), .pin8(1'b0), .pin9(_74173_1_pin9), .pin10(_74173_1_pin9), .pin11(D7),
    .pin12(D6), .pin13(D5), .pin14(D4), .pin15(RESET), .pin16(1'b1));
  _7404 _7404_1 (
    .pin1(INSTR_LOAD), .pin2(_74173_1_pin9), .pin3(SEL2_LOAD), .pin4(_7404_1_pin4), .pin5(1'b0), .pin7(1'b0),
    .pin9(1'b0), .pin10(_7404_1_pin10), .pin11(ARG_LOAD), .pin12(_7404_1_pin12), .pin13(ARG_EN), .pin14(1'b1));  // open: pin6, pin8
  _74173 _74173_3 (
    .pin1(_7404_1_pin12), .pin2(_7404_1_pin12), .pin3(A0), .pin4(A1), .pin5(A2), .pin6(A3), .pin7(CP),
    .pin8(1'b0), .pin9(_7404_1_pin10), .pin10(_7404_1_pin10), .pin11(D3), .pin12(D2), .pin13(D1), .pin14(D0),
    .pin15(RESET), .pin16(1'b1));
  _74173 _74173_4 (
    .pin1(_7404_1_pin12), .pin2(_7404_1_pin12), .pin3(A4), .pin4(A5), .pin5(A6), .pin6(A7), .pin7(CP),
    .pin8(1'b0), .pin9(_7404_1_pin10), .pin10(_7404_1_pin10), .pin11(D7), .pin12(D6), .pin13(D5), .pin14(D4),
    .pin15(RESET), .pin16(1'b1));
  _74173 S2 (
    .pin1(1'b0), .pin2(1'b0), .pin3(S2D0), .pin4(S2D1), .pin5(S2D2), .pin7(CP), .pin8(1'b0),
    .pin9(_7404_1_pin4), .pin10(_7404_1_pin4), .pin11(1'b0), .pin12(D7), .pin13(D6), .pin14(D5),
    .pin15(RESET), .pin16(1'b1));  // open: pin6

  assign IR0 = INSTR_OUT[0];
  assign IR1 = INSTR_OUT[1];
  assign IR2 = INSTR_OUT[2];
  assign IR3 = INSTR_OUT[3];
  assign IR4 = INSTR_OUT[4];
  assign IR5 = INSTR_OUT[5];
  assign IR6 = INSTR_OUT[6];
  assign IR7 = INSTR_OUT[7];
  assign S1D0 = INSTR_OUT[5];
  assign S1D1 = INSTR_OUT[6];
  assign S1D2 = INSTR_OUT[7];
endmodule
