// Digital circuit FLAG_UNIT.dig as structural Verilog
module FLAG_UNIT (
  input  F0,
  input  F1,
  input  F2,
  input  F3,
  input  IR5,
  input  IR6,
  input  IR7,
  input  FLAGS_LOAD,
  input  FLAGS_SET,
  input  CP,
  input  RESET,
  output FQ0,
  output FQ1,
  output FQ2,
  output FQ3
);

  wire _7404_1_pin2, _7404_1_pin10, _7404_2_pin4, _7404_2_pin6, _7404_2_pin8, _7404_2_pin10, _7404_2_pin12,
       _7408_1_pin3, _7408_1_pin6, _7408_1_pin8, _7408_1_pin11, _7408_2_pin3, _7432_1_pin3, _7432_1_pin6,
       _7432_1_pin8, _7432_1_pin11, _74139_1_pin4, _74139_1_pin5, _74139_1_pin6, _74139_1_pin7,
       _74139_1_pin9, _74139_1_pin10, _74139_1_pin11, _74139_1_pin12, _74139_1_pin15, _74245_1_pin15,
       _74245_1_pin16, _74245_1_pin17, _74245_1_pin18, _74245_3_pin15, _74245_3_pin16, _74245_3_pin17,
       _74245_3_pin18;

  _7404 _7404_1 (
    .pin1(FLAGS_LOAD), .pin2(_7404_1_pin2), .pin3(1'b0), .pin5(1'b0), .pin7(1'b0), .pin9(1'b0),
    .pin10(_7404_1_pin10), .pin11(FLAGS_SET), .pin13(1'b0), .pin14(1'b1));  // open: pin4, pin6, pin8, pin12
  _74139 _74139_1 (
    .pin1(IR7), .pin2(IR5), .pin3(IR6), .pin4(_74139_1_pin4), .pin5(_74139_1_pin5), .pin6(_74139_1_pin6),
    .pin7(_74139_1_pin7), .pin8(1'b0), .pin9(_74139_1_pin9), .pin10(_74139_1_pin10), .pin11(_74139_1_pin11),
    .pin12(_74139_1_pin12), .pin13(IR6), .pin14(IR5), .pin15(_74139_1_pin15), .pin16(1'b1));
  _7404 _7404_2 (
    .pin1(IR7), .pin2(_74139_1_pin15), .pin3(FLAGS_SET), .pin4(_7404_2_pin4), .pin5(_74139_1_pin12),
    .pin6(_7404_2_pin6), .pin7(1'b0), .pin8(_7404_2_pin8), .pin9(_74139_1_pin11), .pin10(_7404_2_pin10),
    .pin11(_74139_1_pin10), .pin12(_7404_2_pin12), .pin13(_74139_1_pin9), .pin14(1'b1));
  _7408 _7408_1 (
    .pin1(_74139_1_pin4), .pin2(FQ0), .pin3(_7408_1_pin3), .pin4(_74139_1_pin5), .pin5(FQ1),
    .pin6(_7408_1_pin6), .pin7(1'b0), .pin8(_7408_1_pin8), .pin9(_74139_1_pin6), .pin10(FQ2),
    .pin11(_7408_1_pin11), .pin12(_74139_1_pin7), .pin13(FQ3), .pin14(1'b1));
  _7432 _7432_1 (
    .pin1(_7404_2_pin6), .pin2(FQ0), .pin3(_7432_1_pin3), .pin4(_7404_2_pin8), .pin5(FQ1),
    .pin6(_7432_1_pin6), .pin7(1'b0), .pin8(_7432_1_pin8), .pin9(_7404_2_pin10), .pin10(FQ2),
    .pin11(_7432_1_pin11), .pin12(_7404_2_pin12), .pin13(FQ3), .pin14(1'b1));
  _74245 _74245_1 (
    .pin1(1'b1), .pin2(_7408_1_pin3), .pin3(_7408_1_pin6), .pin4(_7408_1_pin8), .pin5(_7408_1_pin11),
    .pin10(1'b0), .pin15(_74245_1_pin15), .pin16(_74245_1_pin16), .pin17(_74245_1_pin17),
    .pin18(_74245_1_pin18), .pin19(IR7), .pin20(1'b1));  // open: pin6, pin7, pin8, pin9, pin11, pin12, pin13, pin14
  _74245 _74245_2 (
    .pin1(1'b1), .pin2(_7432_1_pin3), .pin3(_7432_1_pin6), .pin4(_7432_1_pin8), .pin5(_7432_1_pin11),
    .pin10(1'b0), .pin15(_74245_1_pin15), .pin16(_74245_1_pin16), .pin17(_74245_1_pin17),
    .pin18(_74245_1_pin18), .pin19(_74139_1_pin15), .pin20(1'b1));  // open: pin6, pin7, pin8, pin9, pin11, pin12, pin13, pin14
  _74245 _74245_3 (
    .pin1(1'b1), .pin2(_74245_1_pin18), .pin3(_74245_1_pin17), .pin4(_74245_1_pin16), .pin5(_74245_1_pin15),
    .pin10(1'b0), .pin15(_74245_3_pin15), .pin16(_74245_3_pin16), .pin17(_74245_3_pin17),
    .pin18(_74245_3_pin18), .pin19(_7404_2_pin4), .pin20(1'b1));  // open: pin6, pin7, pin8, pin9, pin11, pin12, pin13, pin14
  _74245 _74245_4 (
    .pin1(1'b1), .pin2(F0), .pin3(F1), .pin4(F2), .pin5(F3), .pin10(1'b0), .pin15(_74245_3_pin15),
    .pin16(_74245_3_pin16), .pin17(_74245_3_pin17), .pin18(_74245_3_pin18), .pin19(_7404_1_pin2), .pin20(1'b1));  // open: pin6, pin7, pin8, pin9, pin11, pin12, pin13, pin14
  _7408 _7408_2 (
    .pin1(_7404_1_pin2), .pin2(_7404_1_pin10), .pin3(_7408_2_pin3), .pin4(1'b0), .pin5(1'b0), .pin7(1'b0),
    .pin9(1'b0), .pin10(1'b0), .pin12(1'b0), .pin13(1'b0), .pin14(1'b1));  // open: pin6, pin8, pin11
  _74173 _74173_1 (
    .pin1(1'b0), .pin2(1'b0), .pin3(FQ0), .pin4(FQ1), .pin5(FQ2), .pin6(FQ3), .pin7(CP), .pin8(1'b0),
    .pin9(_7408_2_pin3), .pin10(_7408_2_pin3), .pin11(_74245_3_pin15), .pin12(_74245_3_pin16),
    .pin13(_74245_3_pin17), .pin14(_74245_3_pin18), .pin15(RESET), .pin16(1'b1));

  // Notes on the sheet:
  //   F0: CARRY FLAG
  //   F1: ZERO FLAG
  //   F2: RESERVED
  //   F3: RESERVED
  //   IR5: CARRY FLAG
  //   IR6: CARRY FLAG
  //   IR7: CARRY FLAG
  //   FLAGS_LOAD: CARRY FLAG
  //   FLAGS_SET: CARRY FLAG
endmodule
