// Digital circuit MEMORY_UNIT.dig as structural Verilog
module MEMORY_UNIT (
  input  D0,
  input  D1,
  input  D2,
  input  D3,
  input  D4,
  input  D5,
  input  D6,
  input  D7,
  input  EN_MEM,
  input  LOAD_MEM,
  input  LOAD_MAR,
  input  CP,
  input  RESET,
  output Q0,
  output Q1,
  output Q2,
  output Q3,
  output Q4,
  output Q5,
  output Q6,
  output Q7,
  output [7:0] MAR_OUT
);

  wire _7404_1_pin2, _7404_1_pin12, _7404_2_pin2, _7404_2_pin4, _7404_2_pin6, _7404_2_pin12, _7404_3_pin2,
       _7404_3_pin4, _7404_3_pin6, _7404_3_pin12, _74154_1_pin1, _74154_1_pin2, _74154_1_pin3, _74154_1_pin4,
       _74154_1_pin5, _74154_1_pin6, _74154_1_pin7, _74154_1_pin8, _74154_1_pin9, _74154_1_pin10,
       _74154_1_pin11, _74154_1_pin13, _74154_1_pin14, _74154_1_pin15, _74154_1_pin16, _74154_1_pin17,
       _74154_2_pin1, _74154_2_pin2, _74154_2_pin3, _74154_2_pin4, _74154_2_pin5, _74154_2_pin6,
       _74154_2_pin7, _74154_2_pin8, _74154_2_pin9, _74154_2_pin10, _74154_2_pin11, _74154_2_pin13,
       _74154_2_pin14, _74154_2_pin15, _74154_2_pin16, _74154_2_pin17, _74173_1_pin9, RAM0_q0, RAM0_q1,
       RAM0_q2, RAM0_q3, RAM0_q4, RAM0_q5, RAM0_q6, RAM0_q7;

  _74173 _74173_1 (
    .pin1(1'b0), .pin2(1'b0), .pin3(MAR_OUT[4]), .pin4(MAR_OUT[5]), .pin5(MAR_OUT[6]), .pin6(MAR_OUT[7]),
    .pin7(CP), .pin8(1'b0), .pin9(_74173_1_pin9), .pin10(_74173_1_pin9), .pin11(D7), .pin12(D6), .pin13(D5),
    .pin14(D4), .pin15(RESET), .pin16(1'b1));
  _74173 _74173_2 (
    .pin1(1'b0), .pin2(1'b0), .pin3(MAR_OUT[0]), .pin4(MAR_OUT[1]), .pin5(MAR_OUT[2]), .pin6(MAR_OUT[3]),
    .pin7(CP), .pin8(1'b0), .pin9(_74173_1_pin9), .pin10(_74173_1_pin9), .pin11(D3), .pin12(D2), .pin13(D1),
    .pin14(D0), .pin15(RESET), .pin16(1'b1));
  _7404 _7404_1 (
    .pin1(LOAD_MEM), .pin2(_7404_1_pin2), .pin3(LOAD_MAR), .pin4(_74173_1_pin9), .pin5(1'b0), .pin7(1'b0),
    .pin9(1'b0), .pin11(1'b0), .pin12(_7404_1_pin12), .pin13(EN_MEM), .pin14(1'b1));  // open: pin6, pin8, pin10
  _74154 _74154_1 (
    .pin1(_74154_1_pin1), .pin2(_74154_1_pin2), .pin3(_74154_1_pin3), .pin4(_74154_1_pin4),
    .pin5(_74154_1_pin5), .pin6(_74154_1_pin6), .pin7(_74154_1_pin7), .pin8(_74154_1_pin8),
    .pin9(_74154_1_pin9), .pin10(_74154_1_pin10), .pin11(_74154_1_pin11), .pin12(1'b0),
    .pin13(_74154_1_pin13), .pin14(_74154_1_pin14), .pin15(_74154_1_pin15), .pin16(_74154_1_pin16),
    .pin17(_74154_1_pin17), .pin18(_7404_1_pin12), .pin19(_7404_1_pin12), .pin20(MAR_OUT[7]),
    .pin21(MAR_OUT[6]), .pin22(MAR_OUT[5]), .pin23(MAR_OUT[4]), .pin24(1'b1));
  _74154 _74154_2 (
    .pin1(_74154_2_pin1), .pin2(_74154_2_pin2), .pin3(_74154_2_pin3), .pin4(_74154_2_pin4),
    .pin5(_74154_2_pin5), .pin6(_74154_2_pin6), .pin7(_74154_2_pin7), .pin8(_74154_2_pin8),
    .pin9(_74154_2_pin9), .pin10(_74154_2_pin10), .pin11(_74154_2_pin11), .pin12(1'b0),
    .pin13(_74154_2_pin13), .pin14(_74154_2_pin14), .pin15(_74154_2_pin15), .pin16(_74154_2_pin16),
    .pin17(_74154_2_pin17), .pin18(_7404_1_pin2), .pin19(_7404_1_pin2), .pin20(MAR_OUT[7]),
    .pin21(MAR_OUT[6]), .pin22(MAR_OUT[5]), .pin23(MAR_OUT[4]), .pin24(1'b1));
  _128_BIT_RAM RAM0 (
    .D0(D0), .D1(D1), .D2(D2), .D3(D3), .D4(D4), .D5(D5), .D6(D6), .D7(D7), .A3(MAR_OUT[3]), .A2(MAR_OUT[2]),
    .A1(MAR_OUT[1]), .A0(MAR_OUT[0]), .EN(_74154_1_pin1), .WRT(_74154_2_pin1), .Q0(RAM0_q0), .Q1(RAM0_q1),
    .Q2(RAM0_q2), .Q3(RAM0_q3), .Q4(RAM0_q4), .Q5(RAM0_q5), .Q6(RAM0_q6), .Q7(RAM0_q7));
  _128_BIT_RAM _128_bit_ram_1 (
    .D0(D0), .D1(D1), .D2(D2), .D3(D3), .D4(D4), .D5(D5), .D6(D6), .D7(D7), .A3(MAR_OUT[3]), .A2(MAR_OUT[2]),
    .A1(MAR_OUT[1]), .A0(MAR_OUT[0]), .EN(_74154_1_pin2), .WRT(_74154_2_pin2), .Q0(RAM0_q0), .Q1(RAM0_q1),
    .Q2(RAM0_q2), .Q3(RAM0_q3), .Q4(RAM0_q4), .Q5(RAM0_q5), .Q6(RAM0_q6), .Q7(RAM0_q7));
  _128_BIT_RAM _128_bit_ram_2 (
    .D0(D0), .D1(D1), .D2(D2), .D3(D3), .D4(D4), .D5(D5), .D6(D6), .D7(D7), .A3(MAR_OUT[3]), .A2(MAR_OUT[2]),
    .A1(MAR_OUT[1]), .A0(MAR_OUT[0]), .EN(_74154_1_pin3), .WRT(_74154_2_pin3), .Q0(RAM0_q0), .Q1(RAM0_q1),
    .Q2(RAM0_q2), .Q3(RAM0_q3), .Q4(RAM0_q4), .Q5(RAM0_q5), .Q6(RAM0_q6), .Q7(RAM0_q7));
  _128_BIT_RAM _128_bit_ram_3 (
    .D0(D0), .D1(D1), .D2(D2), .D3(D3), .D4(D4), .D5(D5), .D6(D6), .D7(D7), .A3(MAR_OUT[3]), .A2(MAR_OUT[2]),
    .A1(MAR_OUT[1]), .A0(MAR_OUT[0]), .EN(_74154_1_pin4), .WRT(_74154_2_pin4), .Q0(RAM0_q0), .Q1(RAM0_q1),
    .Q2(RAM0_q2), .Q3(RAM0_q3), .Q4(RAM0_q4), .Q5(RAM0_q5), .Q6(RAM0_q6), .Q7(RAM0_q7));
  _128_BIT_RAM RAM1 (
    .D0(D0), .D1(D1), .D2(D2), .D3(D3), .D4(D4), .D5(D5), .D6(D6), .D7(D7), .A3(MAR_OUT[3]), .A2(MAR_OUT[2]),
    .A1(MAR_OUT[1]), .A0(MAR_OUT[0]), .EN(_74154_1_pin5), .WRT(_74154_2_pin5), .Q0(RAM0_q0), .Q1(RAM0_q1),
    .Q2(RAM0_q2), .Q3(RAM0_q3), .Q4(RAM0_q4), .Q5(RAM0_q5), .Q6(RAM0_q6), .Q7(RAM0_q7));
  _128_BIT_RAM _128_bit_ram_4 (
    .D0(D0), .D1(D1), .D2(D2), .D3(D3), .D4(D4), .D5(D5), .D6(D6), .D7(D7), .A3(MAR_OUT[3]), .A2(MAR_OUT[2]),
    .A1(MAR_OUT[1]), .A0(MAR_OUT[0]), .EN(_74154_1_pin6), .WRT(_74154_2_pin6), .Q0(RAM0_q0), .Q1(RAM0_q1),
    .Q2(RAM0_q2), .Q3(RAM0_q3), .Q4(RAM0_q4), .Q5(RAM0_q5), .Q6(RAM0_q6), .Q7(RAM0_q7));
  _128_BIT_RAM _128_bit_ram_5 (
    .D0(D0), .D1(D1), .D2(D2), .D3(D3), .D4(D4), .D5(D5), .D6(D6), .D7(D7), .A3(MAR_OUT[3]), .A2(MAR_OUT[2]),
    .A1(MAR_OUT[1]), .A0(MAR_OUT[0]), .EN(_74154_1_pin7), .WRT(_74154_2_pin7), .Q0(RAM0_q0), .Q1(RAM0_q1),
    .Q2(RAM0_q2), .Q3(RAM0_q3), .Q4(RAM0_q4), .Q5(RAM0_q5), .Q6(RAM0_q6), .Q7(RAM0_q7));
  _128_BIT_RAM _128_bit_ram_6 (
    .D0(D0), .D1(D1), .D2(D2), .D3(D3), .D4(D4), .D5(D5), .D6(D6), .D7(D7), .A3(MAR_OUT[3]), .A2(MAR_OUT[2]),
    .A1(MAR_OUT[1]), .A0(MAR_OUT[0]), .EN(_74154_1_pin8), .WRT(_74154_2_pin8), .Q0(RAM0_q0), .Q1(RAM0_q1),
    .Q2(RAM0_q2), .Q3(RAM0_q3), .Q4(RAM0_q4), .Q5(RAM0_q5), .Q6(RAM0_q6), .Q7(RAM0_q7));
  _128_BIT_RAM RAM2 (
    .D0(D0), .D1(D1), .D2(D2), .D3(D3), .D4(D4), .D5(D5), .D6(D6), .D7(D7), .A3(MAR_OUT[3]), .A2(MAR_OUT[2]),
    .A1(MAR_OUT[1]), .A0(MAR_OUT[0]), .EN(_74154_1_pin9), .WRT(_74154_2_pin9), .Q0(RAM0_q0), .Q1(RAM0_q1),
    .Q2(RAM0_q2), .Q3(RAM0_q3), .Q4(RAM0_q4), .Q5(RAM0_q5), .Q6(RAM0_q6), .Q7(RAM0_q7));
  _128_BIT_RAM _128_bit_ram_7 (
    .D0(D0), .D1(D1), .D2(D2), .D3(D3), .D4(D4), .D5(D5), .D6(D6), .D7(D7), .A3(MAR_OUT[3]), .A2(MAR_OUT[2]),
    .A1(MAR_OUT[1]), .A0(MAR_OUT[0]), .EN(_74154_1_pin10), .WRT(_74154_2_pin10), .Q0(RAM0_q0), .Q1(RAM0_q1),
    .Q2(RAM0_q2), .Q3(RAM0_q3), .Q4(RAM0_q4), .Q5(RAM0_q5), .Q6(RAM0_q6), .Q7(RAM0_q7));
  _128_BIT_RAM _128_bit_ram_8 (
    .D0(D0), .D1(D1), .D2(D2), .D3(D3), .D4(D4), .D5(D5), .D6(D6), .D7(D7), .A3(MAR_OUT[3]), .A2(MAR_OUT[2]),
    .A1(MAR_OUT[1]), .A0(MAR_OUT[0]), .EN(_74154_1_pin11), .WRT(_74154_2_pin11), .Q0(RAM0_q0), .Q1(RAM0_q1),
    .Q2(RAM0_q2), .Q3(RAM0_q3), .Q4(RAM0_q4), .Q5(RAM0_q5), .Q6(RAM0_q6), .Q7(RAM0_q7));
  _128_BIT_RAM _128_bit_ram_9 (
    .D0(D0), .D1(D1), .D2(D2), .D3(D3), .D4(D4), .D5(D5), .D6(D6), .D7(D7), .A3(MAR_OUT[3]), .A2(MAR_OUT[2]),
    .A1(MAR_OUT[1]), .A0(MAR_OUT[0]), .EN(_74154_1_pin13), .WRT(_74154_2_pin13), .Q0(RAM0_q0), .Q1(RAM0_q1),
    .Q2(RAM0_q2), .Q3(RAM0_q3), .Q4(RAM0_q4), .Q5(RAM0_q5), .Q6(RAM0_q6), .Q7(RAM0_q7));
  _128_BIT_RAM RAM3 (
    .D0(D0), .D1(D1), .D2(D2), .D3(D3), .D4(D4), .D5(D5), .D6(D6), .D7(D7), .A3(MAR_OUT[3]), .A2(MAR_OUT[2]),
    .A1(MAR_OUT[1]), .A0(MAR_OUT[0]), .EN(_74154_1_pin14), .WRT(_74154_2_pin14), .Q0(RAM0_q0), .Q1(RAM0_q1),
    .Q2(RAM0_q2), .Q3(RAM0_q3), .Q4(RAM0_q4), .Q5(RAM0_q5), .Q6(RAM0_q6), .Q7(RAM0_q7));
  _128_BIT_RAM _128_bit_ram_10 (
    .D0(D0), .D1(D1), .D2(D2), .D3(D3), .D4(D4), .D5(D5), .D6(D6), .D7(D7), .A3(MAR_OUT[3]), .A2(MAR_OUT[2]),
    .A1(MAR_OUT[1]), .A0(MAR_OUT[0]), .EN(_74154_1_pin15), .WRT(_74154_2_pin15), .Q0(RAM0_q0), .Q1(RAM0_q1),
    .Q2(RAM0_q2), .Q3(RAM0_q3), .Q4(RAM0_q4), .Q5(RAM0_q5), .Q6(RAM0_q6), .Q7(RAM0_q7));
  _128_BIT_RAM _128_bit_ram_11 (
    .D0(D0), .D1(D1), .D2(D2), .D3(D3), .D4(D4), .D5(D5), .D6(D6), .D7(D7), .A3(MAR_OUT[3]), .A2(MAR_OUT[2]),
    .A1(MAR_OUT[1]), .A0(MAR_OUT[0]), .EN(_74154_1_pin16), .WRT(_74154_2_pin16), .Q0(RAM0_q0), .Q1(RAM0_q1),
    .Q2(RAM0_q2), .Q3(RAM0_q3), .Q4(RAM0_q4), .Q5(RAM0_q5), .Q6(RAM0_q6), .Q7(RAM0_q7));
  _128_BIT_RAM _128_bit_ram_12 (
    .D0(D0), .D1(D1), .D2(D2), .D3(D3), .D4(D4), .D5(D5), .D6(D6), .D7(D7), .A3(MAR_OUT[3]), .A2(MAR_OUT[2]),
    .A1(MAR_OUT[1]), .A0(MAR_OUT[0]), .EN(_74154_1_pin17), .WRT(_74154_2_pin17), .Q0(RAM0_q0), .Q1(RAM0_q1),
    .Q2(RAM0_q2), .Q3(RAM0_q3), .Q4(RAM0_q4), .Q5(RAM0_q5), .Q6(RAM0_q6), .Q7(RAM0_q7));
  _7404 _7404_2 (
    .pin1(RAM0_q3), .pin2(_7404_2_pin2), .pin3(RAM0_q2), .pin4(_7404_2_pin4), .pin5(RAM0_q1),
    .pin6(_7404_2_pin6), .pin7(1'b0), .pin9(1'b0), .pin11(1'b0), .pin12(_7404_2_pin12), .pin13(RAM0_q0),
    .pin14(1'b1));  // open: pin8, pin10
  _7404 _7404_3 (
    .pin1(RAM0_q7), .pin2(_7404_3_pin2), .pin3(RAM0_q6), .pin4(_7404_3_pin4), .pin5(RAM0_q5),
    .pin6(_7404_3_pin6), .pin7(1'b0), .pin9(1'b0), .pin11(1'b0), .pin12(_7404_3_pin12), .pin13(RAM0_q4),
    .pin14(1'b1));  // open: pin8, pin10
  _74245 _74245_1 (
    .pin1(1'b0), .pin2(Q7), .pin3(Q6), .pin4(Q5), .pin5(Q4), .pin6(Q3), .pin7(Q2), .pin8(Q1), .pin9(Q0),
    .pin10(1'b0), .pin11(_7404_2_pin12), .pin12(_7404_2_pin6), .pin13(_7404_2_pin4), .pin14(_7404_2_pin2),
    .pin15(_7404_3_pin12), .pin16(_7404_3_pin6), .pin17(_7404_3_pin4), .pin18(_7404_3_pin2),
    .pin19(_7404_1_pin12), .pin20(1'b1));
endmodule
