// Digital circuit MEMORY_UNIT_2.dig as structural Verilog
module MEMORY_UNIT_2 (
  input  D0,
  input  D1,
  input  D2,
  input  D3,
  input  D4,
  input  D5,
  input  D6,
  input  D7,
  input  EN_MEM,
  input  LOAD_MEM,
  input  LOAD_MAR,
  input  CP,
  input  RESET,
  input  RESET_MAR,
  output Q0,
  output Q1,
  output Q2,
  output Q3,
  output Q4,
  output Q5,
  output Q6,
  output Q7,
  output [7:0] MAR_OUT
);

  wire _7404_1_pin2, or_1_out;

  or or_1 (or_1_out, RESET, RESET_MAR);
  _7404 _7404_1 (
    .pin1(LOAD_MAR), .pin2(_7404_1_pin2), .pin3(1'b0), .pin5(1'b0), .pin7(1'b0), .pin9(1'b0), .pin11(1'b0),
    .pin12(1'b0), .pin13(1'b0), .pin14(1'b1));  // open: pin4, pin6, pin8, pin10
  _74173 _74173_1 (
    .pin1(1'b0), .pin2(1'b0), .pin3(MAR_OUT[0]), .pin4(MAR_OUT[1]), .pin5(MAR_OUT[2]), .pin6(MAR_OUT[3]),
    .pin7(CP), .pin8(1'b0), .pin9(_7404_1_pin2), .pin10(_7404_1_pin2), .pin11(D3), .pin12(D2), .pin13(D1),
    .pin14(D0), .pin15(or_1_out), .pin16(1'b1));
  RAMDualPort #(.AddrBits(8), .isProgramMemory("true"), .Bits(8)) MAIN_MEMORY (
    .A(MAR_OUT), .Din({D7, D6, D5, D4, D3, D2, D1, D0}), .str(LOAD_MEM), .C(CP), .ld(EN_MEM),
    .D({Q7, Q6, Q5, Q4, Q3, Q2, Q1, Q0}));
  _74173 _74173_2 (
    .pin1(1'b0), .pin2(1'b0), .pin3(MAR_OUT[4]), .pin4(MAR_OUT[5]), .pin5(MAR_OUT[6]), .pin6(MAR_OUT[7]),
    .pin7(CP), .pin8(1'b0), .pin9(_7404_1_pin2), .pin10(_7404_1_pin2), .pin11(D7), .pin12(D6), .pin13(D5),
    .pin14(D4), .pin15(or_1_out), .pin16(1'b1));
endmodule
