// Digital circuit OUTPUT_REGISTER.dig as structural Verilog
module OUTPUT_REGISTER (
  input  D0,
  input  D1,
  input  D2,
  input  D3,
  input  D4,
  input  D5,
  input  D6,
  input  D7,
  input  LOAD_OUT,
  input  RESET,
  input  CP,
  output [3:0] OUTP0,
  output [3:0] OUTP1
);

  wire _7404_1_pin12;

  _7404 _7404_1 (
    .pin1(1'b0), .pin3(1'b0), .pin5(1'b0), .pin7(1'b0), .pin9(1'b0), .pin11(1'b0), .pin12(_7404_1_pin12),
    .pin13(LOAD_OUT), .pin14(1'b1));  // open: pin2, pin4, pin6, pin8, pin10
  _74173 _74173_1 (
    .pin1(1'b0), .pin2(1'b0), .pin3(OUTP0[0]), .pin4(OUTP0[1]), .pin5(OUTP0[2]), .pin6(OUTP0[3]), .pin7(CP),
    .pin8(1'b0), .pin9(_7404_1_pin12), .pin10(_7404_1_pin12), .pin11(D3), .pin12(D2), .pin13(D1), .pin14(D0),
    .pin15(RESET), .pin16(1'b1));
  _74173 _74173_2 (
    .pin1(1'b0), .pin2(1'b0), .pin3(OUTP1[0]), .pin4(OUTP1[1]), .pin5(OUTP1[2]), .pin6(OUTP1[3]), .pin7(CP),
    .pin8(1'b0), .pin9(_7404_1_pin12), .pin10(_7404_1_pin12), .pin11(D7), .pin12(D6), .pin13(D5), .pin14(D4),
    .pin15(RESET), .pin16(1'b1));
endmodule
