// Digital circuit PROGRAM_COUNTER.dig as structural Verilog
module PROGRAM_COUNTER (
  input  D0,
  input  D1,
  input  D2,
  input  D3,
  input  D4,
  input  D5,
  input  D6,
  input  D7,
  input  LOAD,
  input  COUNT,
  input  EN,
  input  CLEAR,
  input  CP,
  output Q0,
  output Q1,
  output Q2,
  output Q3,
  output Q4,
  output Q5,
  output Q6,
  output Q7,
  output [7:0] PC_OUT
);

  wire _7404_1_pin2, _7404_1_pin4, _7404_1_pin12, _74161_1_pin15;

  _7404 _7404_1 (
    .pin1(LOAD), .pin2(_7404_1_pin2), .pin3(CLEAR), .pin4(_7404_1_pin4), .pin5(1'b0), .pin7(1'b0),
    .pin9(1'b0), .pin11(1'b0), .pin12(_7404_1_pin12), .pin13(EN), .pin14(1'b1));  // open: pin6, pin8, pin10
  _74161 _74161_1 (
    .pin1(_7404_1_pin4), .pin2(CP), .pin3(D0), .pin4(D1), .pin5(D2), .pin6(D3), .pin7(COUNT), .pin8(1'b0),
    .pin9(_7404_1_pin2), .pin10(COUNT), .pin11(PC_OUT[3]), .pin12(PC_OUT[2]), .pin13(PC_OUT[1]),
    .pin14(PC_OUT[0]), .pin15(_74161_1_pin15), .pin16(1'b1));
  _74161 _74161_2 (
    .pin1(_7404_1_pin4), .pin2(CP), .pin3(D4), .pin4(D5), .pin5(D6), .pin6(D7), .pin7(COUNT), .pin8(1'b0),
    .pin9(_7404_1_pin2), .pin10(_74161_1_pin15), .pin11(PC_OUT[7]), .pin12(PC_OUT[6]), .pin13(PC_OUT[5]),
    .pin14(PC_OUT[4]), .pin16(1'b1));  // open: pin15
  _74245 _74245_1 (
    .pin1(1'b0), .pin2(Q7), .pin3(Q6), .pin4(Q5), .pin5(Q4), .pin6(Q3), .pin7(Q2), .pin8(Q1), .pin9(Q0),
    .pin10(1'b0), .pin11(PC_OUT[0]), .pin12(PC_OUT[1]), .pin13(PC_OUT[2]), .pin14(PC_OUT[3]),
    .pin15(PC_OUT[4]), .pin16(PC_OUT[5]), .pin17(PC_OUT[6]), .pin18(PC_OUT[7]), .pin19(_7404_1_pin12),
    .pin20(1'b1));
endmodule
