// Digital circuit PROGRAM_UNIT.dig as structural Verilog
module PROGRAM_UNIT (
  input  PROGRAM,
  input  READ_PIN,
  input  CLOCK_IN,
  input  WRITE_PIN,
  input  RESET,
  input  [7:0] INSTR,
  output BUSY,
  output WRITING,
  output EN_MEM,
  output LOAD_MEM,
  output LOAD_MAR,
  output [7:0] DATA_OUT
);

  wire and_1_out, and_2_out, and_3_out, and_4_out, not_1_out, not_2_out, or_1_out, or_2_out;
  wire [3:0] STEP_out;
  wire [4:4] READ_out;
  wire [5:3] PROGRAM_ROM_d;
  wire [7:0] ADDR_out, driver_1_out, INSTR_q;

  not not_1 (not_1_out, BUSY);
  not not_2 (not_2_out, BUSY);
  and and_1 (and_1_out, not_1_out, WRITE_PIN);
  and and_2 (and_2_out, not_2_out, READ_PIN);
  and and_3 (and_3_out, WRITE_PIN, PROGRAM, CLOCK_IN);
  and and_4 (and_4_out, READ_PIN, PROGRAM, CLOCK_IN);
  or or_1 (or_1_out, and_3_out, PROGRAM_ROM_d[3]);
  or or_2 (or_2_out, and_4_out, PROGRAM_ROM_d[3]);
  CounterPreset #(.Bits(8)) ADDR (
    .en(PROGRAM_ROM_d[5]), .C(CLOCK_IN), .dir(1'b0), .in(INSTR), .ld(1'b0), .clr(RESET), .out(ADDR_out));  // open: ovf
  Register #(.Bits(8)) u_INSTR (.D(INSTR), .C(CLOCK_IN), .en(PROGRAM_ROM_d[4]), .Q(INSTR_q));
  Counter WRITE (.en(and_1_out), .C(or_1_out), .clr(PROGRAM_ROM_d[3]), .out(WRITING));  // open: ovf
  Counter READ (.en(and_2_out), .C(or_2_out), .clr(PROGRAM_ROM_d[3]), .out(READ_out[4]));  // open: ovf
  Counter #(.Bits(4)) STEP (.en(BUSY), .C(CLOCK_IN), .clr(PROGRAM_ROM_d[3]), .out(STEP_out));  // open: ovf
  assign driver_1_out = LOAD_MAR ? ADDR_out : 8'bz;  // Driver driver_1
  or or_3 (BUSY, WRITING, READ_out[4]);
  ROM #(.AddrBits(5), .Bits(6)) PROGRAM_ROM (
    .A({READ_out[4], STEP_out}), .sel(1'b1), .D({PROGRAM_ROM_d, LOAD_MAR, LOAD_MEM, EN_MEM}));
  assign driver_1_out = LOAD_MEM ? INSTR_q : 8'bz;  // Driver driver_2
  assign DATA_OUT = PROGRAM ? driver_1_out : 8'bz;  // Driver driver_3
  LED led_1 (.in(BUSY));
  LED led_2 (.in(WRITING));
  LED led_3 (.in(STEP_out[0]));
  LED led_4 (.in(STEP_out[1]));
  LED led_5 (.in(STEP_out[2]));
  LED led_6 (.in(STEP_out[3]));

  // Notes on the sheet:
  //   contents of PROGRAM_ROM (hex, n*v repeats v):
  //   0,10,2,0,0,0,0,0,0,0,0,0,0,0,0,8,0,0,0,0,0,0,0,0,0,0,0,0,0,0,0,8
endmodule
