// Digital circuit REGISTER_UNIT.dig as structural Verilog
module REGISTER_UNIT (
  input  D0,
  input  D1,
  input  D2,
  input  D3,
  input  D4,
  input  D5,
  input  D6,
  input  D7,
  input  LOAD,
  input  EN,
  input  CP,
  input  RESET,
  input  S1D0,
  input  S1D1,
  input  S1D2,
  input  S2D0,
  input  S2D1,
  input  S2D2,
  output Q0,
  output Q1,
  output Q2,
  output Q3,
  output Q4,
  output Q5,
  output Q6,
  output Q7
);

  wire _7404_1_pin2, _7404_1_pin4, _74138_1_pin12, _74138_1_pin13, _74138_1_pin14, _74138_1_pin15,
       _74138_2_pin12, _74138_2_pin13, _74138_2_pin14, _74138_2_pin15;

  _7404 _7404_1 (
    .pin1(LOAD), .pin2(_7404_1_pin2), .pin3(EN), .pin4(_7404_1_pin4), .pin5(1'b0), .pin7(1'b0), .pin9(1'b0),
    .pin11(1'b0), .pin13(1'b0), .pin14(1'b1));  // open: pin6, pin8, pin10, pin12
  _74138 _74138_1 (
    .pin1(S1D0), .pin2(S1D1), .pin3(S1D2), .pin4(_7404_1_pin2), .pin5(_7404_1_pin2), .pin6(LOAD),
    .pin8(1'b0), .pin12(_74138_1_pin12), .pin13(_74138_1_pin13), .pin14(_74138_1_pin14),
    .pin15(_74138_1_pin15), .pin16(1'b1));  // open: pin7, pin9, pin10, pin11
  _74138 _74138_2 (
    .pin1(S2D0), .pin2(S2D1), .pin3(S2D2), .pin4(_7404_1_pin4), .pin5(_7404_1_pin4), .pin6(EN), .pin8(1'b0),
    .pin12(_74138_2_pin12), .pin13(_74138_2_pin13), .pin14(_74138_2_pin14), .pin15(_74138_2_pin15),
    .pin16(1'b1));  // open: pin7, pin9, pin10, pin11
  _74173 _74173_1 (
    .pin1(_74138_2_pin15), .pin2(_74138_2_pin15), .pin3(Q0), .pin4(Q1), .pin5(Q2), .pin6(Q3), .pin7(CP),
    .pin8(1'b0), .pin9(_74138_1_pin15), .pin10(_74138_1_pin15), .pin11(D3), .pin12(D2), .pin13(D1),
    .pin14(D0), .pin15(RESET), .pin16(1'b1));
  _74173 _74173_2 (
    .pin1(_74138_2_pin15), .pin2(_74138_2_pin15), .pin3(Q4), .pin4(Q5), .pin5(Q6), .pin6(Q7), .pin7(CP),
    .pin8(1'b0), .pin9(_74138_1_pin15), .pin10(_74138_1_pin15), .pin11(D7), .pin12(D6), .pin13(D5),
    .pin14(D4), .pin15(RESET), .pin16(1'b1));
  _74173 _74173_3 (
    .pin1(_74138_2_pin14), .pin2(_74138_2_pin14), .pin3(Q0), .pin4(Q1), .pin5(Q2), .pin6(Q3), .pin7(CP),
    .pin8(1'b0), .pin9(_74138_1_pin14), .pin10(_74138_1_pin14), .pin11(D3), .pin12(D2), .pin13(D1),
    .pin14(D0), .pin15(RESET), .pin16(1'b1));
  _74173 _74173_4 (
    .pin1(_74138_2_pin14), .pin2(_74138_2_pin14), .pin3(Q4), .pin4(Q5), .pin5(Q6), .pin6(Q7), .pin7(CP),
    .pin8(1'b0), .pin9(_74138_1_pin14), .pin10(_74138_1_pin14), .pin11(D7), .pin12(D6), .pin13(D5),
    .pin14(D4), .pin15(RESET), .pin16(1'b1));
  _74173 _74173_5 (
    .pin1(_74138_2_pin13), .pin2(_74138_2_pin13), .pin3(Q0), .pin4(Q1), .pin5(Q2), .pin6(Q3), .pin7(CP),
    .pin8(1'b0), .pin9(_74138_1_pin13), .pin10(_74138_1_pin13), .pin11(D3), .pin12(D2), .pin13(D1),
    .pin14(D0), .pin15(RESET), .pin16(1'b1));
  _74173 _74173_6 (
    .pin1(_74138_2_pin13), .pin2(_74138_2_pin13), .pin3(Q4), .pin4(Q5), .pin5(Q6), .pin6(Q7), .pin7(CP),
    .pin8(1'b0), .pin9(_74138_1_pin13), .pin10(_74138_1_pin13), .pin11(D7), .pin12(D6), .pin13(D5),
    .pin14(D4), .pin15(RESET), .pin16(1'b1));
  _74173 _74173_7 (
    .pin1(_74138_2_pin12), .pin2(_74138_2_pin12), .pin3(Q0), .pin4(Q1), .pin5(Q2), .pin6(Q3), .pin7(CP),
    .pin8(1'b0), .pin9(_74138_1_pin12), .pin10(_74138_1_pin12), .pin11(D3), .pin12(D2), .pin13(D1),
    .pin14(D0), .pin15(RESET), .pin16(1'b1));
  _74173 _74173_8 (
    .pin1(_74138_2_pin12), .pin2(_74138_2_pin12), .pin3(Q4), .pin4(Q5), .pin5(Q6), .pin6(Q7), .pin7(CP),
    .pin8(1'b0), .pin9(_74138_1_pin12), .pin10(_74138_1_pin12), .pin11(D7), .pin12(D6), .pin13(D5),
    .pin14(D4), .pin15(RESET), .pin16(1'b1));
endmodule
