// Digital circuit ZF_LOGIC.dig as structural Verilog
module ZF_LOGIC (
  input  D0,
  input  D1,
  input  D2,
  input  D3,
  input  D4,
  input  D5,
  input  D6,
  input  D7,
  output ZF
);

  wire _7425_1_pin6, _7425_1_pin8;

  _7425 _7425_1 (
    .pin1(D0), .pin2(D1), .pin4(D2), .pin5(D3), .pin6(_7425_1_pin6), .pin7(1'b0), .pin8(_7425_1_pin8),
    .pin9(D4), .pin10(D5), .pin12(D6), .pin13(D7), .pin14(1'b1));  // open: pin3, pin11
  _7408 _7408_1 (
    .pin1(_7425_1_pin6), .pin2(_7425_1_pin8), .pin3(ZF), .pin4(1'b0), .pin5(1'b0), .pin7(1'b0), .pin9(1'b0),
    .pin10(1'b0), .pin12(1'b0), .pin13(1'b0), .pin14(1'b1));  // open: pin6, pin8, pin11
endmodule
