// Logisim project 8bitmicro.circ as structural Verilog
module main (
);

  wire [2:0] control_unit_1_reg_out, fetch_unit_1_select2_out;
  wire [7:0] fetch_unit_1_instr, memory_unit_1_dout;

  MEMORY_UNIT memory_unit_1 (.DOUT(memory_unit_1_dout));  // open: DIN, CLK, MAR_LOAD, MEM_LOAD, MEM_EN, CLEAR
  FETCH_UNIT fetch_unit_1 (
    .DIN(memory_unit_1_dout), .INSTR(fetch_unit_1_instr), .SELECT2_OUT(fetch_unit_1_select2_out));  // open: CLK, CLEAR, INSTR_LOAD, ARG_LOAD, ARG_EN, SELECT2_LOAD, DOUT
  CONTROL_UNIT control_unit_1 (
    .INSTR(fetch_unit_1_instr), .REG_OUT(control_unit_1_reg_out));  // open: RESET, CLK, FLAGS_IN, PC_EN, PC_COUNT, PC_LOAD, REG_EN, REG_LOAD, MAR_LOAD, MEM_EN, MEM_LOAD, FLAGS_LOAD, ALU_OP, LOGIC, AC_LOAD, OUT_LOAD, INSTR_LOAD, ARG_LOAD, ARG_EN, JC, FLAGS_SET, SELECT2_LOAD
  REGISTER_UNIT register_unit_1 (
    .SELECT(control_unit_1_reg_out), .DIN(memory_unit_1_dout), .SELECT2(fetch_unit_1_select2_out),
    .DOUT(memory_unit_1_dout));  // open: REG_LOAD, CLK, CLEAR, REG_EN
  _8_BIT_ALU u_8_bit_alu_1 (.Din(memory_unit_1_dout));  // open: LOAD_AC, EN_ALU, CLK, CLEAR, ALU_OP, LOGIC, CO, ZR, ALU_OUT
endmodule

// CONTROL
module CONTROL_UNIT (
  input  [7:0] INSTR,
  input  RESET,
  input  CLK,
  input  [3:0] FLAGS_IN,
  output [2:0] REG_OUT,
  output PC_EN,
  output PC_COUNT,
  output PC_LOAD,
  output REG_EN,
  output REG_LOAD,
  output MAR_LOAD,
  output MEM_EN,
  output MEM_LOAD,
  output FLAGS_LOAD,
  output [3:0] ALU_OP,
  output LOGIC,
  output AC_LOAD,
  output OUT_LOAD,
  output INSTR_LOAD,
  output ARG_LOAD,
  output ARG_EN,
  output JC,
  output FLAGS_SET,
  output SELECT2_LOAD
);

  wire multiplexer_1_out, not_1_out;
  wire [2:0] STEP_q;
  wire [3:0] not_2_out;
  wire [7:3] rom_3_data;

  not not_1 (not_1_out, CLK);
  assign not_2_out = ~FLAGS_IN;  // NOT_Gate not_2, 4 bits wide
  Counter #(.width(3), .max('h7)) STEP (.Q(STEP_q), .clk(not_1_out), .clr(RESET));  // open: load, D, count, carry
  Multiplexer #(.select(3)) multiplexer_1 (
    .in0(FLAGS_IN[0]), .in1(FLAGS_IN[1]), .in2(FLAGS_IN[2]), .in3(FLAGS_IN[3]), .in4(not_2_out[0]),
    .in5(not_2_out[1]), .in6(not_2_out[2]), .in7(not_2_out[3]), .out(multiplexer_1_out), .sel(INSTR[7:5]));  // open: en
  ROM #(.addrWidth(11)) rom_1 (
    .addr({INSTR, STEP_q}), .data({MEM_LOAD, MEM_EN, MAR_LOAD, REG_LOAD, REG_EN, PC_LOAD, PC_COUNT, PC_EN}));  // open: sel
  ROM #(.addrWidth(11)) rom_2 (
    .addr({INSTR, STEP_q}), .data({OUT_LOAD, AC_LOAD, LOGIC, ALU_OP, FLAGS_LOAD}));  // open: sel
  and and_1 (JC, rom_3_data[3], multiplexer_1_out);
  ROM #(.addrWidth(11)) rom_3 (
    .addr({INSTR, STEP_q}),
    .data({rom_3_data[7:6], SELECT2_LOAD, FLAGS_SET, rom_3_data[3], ARG_EN, ARG_LOAD, INSTR_LOAD}));  // open: sel

  assign REG_OUT = INSTR[7:5];
endmodule

// FETCH
module FETCH_UNIT (
  input  [7:0] DIN,
  input  CLK,
  input  CLEAR,
  input  INSTR_LOAD,
  input  ARG_LOAD,
  input  ARG_EN,
  input  SELECT2_LOAD,
  output [2:0] SELECT2_OUT,
  output [7:0] INSTR,
  output [7:0] DOUT
);

  wire n7404_1_y1, n7404_1_y2, n7404_1_y3, n7404_1_y6;

  _7404 u_7404_1 (
    .A1(ARG_LOAD), .Y1(n7404_1_y1), .A2(INSTR_LOAD), .Y2(n7404_1_y2), .A3(ARG_EN), .Y3(n7404_1_y3),
    .A6(SELECT2_LOAD), .Y6(n7404_1_y6));  // open: A4, Y5, A5, Y5_2
  _74173 u_74173_1 (
    .D0(DIN[0]), .D1(DIN[1]), .D2(DIN[2]), .D3(DIN[3]), .iE1(n7404_1_y2), .iE2(n7404_1_y2), .CP(CLK),
    .MR(CLEAR), .iOE1(1'b0), .iOE2(1'b0), .Q0(INSTR[0]), .Q1(INSTR[1]), .Q2(INSTR[2]), .Q3(INSTR[3]));
  _74173 u_74173_2 (
    .D0(DIN[4]), .D1(DIN[5]), .D2(DIN[6]), .D3(DIN[7]), .iE1(n7404_1_y2), .iE2(n7404_1_y2), .CP(CLK),
    .MR(CLEAR), .iOE1(1'b0), .iOE2(1'b0), .Q0(INSTR[4]), .Q1(INSTR[5]), .Q2(INSTR[6]), .Q3(INSTR[7]));
  _74173 u_74173_3 (
    .D0(DIN[0]), .D1(DIN[1]), .D2(DIN[2]), .D3(DIN[3]), .iE1(n7404_1_y1), .iE2(n7404_1_y1), .CP(CLK),
    .MR(CLEAR), .iOE1(n7404_1_y3), .iOE2(n7404_1_y3), .Q0(DOUT[0]), .Q1(DOUT[1]), .Q2(DOUT[2]), .Q3(DOUT[3]));
  _74173 u_74173_4 (
    .D0(DIN[4]), .D1(DIN[5]), .D2(DIN[6]), .D3(DIN[7]), .iE1(n7404_1_y1), .iE2(n7404_1_y1), .CP(CLK),
    .MR(CLEAR), .iOE1(n7404_1_y3), .iOE2(n7404_1_y3), .Q0(DOUT[4]), .Q1(DOUT[5]), .Q2(DOUT[6]), .Q3(DOUT[7]));
  _74173 u_74173_5 (
    .D0(DIN[0]), .D1(DIN[1]), .D2(DIN[2]), .D3(DIN[3]), .iE1(n7404_1_y6), .iE2(n7404_1_y6), .CP(CLK),
    .MR(CLEAR), .iOE1(1'b0), .iOE2(1'b0), .Q0(SELECT2_OUT[0]), .Q1(SELECT2_OUT[1]), .Q2(SELECT2_OUT[2]));  // open: Q3
endmodule

module FLAG_UNIT (
  input  f3,
  input  f2,
  input  f1,
  input  f0,
  input  [3:0] Fctrl,
  input  CLK,
  input  SET,
  input  UPDATE,
  output [3:0] FLAGS_OUT
);

  wire or_1_out;
  wire [3:0] controlled_buffer_1_out;

  assign controlled_buffer_1_out = UPDATE ? {f3, f2, f1, f0} : 4'bz;  // Controlled_Buffer controlled_buffer_1
  assign controlled_buffer_1_out = SET ? Fctrl : 4'bz;  // Controlled_Buffer controlled_buffer_2
  or or_1 (or_1_out, UPDATE, SET);
  Register #(.width(4)) register_1 (.D(controlled_buffer_1_out), .en(or_1_out), .Q(FLAGS_OUT), .clk(CLK));  // open: clr
endmodule

module FLAG_CONTROL (
  input  [2:0] INSTR,
  input  [3:0] FLAGS,
  output [3:0] FLAGS_OUT
);

  wire n7404_1_y1, n7404_1_y2, n7404_1_y3, n7404_1_y5_2, n7404_1_y6, n7408_1_y1, n7408_1_y2, n7408_1_y3,
       n7408_1_y4, n7432_1_y1, n7432_1_y2, n7432_1_y3, n7432_1_y4, n74155_1__1y0, n74155_1__1y1,
       n74155_1__1y2, n74155_1__1y3, n74155_1__2y0, n74155_1__2y1, n74155_1__2y2, n74155_1__2y3;

  _74155 u_74155_1 (
    .STROBE(1'b0), .DATA(INSTR[2]), .SELECT_B(INSTR[1]), .SELECT_A(INSTR[0]), .DATA2(1'b0),
    .STROBE2(INSTR[2]), ._1Y0(n74155_1__1y0), ._1Y1(n74155_1__1y1), ._1Y2(n74155_1__1y2),
    ._1Y3(n74155_1__1y3), ._2Y0(n74155_1__2y0), ._2Y1(n74155_1__2y1), ._2Y2(n74155_1__2y2),
    ._2Y3(n74155_1__2y3));
  _7404 u_7404_1 (
    .A1(n74155_1__1y3), .Y1(n7404_1_y1), .A2(n74155_1__1y2), .Y2(n7404_1_y2), .A3(n74155_1__1y1),
    .Y3(n7404_1_y3), .A5(INSTR[2]), .Y5_2(n7404_1_y5_2), .A6(n74155_1__1y0), .Y6(n7404_1_y6));  // open: A4, Y5
  _7408 u_7408_1 (
    .A1(n74155_1__2y3), .B1(FLAGS[3]), .Y1(n7408_1_y1), .A2(n74155_1__2y2), .B2(FLAGS[2]), .Y2(n7408_1_y2),
    .A3(n74155_1__2y0), .B3(FLAGS[0]), .Y3(n7408_1_y3), .A4(FLAGS[1]), .B4(n74155_1__2y1), .Y4(n7408_1_y4));
  _7432 u_7432_1 (
    .A1(n7404_1_y1), .B1(FLAGS[3]), .Y1(n7432_1_y1), .A2(n7404_1_y2), .B2(FLAGS[2]), .Y2(n7432_1_y2),
    .A3(n7404_1_y6), .B3(FLAGS[0]), .Y3(n7432_1_y3), .A4(FLAGS[1]), .B4(n7404_1_y3), .Y4(n7432_1_y4));
  _74243 u_74243_1 (
    .OEB(1'b0), .A0(FLAGS_OUT[0]), .A1(FLAGS_OUT[1]), .A2(FLAGS_OUT[2]), .A3(FLAGS_OUT[3]),
    .OEA(n7404_1_y5_2), .B0(n7408_1_y3), .B1(n7408_1_y4), .B2(n7408_1_y2), .B3(n7408_1_y1));
endmodule

// REGISTER
module REGISTER_UNIT (
  input  [2:0] SELECT,
  input  REG_LOAD,
  input  CLK,
  input  CLEAR,
  input  [7:0] DIN,
  input  [2:0] SELECT2,
  input  REG_EN,
  output [7:0] DOUT
);

  wire n7404_1_y1, n7404_1_y2, n74138_1_y0, n74138_1_y1, n74138_1_y2, n74138_1_y3, n74138_2_y0, n74138_2_y1,
       n74138_2_y2, n74138_2_y3;

  _7404 u_7404_1 (
    .A1(REG_LOAD), .Y1(n7404_1_y1), .A2(REG_EN), .Y2(n7404_1_y2));  // open: A3, Y3, A4, Y5, A5, Y5_2, A6, Y6
  _74138 u_74138_1 (
    .E3(REG_EN), .iE2(n7404_1_y2), .iE1(n7404_1_y2), .A0(SELECT2[0]), .A1(SELECT2[1]), .A2(SELECT2[2]),
    .Y0(n74138_1_y0), .Y1(n74138_1_y1), .Y2(n74138_1_y2), .Y3(n74138_1_y3));  // open: Y4, Y5, Y6, Y7
  _74138 u_74138_2 (
    .E3(REG_LOAD), .iE2(n7404_1_y1), .iE1(n7404_1_y1), .A0(SELECT[0]), .A1(SELECT[1]), .A2(SELECT[2]),
    .Y0(n74138_2_y0), .Y1(n74138_2_y1), .Y2(n74138_2_y2), .Y3(n74138_2_y3));  // open: Y4, Y5, Y6, Y7
  _74173 u_74173_1 (
    .D0(DIN[0]), .D1(DIN[1]), .D2(DIN[2]), .D3(DIN[3]), .iE1(n74138_2_y0), .iE2(n74138_2_y0), .CP(CLK),
    .MR(CLEAR), .iOE1(n74138_1_y0), .iOE2(n74138_1_y0), .Q0(DOUT[0]), .Q1(DOUT[1]), .Q2(DOUT[2]), .Q3(DOUT[3]));
  _74173 u_74173_2 (
    .D0(DIN[4]), .D1(DIN[5]), .D2(DIN[6]), .D3(DIN[7]), .iE1(n74138_2_y0), .iE2(n74138_2_y0), .CP(CLK),
    .MR(CLEAR), .iOE1(n74138_1_y0), .iOE2(n74138_1_y0), .Q0(DOUT[4]), .Q1(DOUT[5]), .Q2(DOUT[6]), .Q3(DOUT[7]));
  _74173 u_74173_3 (
    .D0(DIN[0]), .D1(DIN[1]), .D2(DIN[2]), .D3(DIN[3]), .iE1(n74138_2_y1), .iE2(n74138_2_y1), .CP(CLK),
    .MR(CLEAR), .iOE1(n74138_1_y1), .iOE2(n74138_1_y1), .Q0(DOUT[0]), .Q1(DOUT[1]), .Q2(DOUT[2]), .Q3(DOUT[3]));
  _74173 u_74173_4 (
    .D0(DIN[4]), .D1(DIN[5]), .D2(DIN[6]), .D3(DIN[7]), .iE1(n74138_2_y1), .iE2(n74138_2_y1), .CP(CLK),
    .MR(CLEAR), .iOE1(n74138_1_y1), .iOE2(n74138_1_y1), .Q0(DOUT[4]), .Q1(DOUT[5]), .Q2(DOUT[6]), .Q3(DOUT[7]));
  _74173 u_74173_5 (
    .D0(DIN[0]), .D1(DIN[1]), .D2(DIN[2]), .D3(DIN[3]), .iE1(n74138_2_y2), .iE2(n74138_2_y2), .CP(CLK),
    .MR(CLEAR), .iOE1(n74138_1_y2), .iOE2(n74138_1_y2), .Q0(DOUT[0]), .Q1(DOUT[1]), .Q2(DOUT[2]), .Q3(DOUT[3]));
  _74173 u_74173_6 (
    .D0(DIN[4]), .D1(DIN[5]), .D2(DIN[6]), .D3(DIN[7]), .iE1(n74138_2_y2), .iE2(n74138_2_y2), .CP(CLK),
    .MR(CLEAR), .iOE1(n74138_1_y2), .iOE2(n74138_1_y2), .Q0(DOUT[4]), .Q1(DOUT[5]), .Q2(DOUT[6]), .Q3(DOUT[7]));
  _74173 u_74173_7 (
    .D0(DIN[0]), .D1(DIN[1]), .D2(DIN[2]), .D3(DIN[3]), .iE1(n74138_2_y3), .iE2(n74138_2_y3), .CP(CLK),
    .MR(CLEAR), .iOE1(n74138_1_y3), .iOE2(n74138_1_y3), .Q0(DOUT[0]), .Q1(DOUT[1]), .Q2(DOUT[2]), .Q3(DOUT[3]));
  _74173 u_74173_8 (
    .D0(DIN[4]), .D1(DIN[5]), .D2(DIN[6]), .D3(DIN[7]), .iE1(n74138_2_y3), .iE2(n74138_2_y3), .CP(CLK),
    .MR(CLEAR), .iOE1(n74138_1_y3), .iOE2(n74138_1_y3), .Q0(DOUT[4]), .Q1(DOUT[5]), .Q2(DOUT[6]), .Q3(DOUT[7]));
endmodule

// ALU
module _8_BIT_ALU (
  input  [7:0] Din,
  input  LOAD_AC,
  input  EN_ALU,
  input  CLK,
  input  CLEAR,
  input  [3:0] ALU_OP,
  input  LOGIC,
  output CO,
  output ZR,
  output [7:0] ALU_OUT
);

  wire n7408_1_y3, n7432_1_p5, n7432_1_p6, n7432_1_p11, n7432_1_p12, n74173_1_q0, n74173_1_q1, n74173_1_q2,
       n74173_1_q3, n74173_2_q0, n74173_2_q1, n74173_2_q2, n74173_2_q3, n74181_1_cn_4, n74181_2_cn_4,
       not_1_out, undriven;
  wire [7:0] n74181_1_f0;

  not not_1 (not_1_out, LOAD_AC);
  _74173 u_74173_1 (
    .D0(Din[0]), .D1(Din[1]), .D2(Din[2]), .D3(Din[3]), .iE1(not_1_out), .iE2(not_1_out), .CP(CLK),
    .MR(CLEAR), .iOE1(1'b0), .iOE2(1'b0), .Q0(n74173_1_q0), .Q1(n74173_1_q1), .Q2(n74173_1_q2),
    .Q3(n74173_1_q3));
  _74181 u_74181_1 (
    .S3(ALU_OP[3]), .S2(ALU_OP[2]), .S1(ALU_OP[1]), .S0(ALU_OP[0]), .B3(Din[3]), .A3(n74173_1_q3),
    .B2(Din[2]), .A2(n74173_1_q2), .B1(Din[1]), .A1(n74173_1_q1), .B0(Din[0]), .A0(n74173_1_q0), .M(LOGIC),
    .Cn(1'b1), .Cn_4(n74181_1_cn_4), .F3(n74181_1_f0[3]), .F2(n74181_1_f0[2]), .F1(n74181_1_f0[1]),
    .F0(n74181_1_f0[0]));  // open: G, P, A_B
  _74173 u_74173_2 (
    .D0(Din[4]), .D1(Din[5]), .D2(Din[6]), .D3(Din[7]), .iE1(not_1_out), .iE2(not_1_out), .CP(CLK),
    .MR(CLEAR), .iOE1(1'b0), .iOE2(1'b0), .Q0(n74173_2_q0), .Q1(n74173_2_q1), .Q2(n74173_2_q2),
    .Q3(n74173_2_q3));
  _74181 u_74181_2 (
    .S3(ALU_OP[3]), .S2(ALU_OP[2]), .S1(ALU_OP[1]), .S0(ALU_OP[0]), .B3(Din[7]), .A3(n74173_2_q3),
    .B2(Din[6]), .A2(n74173_2_q2), .B1(Din[5]), .A1(n74173_2_q1), .B0(Din[4]), .A0(n74173_2_q0), .M(LOGIC),
    .Cn(n74181_1_cn_4), .Cn_4(n74181_2_cn_4), .F3(n74181_1_f0[7]), .F2(n74181_1_f0[6]), .F1(n74181_1_f0[5]),
    .F0(n74181_1_f0[4]));  // open: G, P, A_B
  // _7432 7432_1: pin names not known; wires that end beside it: n74181_1_f0[0], n74181_1_f0[4], n74181_1_f0[1], n74181_1_f0[5], n7432_1_p5, n7432_1_p6, n74181_1_f0[2], n74181_1_f0[7], n74181_1_f0[3], n74181_1_f0[6], n7432_1_p11, n7432_1_p12
  assign ALU_OUT = EN_ALU ? n74181_1_f0 : 8'bz;  // Controlled_Buffer controlled_buffer_1
  _7408 u_7408_1 (
    .B1(n7432_1_p6), .Y1(n7432_1_p12), .A2(undriven), .A3(n7432_1_p5), .B3(n7432_1_p11), .Y3(n7408_1_y3),
    .A4(n7408_1_y3), .B4(undriven), .Y4(ZR));  // open: A1, B2, Y2
  not not_2 (CO, n74181_2_cn_4);
endmodule

// MEMORY
module MEMORY_UNIT (
  input  [7:0] DIN,
  input  CLK,
  input  MAR_LOAD,
  input  MEM_LOAD,
  input  MEM_EN,
  input  CLEAR,
  output [7:0] DOUT
);

  wire n7404_1_y1;
  wire [7:0] n74173_1_q0;

  _74173 u_74173_1 (
    .D0(DIN[0]), .D1(DIN[1]), .D2(DIN[2]), .D3(DIN[3]), .iE1(n7404_1_y1), .iE2(n7404_1_y1), .CP(CLK),
    .MR(CLEAR), .iOE1(1'b0), .iOE2(1'b0), .Q0(n74173_1_q0[0]), .Q1(n74173_1_q0[1]), .Q2(n74173_1_q0[2]),
    .Q3(n74173_1_q0[3]));
  _7404 u_7404_1 (.A1(MAR_LOAD), .Y1(n7404_1_y1));  // open: A2, Y2, A3, Y3, A4, Y5, A5, Y5_2, A6, Y6
  _74173 u_74173_2 (
    .D0(DIN[4]), .D1(DIN[5]), .D2(DIN[6]), .D3(DIN[7]), .iE1(n7404_1_y1), .iE2(n7404_1_y1), .CP(CLK),
    .MR(CLEAR), .iOE1(1'b0), .iOE2(1'b0), .Q0(n74173_1_q0[4]), .Q1(n74173_1_q0[5]), .Q2(n74173_1_q0[6]),
    .Q3(n74173_1_q0[7]));
  RAM ram_1 (.addr(n74173_1_q0), .data(DIN), .clk(CLK), .ld(MEM_LOAD));  // open: sel, clr

  assign DOUT = DIN;
endmodule

module PROGRAM_COUNTER (
  input  [7:0] DIN,
  input  CLK,
  input  CLEAR,
  input  PC_LOAD,
  input  PC_EN,
  input  PC_COUNT,
  output [7:0] DOUT
);

  wire n74161_1_tc;

  _74161 u_74161_1 (
    .D0(DIN[0]), .D1(DIN[1]), .D2(DIN[2]), .D3(DIN[3]), .CET(PC_COUNT), .CEP(PC_EN), .iPE(PC_LOAD),
    .iMR(CLEAR), .CP(CLK), .Q0(DOUT[0]), .Q1(DOUT[1]), .Q2(DOUT[2]), .Q3(DOUT[3]), .TC(n74161_1_tc));
  _74161 u_74161_2 (
    .D0(DIN[4]), .D1(DIN[5]), .D2(DIN[6]), .D3(DIN[7]), .CET(n74161_1_tc), .CEP(PC_EN), .iPE(PC_LOAD),
    .iMR(CLEAR), .CP(CLK), .Q0(DOUT[4]), .Q1(DOUT[5]), .Q2(DOUT[6]), .Q3(DOUT[7]));  // open: TC
endmodule
