// Logisim project ALU.circ as structural Verilog
module REGISTER_UNIT (
  input  D7,
  input  D6,
  input  D5,
  input  D4,
  input  D3,
  input  D2,
  input  D1,
  input  D0,
  input  CLK,
  input  LOAD,
  input  EN,
  input  R7,
  input  R6,
  input  R5,
  input  R4,
  input  CLEAR,
  input  R3,
  input  R2,
  input  R1,
  input  R0,
  output ALU7,
  output ALU6,
  output ALU5,
  output ALU4,
  output ALU3,
  output ALU2,
  output ALU1,
  output ALU0,
  output Q7,
  output Q6,
  output Q5,
  output Q4,
  output Q3,
  output Q2,
  output Q1,
  output Q0
);

  wire and_1_out, and_2_out, and_3_out, and_4_out, and_5_out, and_6_out, and_7_out, and_8_out, and_9_out,
       and_10_out, and_11_out, and_12_out, and_13_out, and_14_out, and_15_out, and_16_out, decoder_1_out0,
       decoder_1_out1, decoder_1_out2, decoder_1_out3, decoder_1_out4, decoder_1_out5, decoder_1_out6,
       decoder_2_out0, decoder_2_out1, decoder_2_out2, decoder_2_out3, decoder_2_out4, decoder_2_out5,
       decoder_2_out6, decoder_2_out7;
  wire [7:0] R0_q, R1_q, R2_q, R3_q, R4_q, R5_q, R6_q, R7_q;

  Register SI ();  // open: D, en, Q, clk, clr
  Decoder #(.select(4)) decoder_1 (
    .out0(decoder_1_out0), .out1(decoder_1_out1), .out2(decoder_1_out2), .out3(decoder_1_out3),
    .out4(decoder_1_out4), .out5(decoder_1_out5), .out6(decoder_1_out6), .sel({R3, R2, R1, R0}));  // open: out7, out8, out9, out10, out11, out12, out13, out14, out15, en
  Register SP ();  // open: D, en, Q, clk, clr
  Register DI ();  // open: D, en, Q, clk, clr
  Register BP ();  // open: D, en, Q, clk, clr
  Decoder #(.select(4)) decoder_2 (
    .out0(decoder_2_out0), .out1(decoder_2_out1), .out2(decoder_2_out2), .out3(decoder_2_out3),
    .out4(decoder_2_out4), .out5(decoder_2_out5), .out6(decoder_2_out6), .out7(decoder_2_out7),
    .sel({R7, R6, R5, R4}));  // open: out8, out9, out10, out11, out12, out13, out14, out15, en
  and and_1 (and_1_out, LOAD, decoder_2_out0);
  Register u_R0 (.D({D7, D6, D5, D4, D3, D2, D1, D0}), .en(and_1_out), .Q(R0_q), .clk(CLK), .clr(CLEAR));
  and and_2 (and_2_out, LOAD, decoder_2_out1);
  Register u_R1 (.D({D7, D6, D5, D4, D3, D2, D1, D0}), .en(and_2_out), .Q(R1_q), .clk(CLK), .clr(CLEAR));
  assign {ALU7, ALU6, ALU5, ALU4, ALU3, ALU2, ALU1, ALU0} = decoder_2_out0 ? R0_q : 8'bz;  // Controlled_Buffer controlled_buffer_1
  assign {Q7, Q6, Q5, Q4, Q3, Q2, Q1, Q0} = and_3_out ? R0_q : 8'bz;  // Controlled_Buffer controlled_buffer_2
  and and_3 (and_3_out, decoder_1_out0, EN);
  and and_4 (and_4_out, LOAD, decoder_2_out2);
  and and_5 (and_5_out, LOAD, decoder_2_out3);
  Register u_R2 (.D({D7, D6, D5, D4, D3, D2, D1, D0}), .en(and_4_out), .Q(R2_q), .clk(CLK), .clr(CLEAR));
  assign {ALU7, ALU6, ALU5, ALU4, ALU3, ALU2, ALU1, ALU0} = decoder_2_out1 ? R1_q : 8'bz;  // Controlled_Buffer controlled_buffer_3
  assign {Q7, Q6, Q5, Q4, Q3, Q2, Q1, Q0} = and_7_out ? R1_q : 8'bz;  // Controlled_Buffer controlled_buffer_4
  and and_6 (and_6_out, decoder_1_out2, EN);
  and and_7 (and_7_out, decoder_1_out1, EN);
  and and_8 (and_8_out, LOAD, decoder_2_out4);
  Register u_R3 (.D({D7, D6, D5, D4, D3, D2, D1, D0}), .en(and_5_out), .Q(R3_q), .clk(CLK), .clr(CLEAR));
  assign {ALU7, ALU6, ALU5, ALU4, ALU3, ALU2, ALU1, ALU0} = decoder_2_out2 ? R2_q : 8'bz;  // Controlled_Buffer controlled_buffer_5
  assign {Q7, Q6, Q5, Q4, Q3, Q2, Q1, Q0} = and_6_out ? R2_q : 8'bz;  // Controlled_Buffer controlled_buffer_6
  assign {Q7, Q6, Q5, Q4, Q3, Q2, Q1, Q0} = and_9_out ? R3_q : 8'bz;  // Controlled_Buffer controlled_buffer_7
  and and_9 (and_9_out, decoder_1_out3, EN);
  and and_10 (and_10_out, LOAD, decoder_2_out5);
  Register u_R4 (.D({D7, D6, D5, D4, D3, D2, D1, D0}), .en(and_8_out), .Q(R4_q), .clk(CLK), .clr(CLEAR));
  assign {ALU7, ALU6, ALU5, ALU4, ALU3, ALU2, ALU1, ALU0} = decoder_2_out3 ? R3_q : 8'bz;  // Controlled_Buffer controlled_buffer_8
  assign {Q7, Q6, Q5, Q4, Q3, Q2, Q1, Q0} = and_11_out ? R4_q : 8'bz;  // Controlled_Buffer controlled_buffer_9
  and and_11 (and_11_out, decoder_1_out4, EN);
  and and_12 (and_12_out, LOAD, decoder_2_out6);
  Register u_R5 (.D({D7, D6, D5, D4, D3, D2, D1, D0}), .en(and_10_out), .Q(R5_q), .clk(CLK), .clr(CLEAR));
  assign {ALU7, ALU6, ALU5, ALU4, ALU3, ALU2, ALU1, ALU0} = decoder_2_out5 ? R5_q : 8'bz;  // Controlled_Buffer controlled_buffer_10
  assign {ALU7, ALU6, ALU5, ALU4, ALU3, ALU2, ALU1, ALU0} = decoder_2_out4 ? R4_q : 8'bz;  // Controlled_Buffer controlled_buffer_11
  assign {Q7, Q6, Q5, Q4, Q3, Q2, Q1, Q0} = and_13_out ? R5_q : 8'bz;  // Controlled_Buffer controlled_buffer_12
  and and_13 (and_13_out, decoder_1_out5, EN);
  and and_14 (and_14_out, LOAD, decoder_2_out7);
  Register u_R7 (.D({D7, D6, D5, D4, D3, D2, D1, D0}), .en(and_14_out), .Q(R7_q), .clk(CLK), .clr(CLEAR));
  Register u_R6 (.D({D7, D6, D5, D4, D3, D2, D1, D0}), .en(and_12_out), .Q(R6_q), .clk(CLK), .clr(CLEAR));
  assign {ALU7, ALU6, ALU5, ALU4, ALU3, ALU2, ALU1, ALU0} = decoder_2_out6 ? R6_q : 8'bz;  // Controlled_Buffer controlled_buffer_13
  assign {Q7, Q6, Q5, Q4, Q3, Q2, Q1, Q0} = and_15_out ? R6_q : 8'bz;  // Controlled_Buffer controlled_buffer_14
  and and_15 (and_15_out, decoder_1_out6, EN);
  assign {ALU7, ALU6, ALU5, ALU4, ALU3, ALU2, ALU1, ALU0} = decoder_2_out7 ? R7_q : 8'bz;  // Controlled_Buffer controlled_buffer_15
  assign {Q7, Q6, Q5, Q4, Q3, Q2, Q1, Q0} = and_16_out ? R7_q : 8'bz;  // Controlled_Buffer controlled_buffer_16
  buf and_16 (and_16_out, EN);  // AND_Gate

  // Notes on the sheet:
  //   D2: pull=up
  //   D1: pull=up
  //   D0: pull=up
  //   D5: pull=up
  //   D3: pull=up
  //   D4: pull=up
  //   D7: pull=up
  //   D6: pull=up
endmodule
