// Logisim project microprocessor.circ as structural Verilog: 11 circuits, main circuit main
module main (
);

  wire and_1_out, clock_1_clk, clock_1_mode_2, clock_1_power_2, IR_q0, IR_q1, IR_q2, IR_q3, IR_q4, IR_q5,
       IR_q6, IR_q7, MODE_out, n8_bit_bus_memory_1_q0, n8_bit_bus_memory_1_q1, n8_bit_bus_memory_1_q2,
       n8_bit_bus_memory_1_q3, n8_bit_bus_memory_1_q4, n8_bit_bus_memory_1_q5, n8_bit_bus_memory_1_q6,
       n8_bit_bus_memory_1_q7, n8_bit_register_1_q0, n8_bit_register_1_q1, n8_bit_register_1_q2,
       n8_bit_register_1_q3, n8_bit_register_1_q4, n8_bit_register_1_q5, n8_bit_register_1_q6,
       n8_bit_register_1_q7, not_1_out, POWER_out, program_decoder_1_ae, program_decoder_1_al,
       program_decoder_1_alue, program_decoder_1_be, program_decoder_1_bl, program_decoder_1_hlt,
       program_decoder_1_i2e, program_decoder_1_i2l, program_decoder_1_in, program_decoder_1_irl,
       program_decoder_1_mal, program_decoder_1_mee, program_decoder_1_mel, program_decoder_1_out,
       program_decoder_1_pcc, program_decoder_1_pce, program_decoder_1_pcl, program_decoder_1_sub, RESET_out,
       STEP_out;
  wire [2:0] program_decoder_1_stage;
  wire [3:0] A_q0, A_q4, B_q0, B_q4, n8_bit_controlled_buffer_1_out_13, n8_bit_controlled_buffer_1_out_17,
       PC_q0, PC_q4;
  wire [6:0] keyboard_1_data;
  wire [7:0] MAR_q0, OUTPUT_q0;

  Button POWER (.out(POWER_out));
  Button MODE (.out(MODE_out));
  Button STEP (.out(STEP_out));
  Button RESET (.out(RESET_out));
  Hex_Digit_Display hex_digit_display_1 (.value({1'b0, program_decoder_1_stage}));  // open: dp
  LED led_1 (.in(clock_1_mode_2));
  LED led_2 (.in(clock_1_power_2));
  CLOCK clock_1 (
    .POWER(POWER_out), .MODE(MODE_out), .STEP(STEP_out), .POWER_2(clock_1_power_2), .MODE_2(clock_1_mode_2),
    .CLK(clock_1_clk));
  not not_1 (not_1_out, program_decoder_1_hlt);
  Hex_Digit_Display hex_digit_display_2 (.value(PC_q4));  // open: dp
  and and_1 (and_1_out, clock_1_clk, not_1_out);
  Hex_Digit_Display hex_digit_display_3 (.value(PC_q0));  // open: dp
  _8_Bit_Register IR (
    .CLK(and_1_out), .LOAD(program_decoder_1_irl), .CLR(RESET_out),
    .D0(n8_bit_controlled_buffer_1_out_17[0]), .D1(n8_bit_controlled_buffer_1_out_17[1]),
    .D2(n8_bit_controlled_buffer_1_out_17[2]), .D3(n8_bit_controlled_buffer_1_out_17[3]),
    .D4(n8_bit_controlled_buffer_1_out_13[0]), .D5(n8_bit_controlled_buffer_1_out_13[1]),
    .D6(n8_bit_controlled_buffer_1_out_13[2]), .D7(n8_bit_controlled_buffer_1_out_13[3]), .Q0(IR_q0),
    .Q1(IR_q1), .Q2(IR_q2), .Q3(IR_q3), .Q4(IR_q4), .Q5(IR_q5), .Q6(IR_q6), .Q7(IR_q7));
  PROGRAM_COUNTER PC (
    .CLK(and_1_out), .LOAD(program_decoder_1_pcl), .CLR(RESET_out), .INC(program_decoder_1_pcc),
    .D0(n8_bit_controlled_buffer_1_out_17[0]), .D1(n8_bit_controlled_buffer_1_out_17[1]),
    .D2(n8_bit_controlled_buffer_1_out_17[2]), .D3(n8_bit_controlled_buffer_1_out_17[3]),
    .D4(n8_bit_controlled_buffer_1_out_13[0]), .D5(n8_bit_controlled_buffer_1_out_13[1]),
    .D6(n8_bit_controlled_buffer_1_out_13[2]), .D7(n8_bit_controlled_buffer_1_out_13[3]), .Q0(PC_q0[0]),
    .Q1(PC_q0[1]), .Q2(PC_q0[2]), .Q3(PC_q0[3]), .Q4(PC_q4[0]), .Q5(PC_q4[1]), .Q6(PC_q4[2]), .Q7(PC_q4[3]));
  _8_Bit_Register MAR (
    .CLK(and_1_out), .LOAD(program_decoder_1_mal), .CLR(RESET_out),
    .D0(n8_bit_controlled_buffer_1_out_17[0]), .D1(n8_bit_controlled_buffer_1_out_17[1]),
    .D2(n8_bit_controlled_buffer_1_out_17[2]), .D3(n8_bit_controlled_buffer_1_out_17[3]),
    .D4(n8_bit_controlled_buffer_1_out_13[0]), .D5(n8_bit_controlled_buffer_1_out_13[1]),
    .D6(n8_bit_controlled_buffer_1_out_13[2]), .D7(n8_bit_controlled_buffer_1_out_13[3]), .Q0(MAR_q0[0]),
    .Q1(MAR_q0[1]), .Q2(MAR_q0[2]), .Q3(MAR_q0[3]), .Q4(MAR_q0[4]), .Q5(MAR_q0[5]), .Q6(MAR_q0[6]),
    .Q7(MAR_q0[7]));
  _8_Bit_Bus_Memory u_8_bit_bus_memory_1 (
    .CLK(and_1_out), .LOAD(program_decoder_1_mel), .D0(n8_bit_controlled_buffer_1_out_17[0]),
    .D1(n8_bit_controlled_buffer_1_out_17[1]), .D2(n8_bit_controlled_buffer_1_out_17[2]),
    .D3(n8_bit_controlled_buffer_1_out_17[3]), .D4(n8_bit_controlled_buffer_1_out_13[0]),
    .D5(n8_bit_controlled_buffer_1_out_13[1]), .D6(n8_bit_controlled_buffer_1_out_13[2]),
    .D7(n8_bit_controlled_buffer_1_out_13[3]), .Q0(n8_bit_bus_memory_1_q0), .Q1(n8_bit_bus_memory_1_q1),
    .Q2(n8_bit_bus_memory_1_q2), .Q3(n8_bit_bus_memory_1_q3), .Q4(n8_bit_bus_memory_1_q4),
    .Q5(n8_bit_bus_memory_1_q5), .Q6(n8_bit_bus_memory_1_q6), .Q7(n8_bit_bus_memory_1_q7), .A0(MAR_q0[0]),
    .A1(MAR_q0[1]), .A2(MAR_q0[2]), .A3(MAR_q0[3]), .A4(MAR_q0[4]), .A5(MAR_q0[5]), .A6(MAR_q0[6]),
    .A7(MAR_q0[7]));  // open: RESET
  _8_Bit_Controlled_Buffer u_8_bit_controlled_buffer_1 (
    .in_1(n8_bit_bus_memory_1_q7), .in_2(n8_bit_bus_memory_1_q6), .in_3(n8_bit_bus_memory_1_q5),
    .in_4(n8_bit_bus_memory_1_q4), .in_5(n8_bit_bus_memory_1_q3), .in_6(n8_bit_bus_memory_1_q2),
    .in_7(n8_bit_bus_memory_1_q1), .in_8(n8_bit_bus_memory_1_q0), .EN(program_decoder_1_mee),
    .out_10(n8_bit_controlled_buffer_1_out_13[3]), .out_11(n8_bit_controlled_buffer_1_out_13[2]),
    .out_12(n8_bit_controlled_buffer_1_out_13[1]), .out_13(n8_bit_controlled_buffer_1_out_13[0]),
    .out_14(n8_bit_controlled_buffer_1_out_17[3]), .out_15(n8_bit_controlled_buffer_1_out_17[2]),
    .out_16(n8_bit_controlled_buffer_1_out_17[1]), .out_17(n8_bit_controlled_buffer_1_out_17[0]));
  _8_Bit_Register u_8_bit_register_1 (
    .CLK(and_1_out), .LOAD(program_decoder_1_i2l), .CLR(RESET_out),
    .D0(n8_bit_controlled_buffer_1_out_17[0]), .D1(n8_bit_controlled_buffer_1_out_17[1]),
    .D2(n8_bit_controlled_buffer_1_out_17[2]), .D3(n8_bit_controlled_buffer_1_out_17[3]),
    .D4(n8_bit_controlled_buffer_1_out_13[0]), .D5(n8_bit_controlled_buffer_1_out_13[1]),
    .D6(n8_bit_controlled_buffer_1_out_13[2]), .D7(n8_bit_controlled_buffer_1_out_13[3]),
    .Q0(n8_bit_register_1_q0), .Q1(n8_bit_register_1_q1), .Q2(n8_bit_register_1_q2),
    .Q3(n8_bit_register_1_q3), .Q4(n8_bit_register_1_q4), .Q5(n8_bit_register_1_q5),
    .Q6(n8_bit_register_1_q6), .Q7(n8_bit_register_1_q7));
  PROGRAM_DECODER program_decoder_1 (
    .CLK(and_1_out), .RESET(RESET_out), .R0(IR_q0), .R1(IR_q1), .R2(IR_q2), .R3(IR_q3), .D0(IR_q4),
    .D1(IR_q5), .D2(IR_q6), .D3(IR_q7), .STAGE(program_decoder_1_stage), .PCE(program_decoder_1_pce),
    .PCL(program_decoder_1_pcl), .MAL(program_decoder_1_mal), .MEE(program_decoder_1_mee),
    .MEL(program_decoder_1_mel), .IRL(program_decoder_1_irl), .I2L(program_decoder_1_i2l),
    .I2E(program_decoder_1_i2e), .PCC(program_decoder_1_pcc), .AL(program_decoder_1_al),
    .AE(program_decoder_1_ae), .BL(program_decoder_1_bl), .BE(program_decoder_1_be),
    .ALUE(program_decoder_1_alue), .SUB(program_decoder_1_sub), .HLT(program_decoder_1_hlt),
    .IN(program_decoder_1_in), .OUT(program_decoder_1_out));
  _8_Bit_Controlled_Buffer u_8_bit_controlled_buffer_2 (
    .in_1(n8_bit_register_1_q7), .in_2(n8_bit_register_1_q6), .in_3(n8_bit_register_1_q5),
    .in_4(n8_bit_register_1_q4), .in_5(n8_bit_register_1_q3), .in_6(n8_bit_register_1_q2),
    .in_7(n8_bit_register_1_q1), .in_8(n8_bit_register_1_q0), .EN(program_decoder_1_i2e),
    .out_10(n8_bit_controlled_buffer_1_out_13[3]), .out_11(n8_bit_controlled_buffer_1_out_13[2]),
    .out_12(n8_bit_controlled_buffer_1_out_13[1]), .out_13(n8_bit_controlled_buffer_1_out_13[0]),
    .out_14(n8_bit_controlled_buffer_1_out_17[3]), .out_15(n8_bit_controlled_buffer_1_out_17[2]),
    .out_16(n8_bit_controlled_buffer_1_out_17[1]), .out_17(n8_bit_controlled_buffer_1_out_17[0]));
  _8_Bit_Controlled_Buffer u_8_bit_controlled_buffer_3 (
    .in_1(PC_q4[3]), .in_2(PC_q4[2]), .in_3(PC_q4[1]), .in_4(PC_q4[0]), .in_5(PC_q0[3]), .in_6(PC_q0[2]),
    .in_7(PC_q0[1]), .in_8(PC_q0[0]), .EN(program_decoder_1_pce),
    .out_10(n8_bit_controlled_buffer_1_out_13[3]), .out_11(n8_bit_controlled_buffer_1_out_13[2]),
    .out_12(n8_bit_controlled_buffer_1_out_13[1]), .out_13(n8_bit_controlled_buffer_1_out_13[0]),
    .out_14(n8_bit_controlled_buffer_1_out_17[3]), .out_15(n8_bit_controlled_buffer_1_out_17[2]),
    .out_16(n8_bit_controlled_buffer_1_out_17[1]), .out_17(n8_bit_controlled_buffer_1_out_17[0]));
  _8_Bit_Register OUTPUT (
    .CLK(and_1_out), .LOAD(program_decoder_1_out), .CLR(RESET_out),
    .D0(n8_bit_controlled_buffer_1_out_17[0]), .D1(n8_bit_controlled_buffer_1_out_17[1]),
    .D2(n8_bit_controlled_buffer_1_out_17[2]), .D3(n8_bit_controlled_buffer_1_out_17[3]),
    .D4(n8_bit_controlled_buffer_1_out_13[0]), .D5(n8_bit_controlled_buffer_1_out_13[1]),
    .D6(n8_bit_controlled_buffer_1_out_13[2]), .D7(n8_bit_controlled_buffer_1_out_13[3]), .Q0(OUTPUT_q0[0]),
    .Q1(OUTPUT_q0[1]), .Q2(OUTPUT_q0[2]), .Q3(OUTPUT_q0[3]), .Q4(OUTPUT_q0[4]), .Q5(OUTPUT_q0[5]),
    .Q6(OUTPUT_q0[6]), .Q7(OUTPUT_q0[7]));
  Hex_Digit_Display hex_digit_display_4 (.value(MAR_q0[7:4]));  // open: dp
  Hex_Digit_Display hex_digit_display_5 (.value(MAR_q0[3:0]));  // open: dp
  Hex_Digit_Display hex_digit_display_6 (.value(OUTPUT_q0[7:4]));  // open: dp
  Hex_Digit_Display hex_digit_display_7 (.value(n8_bit_controlled_buffer_1_out_13));  // open: dp
  Keyboard keyboard_1 (
    .clk(and_1_out), .re(program_decoder_1_in), .clr(RESET_out), .data(keyboard_1_data));  // open: avail
  Hex_Digit_Display hex_digit_display_8 (.value(OUTPUT_q0[3:0]));  // open: dp
  Hex_Digit_Display hex_digit_display_9 (.value(n8_bit_controlled_buffer_1_out_17));  // open: dp
  _8_Bit_Register A (
    .CLK(and_1_out), .LOAD(program_decoder_1_al), .CLR(RESET_out), .D0(n8_bit_controlled_buffer_1_out_17[0]),
    .D1(n8_bit_controlled_buffer_1_out_17[1]), .D2(n8_bit_controlled_buffer_1_out_17[2]),
    .D3(n8_bit_controlled_buffer_1_out_17[3]), .D4(n8_bit_controlled_buffer_1_out_13[0]),
    .D5(n8_bit_controlled_buffer_1_out_13[1]), .D6(n8_bit_controlled_buffer_1_out_13[2]),
    .D7(n8_bit_controlled_buffer_1_out_13[3]), .Q0(A_q0[0]), .Q1(A_q0[1]), .Q2(A_q0[2]), .Q3(A_q0[3]),
    .Q4(A_q4[0]), .Q5(A_q4[1]), .Q6(A_q4[2]), .Q7(A_q4[3]));
  _8_Bit_Controlled_Buffer u_8_bit_controlled_buffer_4 (
    .in_1(A_q4[3]), .in_2(A_q4[2]), .in_3(A_q4[1]), .in_4(A_q4[0]), .in_5(A_q0[3]), .in_6(A_q0[2]),
    .in_7(A_q0[1]), .in_8(A_q0[0]), .EN(program_decoder_1_ae), .out_10(n8_bit_controlled_buffer_1_out_13[3]),
    .out_11(n8_bit_controlled_buffer_1_out_13[2]), .out_12(n8_bit_controlled_buffer_1_out_13[1]),
    .out_13(n8_bit_controlled_buffer_1_out_13[0]), .out_14(n8_bit_controlled_buffer_1_out_17[3]),
    .out_15(n8_bit_controlled_buffer_1_out_17[2]), .out_16(n8_bit_controlled_buffer_1_out_17[1]),
    .out_17(n8_bit_controlled_buffer_1_out_17[0]));
  _8_Bit_Controlled_Buffer u_8_bit_controlled_buffer_5 (
    .in_1(B_q4[3]), .in_2(B_q4[2]), .in_3(B_q4[1]), .in_4(B_q4[0]), .in_5(B_q0[3]), .in_6(B_q0[2]),
    .in_7(B_q0[1]), .in_8(B_q0[0]), .EN(program_decoder_1_be), .out_10(n8_bit_controlled_buffer_1_out_13[3]),
    .out_11(n8_bit_controlled_buffer_1_out_13[2]), .out_12(n8_bit_controlled_buffer_1_out_13[1]),
    .out_13(n8_bit_controlled_buffer_1_out_13[0]), .out_14(n8_bit_controlled_buffer_1_out_17[3]),
    .out_15(n8_bit_controlled_buffer_1_out_17[2]), .out_16(n8_bit_controlled_buffer_1_out_17[1]),
    .out_17(n8_bit_controlled_buffer_1_out_17[0]));
  assign {n8_bit_controlled_buffer_1_out_13, n8_bit_controlled_buffer_1_out_17} = program_decoder_1_in ? {1'b0, keyboard_1_data} : 8'bz;  // Controlled_Buffer controlled_buffer_1
  ALU alu_1 (
    .S0(n8_bit_controlled_buffer_1_out_17[0]), .S1(n8_bit_controlled_buffer_1_out_17[1]),
    .S2(n8_bit_controlled_buffer_1_out_17[2]), .S3(n8_bit_controlled_buffer_1_out_17[3]),
    .S4(n8_bit_controlled_buffer_1_out_13[0]), .S5(n8_bit_controlled_buffer_1_out_13[1]),
    .S6(n8_bit_controlled_buffer_1_out_13[2]), .S7(n8_bit_controlled_buffer_1_out_13[3]), .A0(A_q0[0]),
    .A1(A_q0[1]), .A2(A_q0[2]), .A3(A_q0[3]), .A4(A_q4[0]), .A5(A_q4[1]), .A6(A_q4[2]), .A7(A_q4[3]),
    .B7(B_q4[3]), .B6(B_q4[2]), .B5(B_q4[1]), .B4(B_q4[0]), .B3(B_q0[3]), .B2(B_q0[2]), .B1(B_q0[1]),
    .B0(B_q0[0]), .EN(program_decoder_1_alue), .SUB(program_decoder_1_sub));  // open: CO
  _8_Bit_Register B (
    .CLK(and_1_out), .LOAD(program_decoder_1_bl), .CLR(RESET_out), .D0(n8_bit_controlled_buffer_1_out_17[0]),
    .D1(n8_bit_controlled_buffer_1_out_17[1]), .D2(n8_bit_controlled_buffer_1_out_17[2]),
    .D3(n8_bit_controlled_buffer_1_out_17[3]), .D4(n8_bit_controlled_buffer_1_out_13[0]),
    .D5(n8_bit_controlled_buffer_1_out_13[1]), .D6(n8_bit_controlled_buffer_1_out_13[2]),
    .D7(n8_bit_controlled_buffer_1_out_13[3]), .Q0(B_q0[0]), .Q1(B_q0[1]), .Q2(B_q0[2]), .Q3(B_q0[3]),
    .Q4(B_q4[0]), .Q5(B_q4[1]), .Q6(B_q4[2]), .Q7(B_q4[3]));
  Hex_Digit_Display hex_digit_display_10 (.value(A_q4));  // open: dp
  Hex_Digit_Display hex_digit_display_11 (.value(A_q0));  // open: dp
  Hex_Digit_Display hex_digit_display_12 (.value(B_q4));  // open: dp
  Hex_Digit_Display hex_digit_display_13 (.value(B_q0));  // open: dp
endmodule

module _1_Bit_Adder_w__Carry (
  input  A,
  input  CIN,
  input  B,
  output S,
  output CO
);

  wire and_1_out, and_2_out, xor_1_out;

  xor xor_1 (xor_1_out, A, B);
  xor xor_2 (S, xor_1_out, CIN);
  and and_1 (and_1_out, xor_1_out, CIN);
  and and_2 (and_2_out, A, B);
  or or_1 (CO, and_1_out, and_2_out);

  // Notes on the sheet:
  //   CIN: pull=down
endmodule

module _4_Bit_Adder_w__Carry (
  input  A0,
  input  A1,
  input  A2,
  input  A3,
  input  CI,
  input  B0,
  input  B1,
  input  B2,
  input  B3,
  output S0,
  output CO,
  output S1,
  output S2,
  output S3
);

  wire n1_bit_adder_w_carry_1_co, n1_bit_adder_w_carry_2_co, n1_bit_adder_w_carry_3_co;

  _1_Bit_Adder_w__Carry u_1_bit_adder_w_carry_1 (.S(S0), .A(A0), .B(B0), .CO(n1_bit_adder_w_carry_1_co), .CIN(CI));
  _1_Bit_Adder_w__Carry u_1_bit_adder_w_carry_2 (
    .S(S1), .A(A1), .B(B1), .CO(n1_bit_adder_w_carry_2_co), .CIN(n1_bit_adder_w_carry_1_co));
  _1_Bit_Adder_w__Carry u_1_bit_adder_w_carry_3 (
    .S(S2), .A(A2), .B(B2), .CO(n1_bit_adder_w_carry_3_co), .CIN(n1_bit_adder_w_carry_2_co));
  _1_Bit_Adder_w__Carry u_1_bit_adder_w_carry_4 (.S(S3), .A(A3), .B(B3), .CO(CO), .CIN(n1_bit_adder_w_carry_3_co));

  // Notes on the sheet:
  //   CI: pull=down
  //   B0: pull=up
  //   B1: pull=up
  //   B2: pull=up
  //   B3: pull=up
  //   A3: pull=up
  //   A1: pull=up
  //   A0: pull=up
  //   A2: pull=up
endmodule

module _8_Bit_Inverter (
  input  INV,
  input  D0,
  input  D1,
  input  D2,
  input  D3,
  input  D4,
  input  D5,
  input  D6,
  input  D7,
  output Q0,
  output Q1,
  output Q2,
  output Q3,
  output Q4,
  output Q5,
  output Q6,
  output Q7
);

  xor xor_1 (Q0, D0, INV);
  xor xor_2 (Q1, D1, INV);
  xor xor_3 (Q2, D2, INV);
  xor xor_4 (Q4, D4, INV);
  xor xor_5 (Q5, D5, INV);
  xor xor_6 (Q3, D3, INV);
  xor xor_7 (Q7, D7, INV);
  xor xor_8 (Q6, D6, INV);

  // Notes on the sheet:
  //   INV: pull=down
endmodule

module ALU (
  input  A0,
  input  A1,
  input  A2,
  input  A3,
  input  A4,
  input  A5,
  input  A6,
  input  A7,
  input  EN,
  input  SUB,
  input  B7,
  input  B6,
  input  B5,
  input  B4,
  input  B3,
  input  B2,
  input  B1,
  input  B0,
  output S0,
  output S1,
  output S2,
  output S3,
  output CO,
  output S4,
  output S5,
  output S6,
  output S7
);

  wire n4_bit_adder_w_carry_1_co, n4_bit_adder_w_carry_1_s0, n4_bit_adder_w_carry_1_s1,
       n4_bit_adder_w_carry_1_s2, n4_bit_adder_w_carry_1_s3, n4_bit_adder_w_carry_2_s0,
       n4_bit_adder_w_carry_2_s1, n4_bit_adder_w_carry_2_s2, n4_bit_adder_w_carry_2_s3, n8_bit_inverter_1_q0,
       n8_bit_inverter_1_q1, n8_bit_inverter_1_q2, n8_bit_inverter_1_q3, n8_bit_inverter_1_q4,
       n8_bit_inverter_1_q5, n8_bit_inverter_1_q6, n8_bit_inverter_1_q7;

  _8_Bit_Controlled_Buffer u_8_bit_controlled_buffer_1 (
    .in_1(n4_bit_adder_w_carry_2_s3), .in_2(n4_bit_adder_w_carry_2_s2), .in_3(n4_bit_adder_w_carry_2_s1),
    .in_4(n4_bit_adder_w_carry_2_s0), .in_5(n4_bit_adder_w_carry_1_s3), .in_6(n4_bit_adder_w_carry_1_s2),
    .in_7(n4_bit_adder_w_carry_1_s1), .in_8(n4_bit_adder_w_carry_1_s0), .EN(EN), .out_10(S7), .out_11(S6),
    .out_12(S5), .out_13(S4), .out_14(S3), .out_15(S2), .out_16(S1), .out_17(S0));
  _4_Bit_Adder_w__Carry u_4_bit_adder_w_carry_1 (
    .S0(n4_bit_adder_w_carry_1_s0), .S1(n4_bit_adder_w_carry_1_s1), .S2(n4_bit_adder_w_carry_1_s2),
    .S3(n4_bit_adder_w_carry_1_s3), .A0(A0), .A1(A1), .A2(A2), .A3(A3), .B0(n8_bit_inverter_1_q0),
    .B1(n8_bit_inverter_1_q1), .B2(n8_bit_inverter_1_q2), .B3(n8_bit_inverter_1_q3),
    .CO(n4_bit_adder_w_carry_1_co), .CI(SUB));
  _4_Bit_Adder_w__Carry u_4_bit_adder_w_carry_2 (
    .S0(n4_bit_adder_w_carry_2_s0), .S1(n4_bit_adder_w_carry_2_s1), .S2(n4_bit_adder_w_carry_2_s2),
    .S3(n4_bit_adder_w_carry_2_s3), .A0(A4), .A1(A5), .A2(A6), .A3(A7), .B0(n8_bit_inverter_1_q4),
    .B1(n8_bit_inverter_1_q5), .B2(n8_bit_inverter_1_q6), .B3(n8_bit_inverter_1_q7), .CO(CO),
    .CI(n4_bit_adder_w_carry_1_co));
  _8_Bit_Inverter u_8_bit_inverter_1 (
    .Q0(n8_bit_inverter_1_q0), .Q1(n8_bit_inverter_1_q1), .Q2(n8_bit_inverter_1_q2),
    .Q3(n8_bit_inverter_1_q3), .Q4(n8_bit_inverter_1_q4), .Q5(n8_bit_inverter_1_q5),
    .Q6(n8_bit_inverter_1_q6), .Q7(n8_bit_inverter_1_q7), .D0(B0), .D1(B1), .D2(B2), .D3(B3), .D4(B4),
    .D5(B5), .D6(B6), .D7(B7), .INV(SUB));

  // Notes on the sheet:
  //   A7: pull=up
  //   A0: pull=up
  //   A2: pull=up
  //   SUB: pull=up
  //   A6: pull=up
  //   A5: pull=up
  //   EN: pull=up
  //   A3: pull=up
  //   A1: pull=up
endmodule

// BUFFER
module _8_Bit_Controlled_Buffer (
  input  in_1,
  input  in_2,
  input  in_3,
  input  in_4,
  input  in_5,
  input  in_6,
  input  in_7,
  input  in_8,
  input  EN,
  output out_10,
  output out_11,
  output out_12,
  output out_13,
  output out_14,
  output out_15,
  output out_16,
  output out_17
);

  assign out_10 = EN ? in_1 : 1'bz;  // Controlled_Buffer controlled_buffer_1
  assign out_11 = EN ? in_2 : 1'bz;  // Controlled_Buffer controlled_buffer_2
  assign out_12 = EN ? in_3 : 1'bz;  // Controlled_Buffer controlled_buffer_3
  assign out_13 = EN ? in_4 : 1'bz;  // Controlled_Buffer controlled_buffer_4
  assign out_14 = EN ? in_5 : 1'bz;  // Controlled_Buffer controlled_buffer_5
  assign out_15 = EN ? in_6 : 1'bz;  // Controlled_Buffer controlled_buffer_6
  assign out_16 = EN ? in_7 : 1'bz;  // Controlled_Buffer controlled_buffer_7
  assign out_17 = EN ? in_8 : 1'bz;  // Controlled_Buffer controlled_buffer_8
endmodule

// REGISTER
module _8_Bit_Register (
  input  D0,
  input  D1,
  input  D2,
  input  D3,
  input  D4,
  input  D5,
  input  D6,
  input  D7,
  input  CLK,
  input  LOAD,
  input  CLR,
  output Q0,
  output Q1,
  output Q2,
  output Q3,
  output Q4,
  output Q5,
  output Q6,
  output Q7
);

  Register register_1 (
    .D({D7, D6, D5, D4, D3, D2, D1, D0}), .en(LOAD), .Q({Q7, Q6, Q5, Q4, Q3, Q2, Q1, Q0}), .clk(CLK),
    .clr(CLR));

  // Notes on the sheet:
  //   D1: pull=up
  //   D4: pull=up
  //   D6: pull=up
  //   D0: pull=up
  //   D5: pull=up
  //   D2: pull=up
  //   D3: pull=up
  //   D7: pull=up
endmodule

module CLOCK (
  input  POWER,
  input  MODE,
  input  STEP,
  output POWER_2,
  output MODE_2,
  output CLK
);

  wire clock_1_out, controlled_buffer_1_out, not_1_out;

  Clock clock_1 (.out(clock_1_out));
  assign controlled_buffer_1_out = not_1_out ? clock_1_out : 1'bz;  // Controlled_Buffer controlled_buffer_1
  Counter #(.width(1), .max('h1)) counter_1 (.count(POWER), .Q(POWER_2), .clk(POWER));  // open: load, D, carry, clr
  not not_1 (not_1_out, MODE_2);
  Counter #(.width(1), .max('h1)) counter_2 (.count(MODE), .Q(MODE_2), .clk(MODE));  // open: load, D, carry, clr
  assign controlled_buffer_1_out = MODE_2 ? STEP : 1'bz;  // Controlled_Buffer controlled_buffer_2
  and and_1 (CLK, POWER_2, controlled_buffer_1_out);
endmodule

// RAM
module _8_Bit_Bus_Memory (
  input  D0,
  input  D1,
  input  D2,
  input  D3,
  input  D4,
  input  D5,
  input  D6,
  input  D7,
  input  A0,
  input  A1,
  input  A2,
  input  A3,
  input  A4,
  input  A5,
  input  CLK,
  input  A6,
  input  RESET,
  input  A7,
  input  LOAD,
  output Q0,
  output Q1,
  output Q2,
  output Q3,
  output Q4,
  output Q5,
  output Q6,
  output Q7
);

  RAM #(.bus("separate")) ram_1 (
    .addr({A7, A6, A5, A4, A3, A2, A1, A0}), .din({D7, D6, D5, D4, D3, D2, D1, D0}),
    .data({Q7, Q6, Q5, Q4, Q3, Q2, Q1, Q0}), .str(LOAD), .sel(1'b1), .clk(CLK), .ld(1'b1), .clr(RESET));

  // Notes on the sheet:
  //   A6: pull=up
  //   A4: pull=up
  //   A3: pull=up
  //   A2: pull=up
  //   A1: pull=up
  //   A5: pull=up
  //   A7: pull=up
  //   A0: pull=up
endmodule

module PROGRAM_COUNTER (
  input  D0,
  input  D1,
  input  D2,
  input  D3,
  input  D4,
  input  D5,
  input  D6,
  input  D7,
  input  CLK,
  input  LOAD,
  input  CLR,
  input  INC,
  output Q0,
  output Q1,
  output Q2,
  output Q3,
  output Q4,
  output Q5,
  output Q6,
  output Q7
);

  Counter counter_1 (
    .load(LOAD), .D({D7, D6, D5, D4, D3, D2, D1, D0}), .count(INC), .Q({Q7, Q6, Q5, Q4, Q3, Q2, Q1, Q0}),
    .clk(CLK), .clr(CLR));  // open: carry

  // Notes on the sheet:
  //   D0: pull=up
  //   D3: pull=up
  //   D6: pull=up
  //   D2: pull=up
  //   D1: pull=up
  //   D4: pull=up
  //   D7: pull=up
  //   D5: pull=up
endmodule

// DECODER
module PROGRAM_DECODER (
  input  R0,
  input  R1,
  input  R2,
  input  R3,
  input  D0,
  input  D1,
  input  D2,
  input  D3,
  input  CLK,
  input  RESET,
  output PCE,
  output PCL,
  output MAL,
  output MEE,
  output MEL,
  output IRL,
  output I2L,
  output I2E,
  output PCC,
  output AL,
  output AE,
  output BL,
  output [2:0] STAGE,
  output BE,
  output ALUE,
  output SUB,
  output HLT,
  output IN,
  output OUT
);

  wire and_1_out, not_1_out, or_1_out;
  wire [19:16] rom_1_data;

  not not_1 (not_1_out, CLK);
  or or_1 (or_1_out, RESET, and_1_out);
  and and_1 (and_1_out, CLK, rom_1_data[16]);
  Counter #(.width(3), .max('h7)) u_STAGE (
    .count(1'b1), .Q(STAGE), .clk(not_1_out), .clr(or_1_out));  // open: load, D, carry
  Decoder #(.select(3)) decoder_1 (.sel(STAGE));  // open: out0, out1, out2, out3, out4, out5, out6, out7, en
  ROM #(.addrWidth(16), .dataWidth(20)) rom_1 (
    .addr({{5{1'b0}}, D3, D2, D1, D0, R3, R2, R1, R0, STAGE}),
    .data({rom_1_data[19], OUT, IN, rom_1_data[16], HLT, SUB, ALUE, BE, BL, AE, AL, PCC, I2E, I2L, IRL, MEL, MEE, MAL, PCL, PCE}));  // open: sel

  // Notes on the sheet:
  //   contents of rom_1 (hex, n*v repeats v):
  //   5 128 6*0 5 128 0 0 2200 10000 0 0 5 128 0 0 6200 10000 0 0 5 128 0 0 20200 10000 0 0 5 128 0 0
  //   40400 10000 0 0 5 128 6*0 5 128 5 148 4*0 5 128 5 148 4*0 5 128 5 148 4*0 5 128 6*0 5 128 6*0 5 128
  //   6*0 5 128 5 148 4*0 5 128 6*0 5 128 6*0 5 128 6*0 5 128 6*0 5 128 6*0 5 128 5 148 4*0 5 128 5 148
  //   280 10000 0 0 5 128 6*0 5 128 6*0 5 128 5 148 4*0 5 128 5 148 880 10000 0 0 5 128 5 148 4*0 5 128
  //   6*0 5 128 6*0 5 128 6*0 5 128 5 148 4*0 5 128 6*0 5 128 6*0 5 128 6*0 5 128 6*0 5 128 6*0 5 128 5
  //   148 4*0 5 128 5 148 4*0 5 128 6*0 5 128 6*0 5 128 5 148 4*0 5 128 5 148 4*0 5 128 5 148 4*0 5 128
  //   6*0 5 128 6*0 5 128 6*0 5 128 5 148 4*0 5 128 6*0 5 128 6*0 5 128 6*0 5 128 6*0 5 128 6*0 5 128 5
  //   148 4*0 5 128 5 148 4*0 5 128 6*0 5 128 6*0 5 128 5 148 4*0 5 128 5 148 4*0 5 128 5 148 4*0 5 128
  //   6*0 5 128 6*0 5 128 6*0 5 128 5 148 4*0 5 128 6*0 5 128 6*0 5 128 6*0 5 128 8000 5*0 5 128 6*0 5 128
  //   5 148 4*0 5 128 5 148 4*0 5 128 6*0 5 128 6*0 5 128 5 148 4*0 5 128 5 148 4*0 5 128 5 148 4*0 5 128
  //   6*0 5 128 6*0 5 128 6*0 5 128 5 148 4*0 5 128 6*0 5 128 6*0 5 128 6*0 5 128 5 148 82 10000 0 0 5 128
  //   6*0 5 128 5 148 4*0 5 128 5 148 4*0 5 128 6*0 5 128 6*0 5 128 5 148 4*0 5 128 5 148 4*0 5 128 5 148
  //   4*0 5 128 6*0 5 128 6*0 5 128 6*0 5 128 5 148 4*0 5 128 6*0 5 128 6*0 5 128 6*0 5 128 6*0 5 128 6*0
  //   5 128 5 148 4*0 5 128 5 148 4*0 5 128 6*0 5 128 6*0 5 128 5 148 4*0 5 128 5 148 4*0 5 128 5 148 4*0
  //   5 128 6*0 5 128 6*0 5 128 6*0 5 128 5 148 4*0 5 128 6*0 5 128 6*0 5 128 6*0 5 128 6*0 5 128 6*0 5
  //   128 5 148 4*0 5 128 5 148 4*0 5 128 6*0 5 128 6*0 5 128 5 148 4*0 5 128 5 148 4*0 5 128 5 148 4*0 5
  //   128 6*0 5 128 6*0 5 128 6*0 5 128 5 148 4*0 5 128 6*0 5 128 6*0 5 128 6*0 5 128 6*0 5 128 6*0 5 128
  //   5 148 4*0 5 128 5 148 4*0 5 128 6*0 5 128 6*0 5 128 5 148 4*0 5 128 5 148 4*0 5 128 5 148 4*0 5 128
  //   6*0 5 128 6*0 5 128 6*0 5 128 5 148 4*0 5 128 6*0 5 128 6*0 5 128 6*0 5 128 6*0 5 128 6*0 5 128 5
  //   148 4*0 5 128 5 148 4*0 5 128 6*0 5 128 6*0 5 128 5 148 4*0 5 128 5 148 4*0 5 128 5 148 4*0 5 128
  //   6*0 5 128 6*0 5 128 6*0 5 128 5 148 4*0 5 128 6*0 5 128 6*0 5 128 6*0 5 128 6*0 5 128 6*0 5 128 5
  //   148 4*0 5 128 5 148 4*0 5 128 6*0 5 128 6*0 5 128 5 148 4*0 5 128 5 148 4*0 5 128 5 148 4*0 5 128
  //   6*0 5 128 6*0 5 128 6*0 5 128 5 148 4*0 5 128 6*0 5 128 6*0 5 128 6*0 5 128 6*0 5 128 6*0 5 128 5
  //   148 4*0 5 128 5 148 4*0 5 128 6*0 5 128 6*0 5 128 5 148 4*0 5 128 5 148 4*0 5 128 5 148 4*0 5 128
  //   6*0 5 128 6*0 5 128 6*0 5 128 5 148 4*0 5 128 6*0 5 128 6*0 5 128 6*0 5 128 6*0 5 128 6*0 5 128 5
  //   148 4*0 5 128 5 148 4*0 5 128 6*0 5 128 6*0 5 128 5 148 4*0 5 128 5 148 4*0 5 128 5 148 4*0 5 128
  //   6*0 5 128 6*0 5 128 6*0 5 128 5 148 4*0 5 128 6*0 5 128 6*0 5 128 6*0 5 128 6*0 5 128 6*0 5 128 5
  //   148 4*0 5 128 5 148 4*0 5 128 6*0 5 128 6*0 5 128 5 148 4*0 5 128 5 148 4*0 5 128 5 148 4*0 5 128
  //   6*0 5 128 6*0 5 128 6*0 5 128 5 148 4*0 5 128 6*0 5 128 6*0 5 128 6*0 5 128 6*0 5 128 6*0 5 128 5
  //   148 4*0 5 128 5 148 4*0 5 128 6*0 5 128 6*0 5 128 5 148 4*0 5 128 5 148 4*0 5 128 5 148 4*0 5 128
  //   6*0 5 128 6*0 5 128 6*0 5 128 5 148 4*0 5 128 6*0 5 128 6*0 5 128 6*0 5 128 6*0 5 128 6*0 5 128 5
  //   148 4*0 5 128 5 148 4*0 5 128 6*0 5 128 6*0 5 128 5 148 4*0 5 128 5 148 4*0 5 128 5 148 4*0 5 128
  //   6*0 5 128 6*0 5 128 6*0 5 128 5 148 4*0 5 128 6*0 5 128 6*0 5 128 6*0 5 128 6*0 5 128 6*0 5 128 5
  //   148 4*0 5 128 5 148 4*0 5 128 6*0 5 128 6*0 5 128 5 148 4*0 5 128 5 148 4*0 5 128 5 148 4*0 5 128
  //   6*0 5 128 6*0 5 128 6*0 5 128 5 148 4*0 5 128 6*0 5 128 6*0 5 128 6*0 5 128 6*0 5 128 6*0 5 128 5
  //   148 4*0 5 128 5 148 4*0 5 128 6*0 5 128 6*0 5 128 5 148 4*0 5 128 5 148 4*0 5 128 5 148 4*0 5 128
  //   6*0 5 128 6*0 5 128 6*0 5 128 5 148 4*0 5 128 6*0 5 128 6*0 5 128 6*0 5 128 6*0 5 128 6*0 5 128 5
  //   148 4*0 5 128 5 148 4*0 5 128 6*0 5 128 6*0 5 128 5 148 4*0 5 128 5 148 4*0 5 128 5 148 4*0 5 128
  //   6*0 5 128 6*0 5 128 6*0 5 128 5 148 4*0 5 128 6*0 5 128 6*0 5 128 6*0 5 128 6*0 5 128 6*0 5 128 5
  //   148 4*0 5 128 5 148 4*0 5 128 6*0 5 128 6*0 5 128 5 148 4*0 5 128 5 148 4*0 5 128 5 148 4*0 5 128
  //   6*0 5 128 6*0 5 128 6*0 5 128 5 148 4*0 5 128 6*0 5 128 6*0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
endmodule
